// Logisim project CPU 8 bits.circ as structural Verilog: 8 circuits, main circuit main
module main (
  input  [7:0] N1,
  input  [7:0] N2,
  input  [2:0] \Função ,
  output [7:0] SAIDA
);

  CPU cpu_1 (.N1(N2), .N2(N1), .\Função (\Função ), .SAIDA(SAIDA));
endmodule

module CPU (
  input  [7:0] N1,
  input  [7:0] N2,
  input  [2:0] \Função ,
  output [7:0] SAIDA
);

  wire [7:0] deslocador_1_out_2, e_1_out_3, nao_1_out, ou_1_out, soma_1_out_3, xor_1_out;

  NAO nao_1 (.IN(N1), .OUT(nao_1_out));
  E e_1 (.N1(N2), .out_3(e_1_out_3));  // open: N2
  deslocador deslocador_1 (.Entrada(N2), .out_2(deslocador_1_out_2));
  OU ou_1 (.N1(N1), .N2(N2), .OUT(ou_1_out));
  XOR xor_1 (.N1(N1), .N2(N2), .OUT(xor_1_out));
  SOMA soma_1 (.N1(N1), .N2(N2), .out_3(soma_1_out_3));
  Multiplexer #(.select(3), .width(8), .enable("false")) multiplexer_1 (
    .in0(N1), .in1(N2), .in2(nao_1_out), .in3(e_1_out_3), .in4(deslocador_1_out_2), .in5(ou_1_out),
    .in6(xor_1_out), .in7(soma_1_out_3), .out(SAIDA), .sel(\Função ));
endmodule

module deslocador (
  input  [7:0] Entrada,
  output [7:0] out_2
);

  wire and_2_out, and_3_out, and_4_out, and_5_out, and_6_out, and_7_out, and_8_out, and_9_out, and_10_out,
       and_11_out, and_13_out, and_14_out, clock_1_out, not_1_out;

  Clock clock_1 (.out(clock_1_out));
  not not_1 (not_1_out, clock_1_out);
  and and_1 (out_2[7], not_1_out, Entrada[6]);
  and and_2 (and_2_out, Entrada[7], clock_1_out);
  and and_3 (and_3_out, not_1_out, Entrada[5]);
  and and_4 (and_4_out, Entrada[6], clock_1_out);
  or or_1 (out_2[6], and_2_out, and_3_out);
  and and_5 (and_5_out, Entrada[5], clock_1_out);
  and and_6 (and_6_out, not_1_out, Entrada[4]);
  or or_2 (out_2[5], and_4_out, and_6_out);
  and and_7 (and_7_out, not_1_out, Entrada[3]);
  and and_8 (and_8_out, Entrada[4], clock_1_out);
  or or_3 (out_2[4], and_5_out, and_7_out);
  and and_9 (and_9_out, not_1_out, Entrada[2]);
  and and_10 (and_10_out, Entrada[3], clock_1_out);
  or or_4 (out_2[3], and_8_out, and_9_out);
  and and_11 (and_11_out, Entrada[2], clock_1_out);
  or or_5 (out_2[2], and_10_out, and_13_out);
  and and_12 (out_2[0], Entrada[1], clock_1_out);
  and and_13 (and_13_out, not_1_out, Entrada[1]);
  or or_6 (out_2[1], and_11_out, and_14_out);
  and and_14 (and_14_out, not_1_out, Entrada[0]);
endmodule

module E (
  input  [7:0] N1,
  input  [7:0] N2,
  output [7:0] out_3
);

  and and_1 (out_3[0], N1[0], N2[0]);
  and and_2 (out_3[1], N1[1], N2[1]);
  and and_3 (out_3[2], N1[2], N2[2]);
  and and_4 (out_3[3], N1[3], N2[3]);
  and and_5 (out_3[4], N1[4], N2[4]);
  and and_6 (out_3[5], N1[5], N2[5]);
  and and_7 (out_3[6], N1[6], N2[6]);
  and and_8 (out_3[7], N1[7], N2[7]);
endmodule

module OU (
  input  [7:0] N1,
  input  [7:0] N2,
  output [7:0] OUT
);

  or or_1 (OUT[0], N1[0], N2[0]);
  or or_2 (OUT[1], N1[1], N2[1]);
  or or_3 (OUT[2], N1[2], N2[2]);
  or or_4 (OUT[3], N1[3], N2[3]);
  or or_5 (OUT[4], N1[4], N2[4]);
  or or_6 (OUT[5], N1[5], N2[5]);
  or or_7 (OUT[6], N1[6], N2[6]);
  or or_8 (OUT[7], N1[7], N2[7]);
endmodule

module NAO (
  input  [7:0] IN,
  output [7:0] OUT
);

  not not_1 (OUT[0], IN[0]);
  not not_2 (OUT[1], IN[1]);
  not not_3 (OUT[2], IN[2]);
  not not_4 (OUT[3], IN[3]);
  not not_5 (OUT[4], IN[4]);
  not not_6 (OUT[5], IN[5]);
  not not_7 (OUT[6], IN[6]);
  not not_8 (OUT[7], IN[7]);
endmodule

// SUM
module SOMA (
  input  [7:0] N1,
  input  [7:0] N2,
  output [7:0] out_3
);

  Adder adder_1 (.a(N1), .b(N2), .out(out_3));  // open: cin, cout
endmodule

module XOR (
  input  [7:0] N1,
  input  [7:0] N2,
  output [7:0] OUT
);

  xor xor_1 (OUT[0], N1[0], N2[0]);
  xor xor_2 (OUT[1], N1[1], N2[1]);
  xor xor_3 (OUT[2], N1[2], N2[2]);
  xor xor_4 (OUT[3], N1[3], N2[3]);
  xor xor_5 (OUT[4], N1[4], N2[4]);
  xor xor_6 (OUT[5], N1[5], N2[5]);
  xor xor_7 (OUT[6], N1[6], N2[6]);
  xor xor_8 (OUT[7], N1[7], N2[7]);
endmodule
