// Logisim project Microarquitetura.circ as structural Verilog: 2 circuits, main circuit micro
module micro (
  input  CLK,
  input  [7:0] MBR_A,
  input  [7:0] MBR_B,
  input  [1:0] D,
  input  [2:0] ULA,
  input  [3:0] B,
  input  C8,
  input  C7,
  input  C6,
  input  C5,
  input  C4,
  input  C3,
  input  C2,
  input  C1,
  input  C0,
  output [7:0] out_16,
  output [7:0] out_17,
  output [7:0] out_18,
  output [7:0] out_19,
  output [7:0] out_20,
  output [7:0] out_21,
  output [7:0] out_22,
  output [7:0] out_23,
  output [7:0] SAIDA_B,
  output [7:0] SAIDA_C
);

  wire decoder_1_out0, decoder_1_out1, decoder_1_out2, decoder_1_out3, decoder_1_out4, decoder_1_out5,
       decoder_1_out6, decoder_1_out7, decoder_1_out8;
  wire [7:0] controlled_buffer_1_out, controlled_buffer_2_out, controlled_buffer_3_out,
       controlled_buffer_4_out, controlled_buffer_5_out, controlled_buffer_6_out, controlled_buffer_7_out,
       controlled_buffer_8_out, controlled_buffer_9_out, main_1_saida, PC_saida;

  assign controlled_buffer_1_out = C0 ? SAIDA_C : 8'bz;  // Controlled_Buffer controlled_buffer_1
  assign controlled_buffer_2_out = C1 ? SAIDA_C : 8'bz;  // Controlled_Buffer controlled_buffer_2
  assign controlled_buffer_3_out = C2 ? SAIDA_C : 8'bz;  // Controlled_Buffer controlled_buffer_3
  assign controlled_buffer_4_out = C3 ? SAIDA_C : 8'bz;  // Controlled_Buffer controlled_buffer_4
  assign controlled_buffer_5_out = C4 ? SAIDA_C : 8'bz;  // Controlled_Buffer controlled_buffer_5
  assign controlled_buffer_6_out = C5 ? SAIDA_C : 8'bz;  // Controlled_Buffer controlled_buffer_6
  assign controlled_buffer_7_out = C6 ? SAIDA_C : 8'bz;  // Controlled_Buffer controlled_buffer_7
  assign controlled_buffer_8_out = C7 ? SAIDA_C : 8'bz;  // Controlled_Buffer controlled_buffer_8
  assign controlled_buffer_9_out = C8 ? SAIDA_C : 8'bz;  // Controlled_Buffer controlled_buffer_9
  Registrador_main MAR (.CLK(CLK), .D(controlled_buffer_1_out), .SAIDA(out_16));
  Registrador_main MDR (.CLK(CLK), .D(controlled_buffer_2_out), .SAIDA(out_17));
  Registrador_main PC (.CLK(CLK), .D(controlled_buffer_3_out), .SAIDA(PC_saida));
  Registrador_main SP (.CLK(CLK), .D(controlled_buffer_4_out), .SAIDA(out_18));
  Registrador_main LV (.CLK(CLK), .D(controlled_buffer_5_out), .SAIDA(out_19));
  Registrador_main CPP (.CLK(CLK), .D(controlled_buffer_6_out), .SAIDA(out_20));
  Registrador_main TOS (.CLK(CLK), .D(controlled_buffer_7_out), .SAIDA(out_21));
  Registrador_main CPC (.CLK(CLK), .D(controlled_buffer_8_out), .SAIDA(out_22));
  Registrador_main H (.CLK(CLK), .D(controlled_buffer_9_out), .SAIDA(out_23));
  assign SAIDA_B = decoder_1_out0 ? out_17 : 8'bz;  // Controlled_Buffer controlled_buffer_10
  assign SAIDA_B = decoder_1_out1 ? PC_saida : 8'bz;  // Controlled_Buffer controlled_buffer_11
  assign SAIDA_B = decoder_1_out2 ? MBR_A : 8'bz;  // Controlled_Buffer controlled_buffer_12
  assign SAIDA_B = decoder_1_out3 ? MBR_B : 8'bz;  // Controlled_Buffer controlled_buffer_13
  assign SAIDA_B = decoder_1_out4 ? out_18 : 8'bz;  // Controlled_Buffer controlled_buffer_14
  assign SAIDA_B = decoder_1_out5 ? out_19 : 8'bz;  // Controlled_Buffer controlled_buffer_15
  assign SAIDA_B = decoder_1_out6 ? out_20 : 8'bz;  // Controlled_Buffer controlled_buffer_16
  assign SAIDA_B = decoder_1_out7 ? out_21 : 8'bz;  // Controlled_Buffer controlled_buffer_17
  assign SAIDA_B = decoder_1_out8 ? out_22 : 8'bz;  // Controlled_Buffer controlled_buffer_18
  CPU_8_bits_main main_1 (.\Função (ULA), .N1(out_23), .N2(SAIDA_B), .SAIDA(main_1_saida));
  deslocador_main main_2 (.IN(main_1_saida), .OUT(SAIDA_C), .D(D));
  Decoder #(.select(4), .enable("false")) decoder_1 (
    .out0(decoder_1_out0), .out1(decoder_1_out1), .out2(decoder_1_out2), .out3(decoder_1_out3),
    .out4(decoder_1_out4), .out5(decoder_1_out5), .out6(decoder_1_out6), .out7(decoder_1_out7),
    .out8(decoder_1_out8), .sel(B));  // open: out9, out10, out11, out12, out13, out14, out15
endmodule

module main (
  input  [7:0] MBR_A,
  input  [7:0] MBR_B,
  input  [1:0] D,
  input  [2:0] ULA,
  input  [3:0] in_5,
  input  in_6,
  input  in_7,
  input  in_8,
  input  in_9,
  input  in_10,
  input  in_11,
  input  in_12,
  input  in_13,
  input  in_14,
  output [7:0] out_15,
  output [7:0] out_16
);

  wire clock_1_out;

  Clock clock_1 (.out(clock_1_out));
  micro micro_1 (
    .CLK(clock_1_out), .MBR_A(MBR_A), .MBR_B(MBR_B), .D(D), .ULA(ULA), .B(in_5), .C8(in_6), .C7(in_7),
    .C6(in_8), .C5(in_9), .C4(in_10), .C3(in_11), .C2(in_12), .C1(in_13), .C0(in_14), .SAIDA_B(out_15),
    .SAIDA_C(out_16));  // open: out_17, out_18, out_19, out_20, out_21, out_22, out_23, out_16
endmodule
