// Logisim project Registrador.circ as structural Verilog: 1 circuit, main circuit main
module main (
  input  CLK,
  input  [7:0] D,
  output [7:0] SAIDA
);

  D_Flip_Flop d_ff_1 (.clk(CLK), .D(D[7]), .Q(SAIDA[7]));  // open: Qn, preset, en, reset
  D_Flip_Flop d_ff_2 (.clk(CLK), .D(D[6]), .Q(SAIDA[6]));  // open: Qn, preset, en, reset
  D_Flip_Flop d_ff_3 (.clk(CLK), .D(D[4]), .Q(SAIDA[4]));  // open: Qn, preset, en, reset
  D_Flip_Flop d_ff_4 (.clk(CLK), .D(D[5]), .Q(SAIDA[5]));  // open: Qn, preset, en, reset
  D_Flip_Flop d_ff_5 (.clk(CLK), .D(D[3]), .Q(SAIDA[3]));  // open: Qn, preset, en, reset
  D_Flip_Flop d_ff_6 (.clk(CLK), .D(D[2]), .Q(SAIDA[2]));  // open: Qn, preset, en, reset
  D_Flip_Flop d_ff_7 (.clk(CLK), .D(D[1]), .Q(SAIDA[1]));  // open: Qn, preset, en, reset
  D_Flip_Flop d_ff_8 (.clk(CLK), .D(D[0]), .Q(SAIDA[0]));  // open: Qn, preset, en, reset
endmodule
