// Logisim project bcd.circ as structural Verilog: 2 circuits, main circuit main
module main (
);

  wire and_1_out, and_2_out, clock_1_out, D_out, I_out, multiplexer_1_out, multiplexer_2_out,
       multiplexer_3_out, multiplexer_4_out, multiplexer_5_out, multiplexer_6_out, multiplexer_7_out,
       multiplexer_8_out, or_1_out, t_ff_1_q, t_ff_1_qn, t_ff_2_q, t_ff_2_qn, t_ff_3_q, t_ff_3_qn, t_ff_4_q,
       t_ff_4_qn, t_ff_5_q, t_ff_5_qn, t_ff_6_q, t_ff_6_qn, t_ff_7_q, t_ff_7_qn, t_ff_8_q, t_ff_8_qn;

  Clock clock_1 (.out(clock_1_out));
  LED led_1 (.in(multiplexer_1_out));
  T_Flip_Flop t_ff_1 (.clk(clock_1_out), .T(1'b1), .Q(t_ff_1_q), .Qn(t_ff_1_qn));  // open: preset, reset, en
  Multiplexer multiplexer_1 (.in0(t_ff_1_q), .in1(t_ff_1_qn), .out(multiplexer_1_out), .sel(or_1_out));  // open: en
  Button I (.out(I_out));
  Button D (.out(D_out));
  T_Flip_Flop t_ff_2 (.clk(multiplexer_1_out), .T(1'b1), .Q(t_ff_2_q), .Qn(t_ff_2_qn));  // open: preset, reset, en
  and and_1 (and_1_out, I_out, ~D_out);  // AND_Gate
  or or_1 (or_1_out, and_1_out, and_2_out);
  and and_2 (and_2_out, ~I_out, D_out);  // AND_Gate
  LED led_2 (.in(multiplexer_2_out));
  T_Flip_Flop t_ff_3 (.clk(multiplexer_2_out), .T(1'b1), .Q(t_ff_3_q), .Qn(t_ff_3_qn));  // open: preset, reset, en
  Multiplexer multiplexer_2 (.in0(t_ff_2_q), .in1(t_ff_2_qn), .out(multiplexer_2_out), .sel(or_1_out));  // open: en
  LED led_3 (.in(multiplexer_3_out));
  Multiplexer multiplexer_3 (.in0(t_ff_3_q), .in1(t_ff_3_qn), .out(multiplexer_3_out), .sel(or_1_out));  // open: en
  LED led_4 (.in(multiplexer_4_out));
  T_Flip_Flop t_ff_4 (.clk(multiplexer_3_out), .T(1'b1), .Q(t_ff_4_q), .Qn(t_ff_4_qn));  // open: preset, reset, en
  Multiplexer multiplexer_4 (.in0(t_ff_4_q), .in1(t_ff_4_qn), .out(multiplexer_4_out), .sel(or_1_out));  // open: en
  LED led_5 (.in(multiplexer_5_out));
  T_Flip_Flop t_ff_5 (.clk(multiplexer_4_out), .T(1'b1), .Q(t_ff_5_q), .Qn(t_ff_5_qn));  // open: preset, reset, en
  Multiplexer multiplexer_5 (.in0(t_ff_5_q), .in1(t_ff_5_qn), .out(multiplexer_5_out), .sel(or_1_out));  // open: en
  T_Flip_Flop t_ff_6 (.clk(multiplexer_5_out), .T(1'b1), .Q(t_ff_6_q), .Qn(t_ff_6_qn));  // open: preset, reset, en
  LED led_6 (.in(multiplexer_6_out));
  T_Flip_Flop t_ff_7 (.clk(multiplexer_6_out), .T(1'b1), .Q(t_ff_7_q), .Qn(t_ff_7_qn));  // open: preset, reset, en
  Multiplexer multiplexer_6 (.in0(t_ff_6_q), .in1(t_ff_6_qn), .out(multiplexer_6_out), .sel(or_1_out));  // open: en
  LED led_7 (.in(multiplexer_7_out));
  Multiplexer multiplexer_7 (.in0(t_ff_7_q), .in1(t_ff_7_qn), .out(multiplexer_7_out), .sel(or_1_out));  // open: en
  LED led_8 (.in(multiplexer_8_out));
  T_Flip_Flop t_ff_8 (.clk(multiplexer_7_out), .T(1'b1), .Q(t_ff_8_q), .Qn(t_ff_8_qn));  // open: preset, reset, en
  Multiplexer multiplexer_8 (.in0(t_ff_8_q), .in1(t_ff_8_qn), .out(multiplexer_8_out), .sel(or_1_out));  // open: en
endmodule

module BCD (
  input  A,
  input  B,
  input  C,
  input  D,
  output a_2,
  output b_2,
  output c_2,
  output d_2,
  output e,
  output f,
  output g
);

  wire and_1_out, and_2_out, and_3_out, and_4_out, and_5_out, and_6_out, and_7_out, and_8_out, and_9_out,
       and_10_out, and_11_out, and_12_out, and_13_out, and_14_out, and_15_out, and_16_out, and_17_out,
       and_18_out, and_19_out, and_20_out, and_21_out, and_22_out, and_23_out, and_24_out, and_25_out,
       and_26_out, not_1_out, not_2_out, not_3_out, not_4_out, not_5_out, not_6_out, not_7_out, not_8_out,
       not_9_out, not_10_out, not_11_out, not_12_out, not_13_out, not_14_out, not_15_out, not_16_out,
       not_17_out, not_18_out, not_19_out, not_20_out, not_21_out, not_22_out, not_23_out, not_24_out,
       not_25_out, not_26_out, not_27_out, not_28_out, not_29_out, not_30_out, not_31_out, not_32_out,
       not_33_out, not_34_out, not_35_out, not_36_out, not_37_out, not_38_out, not_39_out, not_40_out,
       not_41_out, not_42_out, not_43_out, not_44_out, not_45_out, not_46_out, not_47_out, not_48_out,
       not_49_out, not_50_out, not_51_out, not_52_out;

  not not_1 (not_1_out, A);
  not not_2 (not_2_out, B);
  and and_1 (and_1_out, not_1_out, not_2_out, not_3_out);
  not not_3 (not_3_out, D);
  not not_4 (not_4_out, A);
  and and_2 (and_2_out, not_4_out, C);
  not not_5 (not_5_out, A);
  and and_3 (and_3_out, not_5_out, B, D);
  not not_6 (not_6_out, B);
  and and_4 (and_4_out, A, not_6_out, not_7_out);
  not not_7 (not_7_out, C);
  not not_8 (not_8_out, A);
  and and_5 (and_5_out, not_8_out, not_9_out);
  not not_9 (not_9_out, B);
  not not_10 (not_10_out, A);
  not not_11 (not_11_out, C);
  and and_6 (and_6_out, not_10_out, not_11_out, not_12_out);
  not not_12 (not_12_out, D);
  not not_13 (not_13_out, B);
  and and_7 (and_7_out, not_13_out, not_14_out);
  not not_14 (not_14_out, C);
  not not_15 (not_15_out, A);
  and and_8 (and_8_out, not_15_out, C, D);
  not not_16 (not_16_out, B);
  and and_9 (and_9_out, not_16_out, not_17_out);
  not not_17 (not_17_out, C);
  not not_18 (not_18_out, A);
  and and_10 (and_10_out, not_18_out, D);
  not not_19 (not_19_out, A);
  and and_11 (and_11_out, not_19_out, B);
  not not_20 (not_20_out, A);
  not not_21 (not_21_out, B);
  not not_22 (not_22_out, D);
  not not_23 (not_23_out, A);
  not not_24 (not_24_out, B);
  not not_25 (not_25_out, A);
  not not_26 (not_26_out, D);
  not not_27 (not_27_out, A);
  not not_28 (not_28_out, C);
  not not_29 (not_29_out, B);
  not not_30 (not_30_out, C);
  not not_31 (not_31_out, B);
  and and_12 (and_12_out, not_31_out, not_32_out, not_33_out);
  not not_32 (not_32_out, C);
  not not_33 (not_33_out, D);
  not not_34 (not_34_out, A);
  and and_13 (and_13_out, not_34_out, C, not_35_out);
  not not_35 (not_35_out, D);
  not not_36 (not_36_out, A);
  and and_14 (and_14_out, not_36_out, not_37_out, not_38_out);
  not not_37 (not_37_out, C);
  not not_38 (not_38_out, D);
  not not_39 (not_39_out, A);
  and and_15 (and_15_out, not_39_out, B, not_40_out);
  not not_40 (not_40_out, C);
  not not_41 (not_41_out, A);
  and and_16 (and_16_out, not_41_out, B, not_42_out);
  not not_42 (not_42_out, D);
  not not_43 (not_43_out, B);
  and and_17 (and_17_out, A, not_43_out, not_44_out);
  not not_44 (not_44_out, C);
  not not_45 (not_45_out, A);
  not not_46 (not_46_out, B);
  and and_18 (and_18_out, not_45_out, not_46_out, C);
  not not_47 (not_47_out, A);
  and and_19 (and_19_out, not_47_out, B, not_48_out);
  not not_48 (not_48_out, C);
  not not_49 (not_49_out, A);
  and and_20 (and_20_out, not_49_out, B, not_50_out);
  not not_50 (not_50_out, D);
  and and_21 (and_21_out, A, not_51_out, not_52_out);
  not not_51 (not_51_out, B);
  not not_52 (not_52_out, C);
  or or_1 (a_2, and_1_out, and_2_out, and_3_out, and_4_out);
  or or_2 (b_2, and_5_out, and_6_out, and_7_out, and_8_out);
  or or_3 (c_2, and_9_out, and_10_out, and_11_out);
  and and_22 (and_22_out, not_20_out, not_21_out, not_22_out);
  and and_23 (and_23_out, not_23_out, not_24_out, C);
  and and_24 (and_24_out, not_25_out, C, not_26_out);
  and and_25 (and_25_out, not_27_out, B, not_28_out, D);
  and and_26 (and_26_out, A, not_29_out, not_30_out);
  or or_4 (e, and_12_out, and_13_out);
  or or_5 (f, and_14_out, and_15_out, and_16_out, and_17_out);
  or or_6 (g, and_18_out, and_19_out, and_20_out, and_21_out);
  or or_7 (d_2, and_22_out, and_23_out, and_24_out, and_25_out, and_26_out);
endmodule
