// Logisim project contador-dec-99.circ as structural Verilog: 4 circuits, main circuit main
module main (
);

  wire _10_0_out, _15_9_out, atraso8_1_out, cntbcd_1_q0, cntbcd_1_q1, cntbcd_1_q2, cntbcd_1_q3, D_out, I_out,
       j_k_ff_1_q, j_k_ff_1_qn, j_k_ff_2_q, j_k_ff_2_qn, j_k_ff_3_q, j_k_ff_3_qn, j_k_ff_4_q, j_k_ff_4_qn,
       nor_1_out, nor_2_out, nor_3_out, or_1_out, or_2_out, R_out, xor_1_out, xor_2_out, xor_3_out, xor_4_out;
  wire [2:0] decbcd7s_1_c_2, decbcd7s_2_c_2;
  wire [3:0] decbcd7s_1_b_2, decbcd7s_2_b_2;

  Button I (.out(I_out));
  Button D (.out(D_out));
  nor nor_1 (nor_1_out, I_out, D_out);
  nor nor_2 (nor_2_out, D_out, nor_3_out);
  nor nor_3 (nor_3_out, nor_2_out, I_out);
  DecBCD7S decbcd7s_1 (
    .A(cntbcd_1_q3), .B(cntbcd_1_q2), .C(cntbcd_1_q1), .D(cntbcd_1_q0), .a_2(decbcd7s_1_b_2[1]),
    .b_2(decbcd7s_1_b_2[0]), .c_2(decbcd7s_1_c_2[0]), .d_2(decbcd7s_1_c_2[1]), .e(decbcd7s_1_c_2[2]),
    .f(decbcd7s_1_b_2[2]), .g(decbcd7s_1_b_2[3]));
  J_K_Flip_Flop j_k_ff_1 (
    .J(1'b1), .clk(nor_1_out), .K(1'b1), .Q(j_k_ff_1_q), .Qn(j_k_ff_1_qn), .preset(_15_9_out),
    .en(nor_1_out), .reset(or_2_out));
  xor xor_1 (xor_1_out, nor_3_out, j_k_ff_1_qn);
  Button R (.out(R_out));
  DecBCD7S decbcd7s_2 (
    .A(j_k_ff_4_q), .B(j_k_ff_3_q), .C(j_k_ff_2_q), .D(j_k_ff_1_q), .a_2(decbcd7s_2_b_2[1]),
    .b_2(decbcd7s_2_b_2[0]), .c_2(decbcd7s_2_c_2[0]), .d_2(decbcd7s_2_c_2[1]), .e(decbcd7s_2_c_2[2]),
    .f(decbcd7s_2_b_2[2]), .g(decbcd7s_2_b_2[3]));
  J_K_Flip_Flop j_k_ff_2 (
    .J(1'b1), .clk(xor_1_out), .K(1'b1), .Q(j_k_ff_2_q), .Qn(j_k_ff_2_qn), .en(nor_1_out), .reset(or_1_out));  // open: preset
  or or_1 (or_1_out, or_2_out, _15_9_out);
  xor xor_2 (xor_2_out, nor_3_out, j_k_ff_2_qn);
  or or_2 (or_2_out, _10_0_out, R_out);
  _7_Segment_Display u_7_segment_display_1 (
    .g(decbcd7s_1_b_2[3]), .f(decbcd7s_1_b_2[2]), .a(decbcd7s_1_b_2[1]), .b(decbcd7s_1_b_2[0]),
    .e(decbcd7s_1_c_2[2]), .d(decbcd7s_1_c_2[1]), .c(decbcd7s_1_c_2[0]));  // open: dp
  J_K_Flip_Flop j_k_ff_3 (
    .J(1'b1), .clk(xor_2_out), .K(1'b1), .Q(j_k_ff_3_q), .Qn(j_k_ff_3_qn), .en(nor_1_out), .reset(or_1_out));  // open: preset
  and _10_0 (_10_0_out, ~nor_3_out, j_k_ff_4_q, ~j_k_ff_3_q, j_k_ff_2_q, ~j_k_ff_1_q);  // AND_Gate
  and _15_9 (_15_9_out, nor_3_out, j_k_ff_4_q, atraso8_1_out, j_k_ff_2_q, j_k_ff_1_q);
  _7_Segment_Display u_7_segment_display_2 (
    .g(decbcd7s_2_b_2[3]), .f(decbcd7s_2_b_2[2]), .a(decbcd7s_2_b_2[1]), .b(decbcd7s_2_b_2[0]),
    .e(decbcd7s_2_c_2[2]), .d(decbcd7s_2_c_2[1]), .c(decbcd7s_2_c_2[0]));  // open: dp
  J_K_Flip_Flop j_k_ff_4 (
    .J(1'b1), .clk(xor_3_out), .K(1'b1), .Q(j_k_ff_4_q), .Qn(j_k_ff_4_qn), .preset(_15_9_out),
    .en(nor_1_out), .reset(or_2_out));
  xor xor_3 (xor_3_out, nor_3_out, j_k_ff_3_qn);
  xor xor_4 (xor_4_out, nor_3_out, j_k_ff_4_qn);
  Atraso8 atraso8_1 (.IN(j_k_ff_3_q), .OUT(atraso8_1_out));
  CntBCD cntbcd_1 (
    .CLK(xor_4_out), .EN(nor_1_out), .D__I(nor_3_out), .Q0(cntbcd_1_q0), .Q1(cntbcd_1_q1), .Q2(cntbcd_1_q2),
    .Q3(cntbcd_1_q3), .R(R_out));  // open: CO
endmodule

module DecBCD7S (
  input  A,
  input  B,
  input  C,
  input  D,
  output a_2,
  output b_2,
  output c_2,
  output d_2,
  output e,
  output f,
  output g
);

  wire and_1_out, and_2_out, and_3_out, and_4_out, and_5_out, and_6_out, and_7_out, and_8_out, and_9_out,
       and_10_out, and_11_out, and_12_out, and_13_out, and_14_out, and_15_out, and_16_out, and_17_out,
       and_18_out, and_19_out, and_20_out, and_21_out, and_22_out, and_23_out, and_24_out, and_25_out,
       and_26_out, not_1_out, not_2_out, not_3_out, not_4_out, not_5_out, not_6_out, not_7_out, not_8_out,
       not_9_out, not_10_out, not_11_out, not_12_out, not_13_out, not_14_out, not_15_out, not_16_out,
       not_17_out, not_18_out, not_19_out, not_20_out, not_21_out, not_22_out, not_23_out, not_24_out,
       not_25_out, not_26_out, not_27_out, not_28_out, not_29_out, not_30_out, not_31_out, not_32_out,
       not_33_out, not_34_out, not_35_out, not_36_out, not_37_out, not_38_out, not_39_out, not_40_out,
       not_41_out, not_42_out, not_43_out, not_44_out, not_45_out, not_46_out, not_47_out, not_48_out,
       not_49_out, not_50_out, not_51_out, not_52_out;

  not not_1 (not_1_out, A);
  and and_1 (and_1_out, not_1_out, not_2_out, not_3_out);
  not not_2 (not_2_out, B);
  not not_3 (not_3_out, D);
  not not_4 (not_4_out, A);
  and and_2 (and_2_out, not_4_out, C);
  not not_5 (not_5_out, A);
  and and_3 (and_3_out, not_5_out, B, D);
  and and_4 (and_4_out, A, not_6_out, not_7_out);
  not not_6 (not_6_out, B);
  not not_7 (not_7_out, C);
  not not_8 (not_8_out, A);
  and and_5 (and_5_out, not_8_out, not_9_out);
  not not_9 (not_9_out, B);
  not not_10 (not_10_out, A);
  and and_6 (and_6_out, not_10_out, not_11_out, not_12_out);
  not not_11 (not_11_out, C);
  not not_12 (not_12_out, D);
  not not_13 (not_13_out, B);
  and and_7 (and_7_out, not_13_out, not_14_out);
  not not_14 (not_14_out, C);
  not not_15 (not_15_out, A);
  and and_8 (and_8_out, not_15_out, C, D);
  not not_16 (not_16_out, B);
  and and_9 (and_9_out, not_16_out, not_17_out);
  not not_17 (not_17_out, C);
  not not_18 (not_18_out, A);
  and and_10 (and_10_out, not_18_out, D);
  not not_19 (not_19_out, A);
  and and_11 (and_11_out, not_19_out, B);
  not not_20 (not_20_out, A);
  not not_21 (not_21_out, B);
  not not_22 (not_22_out, D);
  not not_23 (not_23_out, A);
  not not_24 (not_24_out, B);
  not not_25 (not_25_out, A);
  not not_26 (not_26_out, D);
  not not_27 (not_27_out, A);
  not not_28 (not_28_out, C);
  not not_29 (not_29_out, B);
  not not_30 (not_30_out, C);
  not not_31 (not_31_out, B);
  and and_12 (and_12_out, not_31_out, not_32_out, not_33_out);
  not not_32 (not_32_out, C);
  not not_33 (not_33_out, D);
  not not_34 (not_34_out, A);
  and and_13 (and_13_out, not_34_out, C, not_35_out);
  not not_35 (not_35_out, D);
  not not_36 (not_36_out, A);
  and and_14 (and_14_out, not_36_out, not_37_out, not_38_out);
  not not_37 (not_37_out, C);
  not not_38 (not_38_out, D);
  not not_39 (not_39_out, A);
  and and_15 (and_15_out, not_39_out, B, not_40_out);
  not not_40 (not_40_out, C);
  not not_41 (not_41_out, A);
  and and_16 (and_16_out, not_41_out, B, not_42_out);
  not not_42 (not_42_out, D);
  not not_43 (not_43_out, B);
  and and_17 (and_17_out, A, not_43_out, not_44_out);
  not not_44 (not_44_out, C);
  not not_45 (not_45_out, A);
  not not_46 (not_46_out, B);
  and and_18 (and_18_out, not_45_out, not_46_out, C);
  not not_47 (not_47_out, A);
  and and_19 (and_19_out, not_47_out, B, not_48_out);
  not not_48 (not_48_out, C);
  not not_49 (not_49_out, A);
  and and_20 (and_20_out, not_49_out, B, not_50_out);
  not not_50 (not_50_out, D);
  and and_21 (and_21_out, A, not_51_out, not_52_out);
  not not_51 (not_51_out, B);
  not not_52 (not_52_out, C);
  or or_1 (a_2, and_1_out, and_2_out, and_3_out, and_4_out);
  or or_2 (b_2, and_5_out, and_6_out, and_7_out, and_8_out);
  or or_3 (c_2, and_9_out, and_10_out, and_11_out);
  and and_22 (and_22_out, not_20_out, not_21_out, not_22_out);
  and and_23 (and_23_out, not_23_out, not_24_out, C);
  and and_24 (and_24_out, not_25_out, C, not_26_out);
  and and_25 (and_25_out, not_27_out, B, not_28_out, D);
  and and_26 (and_26_out, A, not_29_out, not_30_out);
  or or_4 (e, and_12_out, and_13_out);
  or or_5 (f, and_14_out, and_15_out, and_16_out, and_17_out);
  or or_6 (g, and_18_out, and_19_out, and_20_out, and_21_out);
  or or_7 (d_2, and_22_out, and_23_out, and_24_out, and_25_out, and_26_out);
endmodule

module Atraso8 (
  input  IN,
  output OUT
);

  wire not_1_out, not_2_out, not_3_out, not_4_out, not_5_out, not_6_out, not_8_out;

  not not_1 (not_1_out, IN);
  not not_2 (not_2_out, not_1_out);
  not not_3 (not_3_out, not_2_out);
  not not_4 (not_4_out, not_3_out);
  not not_5 (not_5_out, not_6_out);
  not not_6 (not_6_out, not_4_out);
  not not_7 (OUT, not_8_out);
  not not_8 (not_8_out, not_5_out);
endmodule

module CntBCD (
  input  CLK,
  input  EN,
  input  D__I,
  input  R,
  output Q0,
  output Q1,
  output Q2,
  output Q3,
  output CO
);

  wire _10_0_out, _15_9_out, atraso8_1_out, j_k_ff_1_qn, j_k_ff_2_qn, j_k_ff_3_qn, j_k_ff_4_qn, or_1_out,
       or_2_out, xor_1_out, xor_2_out, xor_3_out;

  J_K_Flip_Flop j_k_ff_1 (
    .J(1'b1), .clk(CLK), .K(1'b1), .Q(Q0), .Qn(j_k_ff_1_qn), .preset(_15_9_out), .en(EN), .reset(or_2_out));
  xor xor_1 (xor_1_out, D__I, j_k_ff_1_qn);
  J_K_Flip_Flop j_k_ff_2 (
    .J(1'b1), .clk(xor_1_out), .K(1'b1), .Q(Q1), .Qn(j_k_ff_2_qn), .en(EN), .reset(or_1_out));  // open: preset
  or or_1 (or_1_out, or_2_out, _15_9_out);
  J_K_Flip_Flop j_k_ff_3 (
    .J(1'b1), .clk(xor_2_out), .K(1'b1), .Q(Q2), .Qn(j_k_ff_3_qn), .en(EN), .reset(or_1_out));  // open: preset
  xor xor_2 (xor_2_out, D__I, j_k_ff_2_qn);
  or or_2 (or_2_out, _10_0_out, R);
  xor xor_3 (xor_3_out, D__I, j_k_ff_3_qn);
  and _10_0 (_10_0_out, ~D__I, Q3, ~Q2, Q1, ~Q0);  // AND_Gate
  and _15_9 (_15_9_out, D__I, Q3, atraso8_1_out, Q1, Q0);
  J_K_Flip_Flop j_k_ff_4 (
    .J(1'b1), .clk(xor_3_out), .K(1'b1), .Q(Q3), .Qn(j_k_ff_4_qn), .preset(_15_9_out), .en(EN),
    .reset(or_2_out));
  xor xor_4 (CO, D__I, j_k_ff_4_qn);
  Atraso8 atraso8_1 (.IN(Q2), .OUT(atraso8_1_out));
endmodule
