// Logisim project count-up-dn.circ as structural Verilog: 5 circuits, main circuit main
module main (
);

  wire button_1_out, button_2_out, d_ff_1_q, d_ff_1_qn, d_ff_2_q, d_ff_2_qn, d_ff_3_q, d_ff_3_qn, d_ff_4_q,
       d_ff_4_qn, dec_1_a2, dec_1_b2, dec_1_c2, dec_1_d2, decbcd7s_1_a2, decbcd7s_1_b2, decbcd7s_1_c2,
       decbcd7s_1_d2, decbcd7s_1_e, decbcd7s_1_f, decbcd7s_1_g, decbcd7s_2_a2, decbcd7s_2_b2, decbcd7s_2_c2,
       decbcd7s_2_d2, decbcd7s_2_e, decbcd7s_2_f, decbcd7s_2_g, nor_1_out, nor_2_out, not_1_out, not_2_out,
       or_1_out, rst_1_s, selclk_1_o, selclk_2_o, selclk_3_o;

  Button button_1 (.out(button_1_out));
  Button button_2 (.out(button_2_out));
  or or_1 (or_1_out, button_1_out, button_2_out);
  not not_1 (not_1_out, or_1_out);
  nor nor_1 (nor_1_out, button_1_out, nor_2_out);
  nor nor_2 (nor_2_out, nor_1_out, button_2_out);
  not not_2 (not_2_out, nor_1_out);
  D_Flip_Flop d_ff_1 (
    .clk(not_1_out), .D(d_ff_1_qn), .Q(d_ff_1_q), .Qn(d_ff_1_qn), .reset(rst_1_s));  // open: preset, en
  SelClk selclk_1 (.Q(d_ff_1_q), .Q_2(d_ff_1_qn), .S(1'b1), .O(selclk_1_o));
  D_Flip_Flop d_ff_2 (
    .clk(selclk_1_o), .D(d_ff_2_qn), .Q(d_ff_2_q), .Qn(d_ff_2_qn), .reset(rst_1_s));  // open: preset, en
  DecBCD7S decbcd7s_1 (
    .a(d_ff_4_q), .b(d_ff_3_q), .c(d_ff_2_q), .d(d_ff_1_q), .a2(decbcd7s_1_a2), .b2(decbcd7s_1_b2),
    .c2(decbcd7s_1_c2), .d2(decbcd7s_1_d2), .e(decbcd7s_1_e), .f(decbcd7s_1_f), .g(decbcd7s_1_g));
  SelClk selclk_2 (.Q(d_ff_2_q), .Q_2(d_ff_2_qn), .S(1'b1), .O(selclk_2_o));
  dec dec_1 (
    .p(not_2_out), .a(d_ff_4_q), .b(d_ff_3_q), .c(d_ff_2_q), .d(d_ff_1_q), .a2(dec_1_a2), .b2(dec_1_b2),
    .c2(dec_1_c2), .d2(dec_1_d2));
  _7_Segment_Display u_7_segment_display_1 (
    .g(decbcd7s_1_g), .f(decbcd7s_1_f), .a(decbcd7s_1_a2), .b(decbcd7s_1_b2), .e(decbcd7s_1_e),
    .d(decbcd7s_1_d2), .c(decbcd7s_1_c2));  // open: dp
  D_Flip_Flop d_ff_3 (
    .clk(selclk_2_o), .D(d_ff_3_qn), .Q(d_ff_3_q), .Qn(d_ff_3_qn), .reset(rst_1_s));  // open: preset, en
  DecBCD7S decbcd7s_2 (
    .a(dec_1_a2), .b(dec_1_b2), .c(dec_1_c2), .d(dec_1_d2), .a2(decbcd7s_2_a2), .b2(decbcd7s_2_b2),
    .c2(decbcd7s_2_c2), .d2(decbcd7s_2_d2), .e(decbcd7s_2_e), .f(decbcd7s_2_f), .g(decbcd7s_2_g));
  SelClk selclk_3 (.Q(d_ff_3_q), .Q_2(d_ff_3_qn), .S(1'b1), .O(selclk_3_o));
  D_Flip_Flop d_ff_4 (
    .clk(selclk_3_o), .D(d_ff_4_qn), .Q(d_ff_4_q), .Qn(d_ff_4_qn), .reset(rst_1_s));  // open: preset, en
  _7_Segment_Display u_7_segment_display_2 (
    .g(decbcd7s_2_g), .f(decbcd7s_2_f), .a(decbcd7s_2_a2), .b(decbcd7s_2_b2), .e(decbcd7s_2_e),
    .d(decbcd7s_2_d2), .c(decbcd7s_2_c2));  // open: dp
  Rst rst_1 (.a(d_ff_4_q), .b(d_ff_3_q), .c(d_ff_2_q), .d(not_1_out), .s(rst_1_s));
endmodule

module SelClk (
  input  Q,
  input  Q_2,
  input  S,
  output O
);

  wire and_1_out, and_2_out, not_1_out;

  not not_1 (not_1_out, S);
  and and_1 (and_1_out, Q, not_1_out);
  or or_1 (O, and_1_out, and_2_out);
  and and_2 (and_2_out, Q_2, S);
endmodule

module Rst (
  input  a,
  input  b,
  input  c,
  input  d,
  output s
);

  wire and_1_out, and_2_out, or_1_out;

  and and_1 (and_1_out, a, c);
  and and_2 (and_2_out, a, b);
  or or_1 (or_1_out, and_1_out, and_2_out);
  and and_3 (s, or_1_out, d);
endmodule

module DecBCD7S (
  input  a,
  input  b,
  input  c,
  input  d,
  output a2,
  output b2,
  output c2,
  output d2,
  output e,
  output f,
  output g
);

  wire and_1_out, and_2_out, and_3_out, and_4_out, and_5_out, and_6_out, and_7_out, and_8_out, and_9_out,
       and_10_out, and_11_out, and_12_out, and_13_out, and_14_out, and_15_out, and_16_out, and_17_out,
       and_18_out, and_19_out, and_20_out, and_21_out, and_22_out, and_23_out, and_24_out, and_25_out,
       and_26_out, not_1_out, not_2_out, not_3_out, not_4_out, not_5_out, not_6_out, not_7_out, not_8_out,
       not_9_out, not_10_out, not_11_out, not_12_out, not_13_out, not_14_out, not_15_out, not_16_out,
       not_17_out, not_18_out, not_19_out, not_20_out, not_21_out, not_22_out, not_23_out, not_24_out,
       not_25_out, not_26_out, not_27_out, not_28_out, not_29_out, not_30_out, not_31_out, not_32_out,
       not_33_out, not_34_out, not_35_out, not_36_out, not_37_out, not_38_out, not_39_out, not_40_out,
       not_41_out, not_42_out, not_43_out, not_44_out, not_45_out, not_46_out, not_47_out, not_48_out,
       not_49_out, not_50_out, not_51_out, not_52_out;

  not not_1 (not_1_out, a);
  and and_1 (and_1_out, not_1_out, not_2_out, not_3_out);
  not not_2 (not_2_out, b);
  not not_3 (not_3_out, d);
  not not_4 (not_4_out, a);
  and and_2 (and_2_out, not_4_out, c);
  not not_5 (not_5_out, a);
  and and_3 (and_3_out, not_5_out, b, d);
  not not_6 (not_6_out, b);
  and and_4 (and_4_out, a, not_6_out, not_7_out);
  not not_7 (not_7_out, c);
  not not_8 (not_8_out, a);
  and and_5 (and_5_out, not_8_out, not_9_out);
  not not_9 (not_9_out, b);
  not not_10 (not_10_out, a);
  and and_6 (and_6_out, not_10_out, not_11_out, not_12_out);
  not not_11 (not_11_out, c);
  not not_12 (not_12_out, d);
  not not_13 (not_13_out, b);
  and and_7 (and_7_out, not_13_out, not_14_out);
  not not_14 (not_14_out, c);
  not not_15 (not_15_out, a);
  and and_8 (and_8_out, not_15_out, c, d);
  not not_16 (not_16_out, b);
  and and_9 (and_9_out, not_16_out, not_17_out);
  not not_17 (not_17_out, c);
  not not_18 (not_18_out, a);
  and and_10 (and_10_out, not_18_out, d);
  not not_19 (not_19_out, a);
  and and_11 (and_11_out, not_19_out, b);
  not not_20 (not_20_out, a);
  not not_21 (not_21_out, b);
  not not_22 (not_22_out, d);
  not not_23 (not_23_out, a);
  not not_24 (not_24_out, b);
  not not_25 (not_25_out, a);
  not not_26 (not_26_out, d);
  not not_27 (not_27_out, a);
  not not_28 (not_28_out, c);
  not not_29 (not_29_out, b);
  not not_30 (not_30_out, c);
  not not_31 (not_31_out, b);
  and and_12 (and_12_out, not_31_out, not_32_out, not_33_out);
  not not_32 (not_32_out, c);
  not not_33 (not_33_out, d);
  not not_34 (not_34_out, a);
  and and_13 (and_13_out, not_34_out, c, not_35_out);
  not not_35 (not_35_out, d);
  not not_36 (not_36_out, a);
  and and_14 (and_14_out, not_36_out, not_37_out, not_38_out);
  not not_37 (not_37_out, c);
  not not_38 (not_38_out, d);
  not not_39 (not_39_out, a);
  and and_15 (and_15_out, not_39_out, b, not_40_out);
  not not_40 (not_40_out, c);
  not not_41 (not_41_out, a);
  and and_16 (and_16_out, not_41_out, b, not_42_out);
  not not_42 (not_42_out, d);
  and and_17 (and_17_out, a, not_43_out, not_44_out);
  not not_43 (not_43_out, b);
  not not_44 (not_44_out, c);
  not not_45 (not_45_out, a);
  and and_18 (and_18_out, not_45_out, not_46_out, c);
  not not_46 (not_46_out, b);
  not not_47 (not_47_out, a);
  and and_19 (and_19_out, not_47_out, b, not_48_out);
  not not_48 (not_48_out, c);
  not not_49 (not_49_out, a);
  and and_20 (and_20_out, not_49_out, b, not_50_out);
  not not_50 (not_50_out, d);
  not not_51 (not_51_out, b);
  and and_21 (and_21_out, a, not_51_out, not_52_out);
  not not_52 (not_52_out, c);
  or or_1 (a2, and_1_out, and_2_out, and_3_out, and_4_out);
  or or_2 (b2, and_5_out, and_6_out, and_7_out, and_8_out);
  or or_3 (c2, and_9_out, and_10_out, and_11_out);
  and and_22 (and_22_out, not_20_out, not_21_out, not_22_out);
  and and_23 (and_23_out, not_23_out, not_24_out, c);
  and and_24 (and_24_out, not_25_out, c, not_26_out);
  and and_25 (and_25_out, not_27_out, b, not_28_out, d);
  and and_26 (and_26_out, a, not_29_out, not_30_out);
  or or_4 (e, and_12_out, and_13_out);
  or or_5 (f, and_14_out, and_15_out, and_16_out, and_17_out);
  or or_6 (g, and_18_out, and_19_out, and_20_out, and_21_out);
  or or_7 (d2, and_22_out, and_23_out, and_24_out, and_25_out, and_26_out);
endmodule

module dec (
  input  p,
  input  a,
  input  b,
  input  c,
  input  d,
  output a2,
  output b2,
  output c2,
  output d2
);

  wire and_1_out, and_2_out, and_3_out, and_4_out, and_5_out, and_6_out, and_7_out, and_8_out, and_9_out,
       and_10_out, and_11_out, and_12_out, and_13_out, and_14_out, and_15_out, and_16_out, and_17_out,
       not_1_out, not_2_out, not_3_out, not_4_out, not_5_out, not_6_out, not_7_out, not_8_out, not_9_out,
       not_10_out;

  and and_1 (and_1_out, a, c);
  and and_2 (and_2_out, a, b);
  and and_3 (and_3_out, p, a);
  not not_1 (not_1_out, a);
  not not_2 (not_2_out, p);
  not not_3 (not_3_out, b);
  not not_4 (not_4_out, c);
  not not_5 (not_5_out, p);
  not not_6 (not_6_out, a);
  not not_7 (not_7_out, c);
  not not_8 (not_8_out, p);
  not not_9 (not_9_out, b);
  not not_10 (not_10_out, c);
  and and_4 (and_4_out, c, d);
  and and_5 (and_5_out, b, d);
  and and_6 (and_6_out, a, d);
  and and_7 (and_7_out, a, b);
  and and_8 (and_8_out, p, d);
  and and_9 (and_9_out, p, a, c);
  or or_1 (a2, and_1_out, and_2_out, and_3_out);
  and and_10 (and_10_out, not_1_out, b, c);
  and and_11 (and_11_out, not_2_out, a, not_3_out, not_4_out);
  and and_12 (and_12_out, p, b);
  and and_13 (and_13_out, p, a, c);
  and and_14 (and_14_out, not_5_out, not_6_out, b, not_7_out);
  and and_15 (and_15_out, not_8_out, a, not_9_out, not_10_out);
  and and_16 (and_16_out, p, c);
  and and_17 (and_17_out, p, a, b);
  or or_2 (d2, and_4_out, and_5_out, and_6_out, and_7_out, and_8_out, and_9_out);
  or or_3 (b2, and_10_out, and_11_out, and_12_out, and_13_out);
  or or_4 (c2, and_14_out, and_15_out, and_16_out, and_17_out);
endmodule
