// Logisim project impressora.circ as structural Verilog
module main (
  input  [5:0] Letra_1,
  input  [5:0] Letra_2,
  input  [5:0] Letra_3,
  input  [5:0] Letra_4,
  input  [5:0] Letra_5,
  input  [5:0] Letra_1_2,
  input  [5:0] Letra_1_3,
  input  [5:0] Letra_1_4,
  input  [5:0] Letra_1_5,
  input  [5:0] Letra_1_6,
  input  [5:0] Letra_1_7,
  input  [5:0] Letra_1_8,
  input  [5:0] Letra_1_9,
  input  [5:0] Letra_1_10,
  input  [5:0] Letra_1_11,
  input  [5:0] Letra_1_12,
  input  [5:0] Letra_1_13,
  input  [5:0] Letra_1_14,
  input  [5:0] Letra_1_15,
  input  [5:0] Letra_1_16
);

  wire clock_1_out, shift_register_1_out, shift_register_2_out;
  wire [2:0] display_1_c1, display_1_c2;
  wire [3:0] display_1_b1, display_1_b2;
  wire [5:0] graytobin_1_f_2, main_1_letra, main_2_letra, main_3_letra, main_4_letra, main_5_letra,
       main_6_letra, main_7_letra, main_8_letra, main_9_letra, main_10_letra, main_11_letra, main_12_letra,
       main_13_letra, main_14_letra, main_15_letra, main_16_letra, main_17_letra, main_18_letra,
       main_19_letra, main_20_letra, sensor_1_out_39;
  wire [6:0] main_1_col_1, main_1_col_2, main_1_col_3, main_1_col_4, main_1_col_5, main_2_col_1,
       main_2_col_2, main_2_col_3, main_2_col_4, main_2_col_5, main_3_col_1, main_3_col_2, main_3_col_3,
       main_3_col_4, main_3_col_5, main_4_col_1, main_4_col_2, main_4_col_3, main_4_col_4, main_4_col_5,
       main_5_col_1, main_5_col_2, main_5_col_3, main_5_col_4, main_5_col_5, main_6_col_1, main_6_col_2,
       main_6_col_3, main_6_col_4, main_6_col_5, main_7_col_1, main_7_col_2, main_7_col_3, main_7_col_4,
       main_7_col_5, main_8_col_1, main_8_col_2, main_8_col_3, main_8_col_4, main_8_col_5, main_9_col_1,
       main_9_col_2, main_9_col_3, main_9_col_4, main_9_col_5, main_10_col_1, main_10_col_2, main_10_col_3,
       main_10_col_4, main_10_col_5, main_11_col_1, main_11_col_2, main_11_col_3, main_11_col_4,
       main_11_col_5, main_12_col_1, main_12_col_2, main_12_col_3, main_12_col_4, main_12_col_5,
       main_13_col_1, main_13_col_2, main_13_col_3, main_13_col_4, main_13_col_5, main_14_col_1,
       main_14_col_2, main_14_col_3, main_14_col_4, main_14_col_5, main_15_col_1, main_15_col_2,
       main_15_col_3, main_15_col_4, main_15_col_5, main_16_col_1, main_16_col_2, main_16_col_3,
       main_16_col_4, main_16_col_5, main_17_col_1, main_17_col_2, main_17_col_3, main_17_col_4,
       main_17_col_5, main_18_col_1, main_18_col_2, main_18_col_3, main_18_col_4, main_18_col_5,
       main_19_col_1, main_19_col_2, main_19_col_3, main_19_col_4, main_19_col_5, main_20_col_1,
       main_20_col_2, main_20_col_3, main_20_col_4, main_20_col_5;
  wire [18:0] shift_register_1_q18, shift_register_2_q18;
  wire [19:0] circuito_1_m20;

  Clock clock_1 (.out(clock_1_out));
  DotMatrix dotmatrix_1 (
    .col0(main_1_col_1), .col1(main_1_col_2), .col2(main_1_col_3), .col3(main_1_col_4), .col4(main_1_col_5));
  matriz_led_main main_1 (
    .Col_1(main_1_col_1), .Col_2(main_1_col_2), .Col_3(main_1_col_3), .Col_4(main_1_col_4),
    .Col_5(main_1_col_5), .in_1(Letra_1[5]), .in_2(Letra_1[4]), .in_3(Letra_1[3]), .in_4(Letra_1[2]),
    .in_5(Letra_1[1]), .in_6(Letra_1[0]), .Letra(main_1_letra));
  Shift_Register #(.length(19)) shift_register_1 (
    .in(shift_register_2_out), .clk(clock_1_out), .out(shift_register_1_out), .q0(shift_register_1_q18[18]),
    .q1(shift_register_1_q18[17]), .q2(shift_register_1_q18[16]), .q3(shift_register_1_q18[15]),
    .q4(shift_register_1_q18[14]), .q5(shift_register_1_q18[13]), .q6(shift_register_1_q18[12]),
    .q7(shift_register_1_q18[11]), .q8(shift_register_1_q18[10]), .q9(shift_register_1_q18[9]),
    .q10(shift_register_1_q18[8]), .q11(shift_register_1_q18[7]), .q12(shift_register_1_q18[6]),
    .q13(shift_register_1_q18[5]), .q14(shift_register_1_q18[4]), .q15(shift_register_1_q18[3]),
    .q16(shift_register_1_q18[2]), .q17(shift_register_1_q18[1]), .q18(shift_register_1_q18[0]));  // open: shift, load, clr, d0, d1, d2, d3, d4, d5, d6, d7, d8, d9, d10, d11, d12, d13, d14, d15, d16, d17, d18
  DotMatrix dotmatrix_2 (
    .col0(main_2_col_1), .col1(main_2_col_2), .col2(main_2_col_3), .col3(main_2_col_4), .col4(main_2_col_5));
  DotMatrix dotmatrix_3 (
    .col0(main_3_col_1), .col1(main_3_col_2), .col2(main_3_col_3), .col3(main_3_col_4), .col4(main_3_col_5));
  matriz_led_main main_2 (
    .Col_1(main_2_col_1), .Col_2(main_2_col_2), .Col_3(main_2_col_3), .Col_4(main_2_col_4),
    .Col_5(main_2_col_5), .in_1(Letra_2[5]), .in_2(Letra_2[4]), .in_3(Letra_2[3]), .in_4(Letra_2[2]),
    .in_5(Letra_2[1]), .in_6(Letra_2[0]), .Letra(main_2_letra));
  DotMatrix #(.matrixcols(19), .matrixrows(1)) dotmatrix_4 (
    .col0(shift_register_1_q18[18]), .col1(shift_register_1_q18[17]), .col2(shift_register_1_q18[16]),
    .col3(shift_register_1_q18[15]), .col4(shift_register_1_q18[14]), .col5(shift_register_1_q18[13]),
    .col6(shift_register_1_q18[12]), .col7(shift_register_1_q18[11]), .col8(shift_register_1_q18[10]),
    .col9(shift_register_1_q18[9]), .col10(shift_register_1_q18[8]), .col11(shift_register_1_q18[7]),
    .col12(shift_register_1_q18[6]), .col13(shift_register_1_q18[5]), .col14(shift_register_1_q18[4]),
    .col15(shift_register_1_q18[3]), .col16(shift_register_1_q18[2]), .col17(shift_register_1_q18[1]),
    .col18(shift_register_1_q18[0]));
  Sensor sensor_1 (
    .in_1(shift_register_1_q18[18]), .in_2(shift_register_1_q18[17]), .in_3(shift_register_1_q18[16]),
    .in_4(shift_register_1_q18[15]), .in_5(shift_register_1_q18[14]), .in_6(shift_register_1_q18[13]),
    .in_7(shift_register_1_q18[12]), .in_8(shift_register_1_q18[11]), .in_9(shift_register_1_q18[10]),
    .in_10(shift_register_1_q18[9]), .in_11(shift_register_1_q18[8]), .in_12(shift_register_1_q18[7]),
    .in_13(shift_register_1_q18[6]), .in_14(shift_register_1_q18[5]), .in_15(shift_register_1_q18[4]),
    .in_16(shift_register_1_q18[3]), .in_17(shift_register_1_q18[2]), .in_18(shift_register_1_q18[1]),
    .in_19(shift_register_1_q18[0]), .in_20(shift_register_2_q18[18]), .in_21(shift_register_2_q18[17]),
    .in_22(shift_register_2_q18[16]), .in_23(shift_register_2_q18[15]), .in_24(shift_register_2_q18[14]),
    .in_25(shift_register_2_q18[13]), .in_26(shift_register_2_q18[12]), .in_27(shift_register_2_q18[11]),
    .in_28(shift_register_2_q18[10]), .in_29(shift_register_2_q18[9]), .in_30(shift_register_2_q18[8]),
    .in_31(shift_register_2_q18[7]), .in_32(shift_register_2_q18[6]), .in_33(shift_register_2_q18[5]),
    .in_34(shift_register_2_q18[4]), .in_35(shift_register_2_q18[3]), .in_36(shift_register_2_q18[2]),
    .in_37(shift_register_2_q18[1]), .in_38(shift_register_2_q18[0]), .out_39(sensor_1_out_39[0]),
    .out_40(sensor_1_out_39[1]), .out_41(sensor_1_out_39[2]), .out_42(sensor_1_out_39[3]),
    .out_43(sensor_1_out_39[4]), .out_44(sensor_1_out_39[5]));
  DotMatrix dotmatrix_5 (
    .col0(main_4_col_1), .col1(main_4_col_2), .col2(main_4_col_3), .col3(main_4_col_4), .col4(main_4_col_5));
  matriz_led_main main_3 (
    .Col_1(main_3_col_1), .Col_2(main_3_col_2), .Col_3(main_3_col_3), .Col_4(main_3_col_4),
    .Col_5(main_3_col_5), .in_1(Letra_3[5]), .in_2(Letra_3[4]), .in_3(Letra_3[3]), .in_4(Letra_3[2]),
    .in_5(Letra_3[1]), .in_6(Letra_3[0]), .Letra(main_3_letra));
  DotMatrix dotmatrix_6 (
    .col0(main_5_col_1), .col1(main_5_col_2), .col2(main_5_col_3), .col3(main_5_col_4), .col4(main_5_col_5));
  matriz_led_main main_4 (
    .Col_1(main_4_col_1), .Col_2(main_4_col_2), .Col_3(main_4_col_3), .Col_4(main_4_col_4),
    .Col_5(main_4_col_5), .in_1(Letra_4[5]), .in_2(Letra_4[4]), .in_3(Letra_4[3]), .in_4(Letra_4[2]),
    .in_5(Letra_4[1]), .in_6(Letra_4[0]), .Letra(main_4_letra));
  Shift_Register #(.length(19)) shift_register_2 (
    .in(shift_register_1_out), .clk(clock_1_out), .out(shift_register_2_out), .q0(shift_register_2_q18[18]),
    .q1(shift_register_2_q18[17]), .q2(shift_register_2_q18[16]), .q3(shift_register_2_q18[15]),
    .q4(shift_register_2_q18[14]), .q5(shift_register_2_q18[13]), .q6(shift_register_2_q18[12]),
    .q7(shift_register_2_q18[11]), .q8(shift_register_2_q18[10]), .q9(shift_register_2_q18[9]),
    .q10(shift_register_2_q18[8]), .q11(shift_register_2_q18[7]), .q12(shift_register_2_q18[6]),
    .q13(shift_register_2_q18[5]), .q14(shift_register_2_q18[4]), .q15(shift_register_2_q18[3]),
    .q16(shift_register_2_q18[2]), .q17(shift_register_2_q18[1]), .q18(shift_register_2_q18[0]));  // open: shift, load, clr, d0, d1, d2, d3, d4, d5, d6, d7, d8, d9, d10, d11, d12, d13, d14, d15, d16, d17, d18
  DotMatrix #(.matrixcols(19), .matrixrows(1)) dotmatrix_7 (
    .col0(shift_register_2_q18[18]), .col1(shift_register_2_q18[17]), .col2(shift_register_2_q18[16]),
    .col3(shift_register_2_q18[15]), .col4(shift_register_2_q18[14]), .col5(shift_register_2_q18[13]),
    .col6(shift_register_2_q18[12]), .col7(shift_register_2_q18[11]), .col8(shift_register_2_q18[10]),
    .col9(shift_register_2_q18[9]), .col10(shift_register_2_q18[8]), .col11(shift_register_2_q18[7]),
    .col12(shift_register_2_q18[6]), .col13(shift_register_2_q18[5]), .col14(shift_register_2_q18[4]),
    .col15(shift_register_2_q18[3]), .col16(shift_register_2_q18[2]), .col17(shift_register_2_q18[1]),
    .col18(shift_register_2_q18[0]));
  DotMatrix dotmatrix_8 (
    .col0(main_6_col_1), .col1(main_6_col_2), .col2(main_6_col_3), .col3(main_6_col_4), .col4(main_6_col_5));
  matriz_led_main main_5 (
    .Col_1(main_5_col_1), .Col_2(main_5_col_2), .Col_3(main_5_col_3), .Col_4(main_5_col_4),
    .Col_5(main_5_col_5), .in_1(Letra_5[5]), .in_2(Letra_5[4]), .in_3(Letra_5[3]), .in_4(Letra_5[2]),
    .in_5(Letra_5[1]), .in_6(Letra_5[0]), .Letra(main_5_letra));
  DotMatrix dotmatrix_9 (
    .col0(main_7_col_1), .col1(main_7_col_2), .col2(main_7_col_3), .col3(main_7_col_4), .col4(main_7_col_5));
  matriz_led_main main_6 (
    .Col_1(main_6_col_1), .Col_2(main_6_col_2), .Col_3(main_6_col_3), .Col_4(main_6_col_4),
    .Col_5(main_6_col_5), .in_1(Letra_1_2[5]), .in_2(Letra_1_2[4]), .in_3(Letra_1_2[3]), .in_4(Letra_1_2[2]),
    .in_5(Letra_1_2[1]), .in_6(Letra_1_2[0]), .Letra(main_6_letra));
  GrayToBin graytobin_1 (
    .a(sensor_1_out_39[5]), .b(sensor_1_out_39[4]), .c(sensor_1_out_39[3]), .d(sensor_1_out_39[2]),
    .e(sensor_1_out_39[1]), .f(sensor_1_out_39[0]), .A_2(graytobin_1_f_2[5]), .B_2(graytobin_1_f_2[4]),
    .C_2(graytobin_1_f_2[3]), .D_2(graytobin_1_f_2[2]), .E_2(graytobin_1_f_2[1]), .F_2(graytobin_1_f_2[0]));
  DotMatrix dotmatrix_10 (
    .col0(main_8_col_1), .col1(main_8_col_2), .col2(main_8_col_3), .col3(main_8_col_4), .col4(main_8_col_5));
  matriz_led_main main_7 (
    .Col_1(main_7_col_1), .Col_2(main_7_col_2), .Col_3(main_7_col_3), .Col_4(main_7_col_4),
    .Col_5(main_7_col_5), .in_1(Letra_1_3[5]), .in_2(Letra_1_3[4]), .in_3(Letra_1_3[3]), .in_4(Letra_1_3[2]),
    .in_5(Letra_1_3[1]), .in_6(Letra_1_3[0]), .Letra(main_7_letra));
  DotMatrix dotmatrix_11 (
    .col0(main_9_col_1), .col1(main_9_col_2), .col2(main_9_col_3), .col3(main_9_col_4), .col4(main_9_col_5));
  matriz_led_main main_8 (
    .Col_1(main_8_col_1), .Col_2(main_8_col_2), .Col_3(main_8_col_3), .Col_4(main_8_col_4),
    .Col_5(main_8_col_5), .in_1(Letra_1_4[5]), .in_2(Letra_1_4[4]), .in_3(Letra_1_4[3]), .in_4(Letra_1_4[2]),
    .in_5(Letra_1_4[1]), .in_6(Letra_1_4[0]), .Letra(main_8_letra));
  matriz_led_main main_9 (
    .Col_1(main_9_col_1), .Col_2(main_9_col_2), .Col_3(main_9_col_3), .Col_4(main_9_col_4),
    .Col_5(main_9_col_5), .in_1(Letra_1_5[5]), .in_2(Letra_1_5[4]), .in_3(Letra_1_5[3]), .in_4(Letra_1_5[2]),
    .in_5(Letra_1_5[1]), .in_6(Letra_1_5[0]), .Letra(main_9_letra));
  DotMatrix dotmatrix_12 (
    .col0(main_10_col_1), .col1(main_10_col_2), .col2(main_10_col_3), .col3(main_10_col_4),
    .col4(main_10_col_5));
  DotMatrix dotmatrix_13 (
    .col0(main_11_col_1), .col1(main_11_col_2), .col2(main_11_col_3), .col3(main_11_col_4),
    .col4(main_11_col_5));
  matriz_led_main main_10 (
    .Col_1(main_10_col_1), .Col_2(main_10_col_2), .Col_3(main_10_col_3), .Col_4(main_10_col_4),
    .Col_5(main_10_col_5), .in_1(Letra_1_6[5]), .in_2(Letra_1_6[4]), .in_3(Letra_1_6[3]),
    .in_4(Letra_1_6[2]), .in_5(Letra_1_6[1]), .in_6(Letra_1_6[0]), .Letra(main_10_letra));
  display display_1 (
    .Num(graytobin_1_f_2), .g2(display_1_b2[3]), .f2(display_1_b2[2]), .a2(display_1_b2[1]),
    .b2(display_1_b2[0]), .g1(display_1_b1[3]), .f1(display_1_b1[2]), .a1(display_1_b1[1]),
    .b1(display_1_b1[0]), .e2(display_1_c2[2]), .d2(display_1_c2[1]), .c2(display_1_c2[0]),
    .e1(display_1_c1[2]), .d1(display_1_c1[1]), .c1(display_1_c1[0]));
  DotMatrix dotmatrix_14 (
    .col0(main_12_col_1), .col1(main_12_col_2), .col2(main_12_col_3), .col3(main_12_col_4),
    .col4(main_12_col_5));
  matriz_led_main main_11 (
    .Col_1(main_11_col_1), .Col_2(main_11_col_2), .Col_3(main_11_col_3), .Col_4(main_11_col_4),
    .Col_5(main_11_col_5), .in_1(Letra_1_7[5]), .in_2(Letra_1_7[4]), .in_3(Letra_1_7[3]),
    .in_4(Letra_1_7[2]), .in_5(Letra_1_7[1]), .in_6(Letra_1_7[0]), .Letra(main_11_letra));
  _7_Segment_Display u_7_segment_display_1 (
    .g(display_1_b2[3]), .f(display_1_b2[2]), .a(display_1_b2[1]), .b(display_1_b2[0]), .e(display_1_c2[2]),
    .d(display_1_c2[1]), .c(display_1_c2[0]));  // open: dp
  _7_Segment_Display u_7_segment_display_2 (
    .g(display_1_b1[3]), .f(display_1_b1[2]), .a(display_1_b1[1]), .b(display_1_b1[0]), .e(display_1_c1[2]),
    .d(display_1_c1[1]), .c(display_1_c1[0]));  // open: dp
  DotMatrix dotmatrix_15 (
    .col0(main_13_col_1), .col1(main_13_col_2), .col2(main_13_col_3), .col3(main_13_col_4),
    .col4(main_13_col_5));
  matriz_led_main main_12 (
    .Col_1(main_12_col_1), .Col_2(main_12_col_2), .Col_3(main_12_col_3), .Col_4(main_12_col_4),
    .Col_5(main_12_col_5), .in_1(Letra_1_8[5]), .in_2(Letra_1_8[4]), .in_3(Letra_1_8[3]),
    .in_4(Letra_1_8[2]), .in_5(Letra_1_8[1]), .in_6(Letra_1_8[0]), .Letra(main_12_letra));
  DotMatrix dotmatrix_16 (
    .col0(main_14_col_1), .col1(main_14_col_2), .col2(main_14_col_3), .col3(main_14_col_4),
    .col4(main_14_col_5));
  matriz_led_main main_13 (
    .Col_1(main_13_col_1), .Col_2(main_13_col_2), .Col_3(main_13_col_3), .Col_4(main_13_col_4),
    .Col_5(main_13_col_5), .in_1(Letra_1_9[5]), .in_2(Letra_1_9[4]), .in_3(Letra_1_9[3]),
    .in_4(Letra_1_9[2]), .in_5(Letra_1_9[1]), .in_6(Letra_1_9[0]), .Letra(main_13_letra));
  Circuito circuito_1 (
    .Sensor(graytobin_1_f_2), .Letra_1(main_1_letra), .Letra_2(main_2_letra), .Letra_3(main_3_letra),
    .Letra_4(main_4_letra), .Letra_5(main_5_letra), .Letra_6(main_6_letra), .Letra_7(main_7_letra),
    .Letra_8(main_8_letra), .Letra_9(main_9_letra), .Letra_10(main_10_letra), .Letra_11(main_11_letra),
    .Letra_12(main_12_letra), .Letra_13(main_13_letra), .Letra_14(main_14_letra), .Letra_15(main_15_letra),
    .Letra_16(main_16_letra), .Letra_17(main_17_letra), .Letra_18(main_18_letra), .Letra_19(main_19_letra),
    .Letra_20(main_20_letra), .M1(circuito_1_m20[19]), .M2(circuito_1_m20[18]), .M3(circuito_1_m20[17]),
    .M4(circuito_1_m20[16]), .M5(circuito_1_m20[15]), .M6(circuito_1_m20[14]), .M7(circuito_1_m20[13]),
    .M8(circuito_1_m20[12]), .M9(circuito_1_m20[11]), .M10(circuito_1_m20[10]), .M11(circuito_1_m20[9]),
    .M12(circuito_1_m20[8]), .M13(circuito_1_m20[7]), .M14(circuito_1_m20[6]), .M15(circuito_1_m20[5]),
    .M16(circuito_1_m20[4]), .M17(circuito_1_m20[3]), .M18(circuito_1_m20[2]), .M19(circuito_1_m20[1]),
    .M20(circuito_1_m20[0]));
  DotMatrix #(.matrixcols(1), .matrixrows(20)) dotmatrix_17 (.col0(circuito_1_m20));
  DotMatrix dotmatrix_18 (
    .col0(main_15_col_1), .col1(main_15_col_2), .col2(main_15_col_3), .col3(main_15_col_4),
    .col4(main_15_col_5));
  matriz_led_main main_14 (
    .Col_1(main_14_col_1), .Col_2(main_14_col_2), .Col_3(main_14_col_3), .Col_4(main_14_col_4),
    .Col_5(main_14_col_5), .in_1(Letra_1_10[5]), .in_2(Letra_1_10[4]), .in_3(Letra_1_10[3]),
    .in_4(Letra_1_10[2]), .in_5(Letra_1_10[1]), .in_6(Letra_1_10[0]), .Letra(main_14_letra));
  DotMatrix dotmatrix_19 (
    .col0(main_16_col_1), .col1(main_16_col_2), .col2(main_16_col_3), .col3(main_16_col_4),
    .col4(main_16_col_5));
  matriz_led_main main_15 (
    .Col_1(main_15_col_1), .Col_2(main_15_col_2), .Col_3(main_15_col_3), .Col_4(main_15_col_4),
    .Col_5(main_15_col_5), .in_1(Letra_1_11[5]), .in_2(Letra_1_11[4]), .in_3(Letra_1_11[3]),
    .in_4(Letra_1_11[2]), .in_5(Letra_1_11[1]), .in_6(Letra_1_11[0]), .Letra(main_15_letra));
  DotMatrix dotmatrix_20 (
    .col0(main_17_col_1), .col1(main_17_col_2), .col2(main_17_col_3), .col3(main_17_col_4),
    .col4(main_17_col_5));
  matriz_led_main main_16 (
    .Col_1(main_16_col_1), .Col_2(main_16_col_2), .Col_3(main_16_col_3), .Col_4(main_16_col_4),
    .Col_5(main_16_col_5), .in_1(Letra_1_12[5]), .in_2(Letra_1_12[4]), .in_3(Letra_1_12[3]),
    .in_4(Letra_1_12[2]), .in_5(Letra_1_12[1]), .in_6(Letra_1_12[0]), .Letra(main_16_letra));
  matriz_led_main main_17 (
    .Col_1(main_17_col_1), .Col_2(main_17_col_2), .Col_3(main_17_col_3), .Col_4(main_17_col_4),
    .Col_5(main_17_col_5), .in_1(Letra_1_13[5]), .in_2(Letra_1_13[4]), .in_3(Letra_1_13[3]),
    .in_4(Letra_1_13[2]), .in_5(Letra_1_13[1]), .in_6(Letra_1_13[0]), .Letra(main_17_letra));
  DotMatrix dotmatrix_21 (
    .col0(main_18_col_1), .col1(main_18_col_2), .col2(main_18_col_3), .col3(main_18_col_4),
    .col4(main_18_col_5));
  DotMatrix dotmatrix_22 (
    .col0(main_19_col_1), .col1(main_19_col_2), .col2(main_19_col_3), .col3(main_19_col_4),
    .col4(main_19_col_5));
  matriz_led_main main_18 (
    .Col_1(main_18_col_1), .Col_2(main_18_col_2), .Col_3(main_18_col_3), .Col_4(main_18_col_4),
    .Col_5(main_18_col_5), .in_1(Letra_1_14[5]), .in_2(Letra_1_14[4]), .in_3(Letra_1_14[3]),
    .in_4(Letra_1_14[2]), .in_5(Letra_1_14[1]), .in_6(Letra_1_14[0]), .Letra(main_18_letra));
  DotMatrix dotmatrix_23 (
    .col0(main_20_col_1), .col1(main_20_col_2), .col2(main_20_col_3), .col3(main_20_col_4),
    .col4(main_20_col_5));
  matriz_led_main main_19 (
    .Col_1(main_19_col_1), .Col_2(main_19_col_2), .Col_3(main_19_col_3), .Col_4(main_19_col_4),
    .Col_5(main_19_col_5), .in_1(Letra_1_15[5]), .in_2(Letra_1_15[4]), .in_3(Letra_1_15[3]),
    .in_4(Letra_1_15[2]), .in_5(Letra_1_15[1]), .in_6(Letra_1_15[0]), .Letra(main_19_letra));
  matriz_led_main main_20 (
    .Col_1(main_20_col_1), .Col_2(main_20_col_2), .Col_3(main_20_col_3), .Col_4(main_20_col_4),
    .Col_5(main_20_col_5), .in_1(Letra_1_16[5]), .in_2(Letra_1_16[4]), .in_3(Letra_1_16[3]),
    .in_4(Letra_1_16[2]), .in_5(Letra_1_16[1]), .in_6(Letra_1_16[0]), .Letra(main_20_letra));

  // Notes on the sheet:
  //   ABCDEFGHIJKLMNOPQRSTUVWXYZ 0123456789
endmodule

// COMP
module Comparador (
  input  [5:0] Letra1,
  input  [5:0] Letra2,
  output out_3
);

  wire xnor_1_out, xnor_2_out, xnor_3_out, xnor_4_out, xnor_5_out, xnor_6_out;

  xnor xnor_1 (xnor_1_out, Letra1[0], Letra2[0]);
  xnor xnor_2 (xnor_2_out, Letra1[1], Letra2[1]);
  xnor xnor_3 (xnor_3_out, Letra1[2], Letra2[2]);
  xnor xnor_4 (xnor_4_out, Letra1[3], Letra2[3]);
  xnor xnor_5 (xnor_5_out, Letra1[4], Letra2[4]);
  xnor xnor_6 (xnor_6_out, Letra1[5], Letra2[5]);
  and and_1 (out_3, xnor_1_out, xnor_2_out, xnor_3_out, xnor_4_out, xnor_5_out, xnor_6_out);
endmodule

module Sensor (
  input  in_1,
  input  in_2,
  input  in_3,
  input  in_4,
  input  in_5,
  input  in_6,
  input  in_7,
  input  in_8,
  input  in_9,
  input  in_10,
  input  in_11,
  input  in_12,
  input  in_13,
  input  in_14,
  input  in_15,
  input  in_16,
  input  in_17,
  input  in_18,
  input  in_19,
  input  in_20,
  input  in_21,
  input  in_22,
  input  in_23,
  input  in_24,
  input  in_25,
  input  in_26,
  input  in_27,
  input  in_28,
  input  in_29,
  input  in_30,
  input  in_31,
  input  in_32,
  input  in_33,
  input  in_34,
  input  in_35,
  input  in_36,
  input  in_37,
  input  in_38,
  output out_39,
  output out_40,
  output out_41,
  output out_42,
  output out_43,
  output out_44
);

  wire conversor0_1_s0, conversor0_1_s1, conversor0_1_s2, conversor0_1_s3, conversor0_1_s4, conversor0_1_s5,
       conversor1_1_s0, conversor1_1_s1, conversor1_1_s2, conversor1_1_s3, conversor1_1_s4, conversor1_1_s5,
       conversor2_1_s0, conversor2_1_s1, conversor2_1_s2, conversor2_1_s3, conversor2_1_s4, conversor2_1_s5,
       conversor3_1_s0, conversor3_1_s1, conversor3_1_s2, conversor3_1_s3, conversor3_1_s4, conversor3_1_s5,
       conversor4_1_s0, conversor4_1_s1, conversor4_1_s2, conversor4_1_s3, conversor4_1_s4, conversor4_1_s5,
       conversor5_1_s0, conversor5_1_s1, conversor5_1_s2, conversor5_1_s3, conversor5_1_s4, conversor5_1_s5;

  or or_1 (out_39, conversor0_1_s0, conversor1_1_s0, conversor2_1_s0, conversor3_1_s0, conversor4_1_s0, conversor5_1_s0);
  Conversor0 conversor0_1 (
    .e6(in_7), .e5(in_6), .e4(in_5), .e3(in_4), .e2(in_3), .e1(in_2), .e0(in_1), .s5(conversor0_1_s5),
    .s4(conversor0_1_s4), .s3(conversor0_1_s3), .s2(conversor0_1_s2), .s1(conversor0_1_s1),
    .s0(conversor0_1_s0));
  or or_2 (out_40, conversor0_1_s1, conversor1_1_s1, conversor2_1_s1, conversor3_1_s1, conversor4_1_s1, conversor5_1_s1);
  Conversor1 conversor1_1 (
    .e6(in_14), .e5(in_13), .e4(in_12), .e3(in_11), .e2(in_10), .e1(in_9), .e0(in_8), .s5(conversor1_1_s5),
    .s4(conversor1_1_s4), .s3(conversor1_1_s3), .s2(conversor1_1_s2), .s1(conversor1_1_s1),
    .s0(conversor1_1_s0));
  or or_3 (out_41, conversor0_1_s2, conversor1_1_s2, conversor2_1_s2, conversor3_1_s2, conversor4_1_s2, conversor5_1_s2);
  Conversor3 conversor3_1 (
    .e6(in_28), .e5(in_27), .e4(in_26), .e3(in_25), .e2(in_24), .e1(in_23), .e0(in_22), .s5(conversor3_1_s5),
    .s4(conversor3_1_s4), .s3(conversor3_1_s3), .s2(conversor3_1_s2), .s1(conversor3_1_s1),
    .s0(conversor3_1_s0));
  Conversor2 conversor2_1 (
    .e6(in_21), .e5(in_20), .e4(in_19), .e3(in_18), .e2(in_17), .e1(in_16), .e0(in_15), .s5(conversor2_1_s5),
    .s4(conversor2_1_s4), .s3(conversor2_1_s3), .s2(conversor2_1_s2), .s1(conversor2_1_s1),
    .s0(conversor2_1_s0));
  or or_4 (out_42, conversor0_1_s3, conversor1_1_s3, conversor2_1_s3, conversor3_1_s3, conversor4_1_s3, conversor5_1_s3);
  Conversor4 conversor4_1 (
    .e6(in_35), .e5(in_34), .e4(in_33), .e3(in_32), .e2(in_31), .e1(in_30), .e0(in_29), .s5(conversor4_1_s5),
    .s4(conversor4_1_s4), .s3(conversor4_1_s3), .s2(conversor4_1_s2), .s1(conversor4_1_s1),
    .s0(conversor4_1_s0));
  or or_5 (out_43, conversor0_1_s4, conversor1_1_s4, conversor2_1_s4, conversor3_1_s4, conversor4_1_s4, conversor5_1_s4);
  Conversor5 conversor5_1 (
    .e2(in_38), .e1(in_37), .e0(in_36), .s5(conversor5_1_s5), .s4(conversor5_1_s4), .s3(conversor5_1_s3),
    .s2(conversor5_1_s2), .s1(conversor5_1_s1), .s0(conversor5_1_s0));
  or or_6 (out_44, conversor0_1_s5, conversor1_1_s5, conversor2_1_s5, conversor3_1_s5, conversor4_1_s5, conversor5_1_s5);
endmodule

module Conversor0 (
  input  e6,
  input  e5,
  input  e4,
  input  e3,
  input  e2,
  input  e1,
  input  e0,
  output s5,
  output s4,
  output s3,
  output s2,
  output s1,
  output s0
);

  wire and_1_out, and_2_out, and_3_out, and_4_out, and_5_out, and_6_out, and_7_out, and_8_out, and_9_out,
       and_10_out, and_11_out, and_12_out, not_1_out, not_2_out, not_3_out, not_4_out, not_5_out, not_6_out,
       not_7_out, not_8_out, not_9_out, not_10_out, not_11_out, not_12_out, not_13_out, not_14_out,
       not_15_out, not_16_out, not_17_out, not_18_out, not_19_out, not_20_out, not_21_out, not_22_out,
       not_23_out, not_24_out, not_25_out, not_26_out, not_27_out, not_28_out, not_29_out, not_30_out,
       not_31_out, not_32_out, not_33_out, not_34_out, not_35_out, not_36_out, not_37_out, not_38_out,
       not_39_out, not_40_out, not_41_out, not_42_out, not_43_out, not_44_out, not_45_out, not_46_out,
       not_47_out, not_48_out, not_49_out, not_50_out, not_51_out, not_52_out, not_53_out, not_54_out,
       not_55_out, not_56_out, not_57_out, not_58_out, not_59_out, not_60_out, not_61_out, not_62_out,
       not_63_out, not_64_out, not_65_out, not_66_out, not_67_out, not_68_out, not_69_out, not_70_out,
       not_71_out, not_72_out;

  not not_1 (not_1_out, e6);
  not not_2 (not_2_out, e5);
  not not_3 (not_3_out, e4);
  not not_4 (not_4_out, e2);
  not not_5 (not_5_out, e1);
  not not_6 (not_6_out, e0);
  not not_7 (not_7_out, e6);
  not not_8 (not_8_out, e5);
  not not_9 (not_9_out, e3);
  not not_10 (not_10_out, e2);
  not not_11 (not_11_out, e1);
  not not_12 (not_12_out, e0);
  not not_13 (not_13_out, e6);
  not not_14 (not_14_out, e4);
  not not_15 (not_15_out, e3);
  not not_16 (not_16_out, e2);
  not not_17 (not_17_out, e1);
  not not_18 (not_18_out, e0);
  not not_19 (not_19_out, e5);
  not not_20 (not_20_out, e4);
  not not_21 (not_21_out, e3);
  not not_22 (not_22_out, e2);
  not not_23 (not_23_out, e1);
  not not_24 (not_24_out, e0);
  not not_25 (not_25_out, e6);
  not not_26 (not_26_out, e5);
  not not_27 (not_27_out, e4);
  not not_28 (not_28_out, e3);
  not not_29 (not_29_out, e2);
  not not_30 (not_30_out, e0);
  not not_31 (not_31_out, e6);
  not not_32 (not_32_out, e5);
  not not_33 (not_33_out, e4);
  not not_34 (not_34_out, e3);
  not not_35 (not_35_out, e1);
  not not_36 (not_36_out, e0);
  not not_37 (not_37_out, e6);
  not not_38 (not_38_out, e5);
  not not_39 (not_39_out, e4);
  not not_40 (not_40_out, e2);
  not not_41 (not_41_out, e1);
  not not_42 (not_42_out, e0);
  not not_43 (not_43_out, e6);
  not not_44 (not_44_out, e5);
  not not_45 (not_45_out, e3);
  not not_46 (not_46_out, e2);
  not not_47 (not_47_out, e1);
  not not_48 (not_48_out, e0);
  not not_49 (not_49_out, e6);
  not not_50 (not_50_out, e5);
  not not_51 (not_51_out, e4);
  not not_52 (not_52_out, e3);
  not not_53 (not_53_out, e2);
  not not_54 (not_54_out, e1);
  not not_55 (not_55_out, e6);
  not not_56 (not_56_out, e5);
  not not_57 (not_57_out, e4);
  not not_58 (not_58_out, e3);
  not not_59 (not_59_out, e2);
  not not_60 (not_60_out, e0);
  not not_61 (not_61_out, e6);
  not not_62 (not_62_out, e5);
  not not_63 (not_63_out, e3);
  not not_64 (not_64_out, e2);
  not not_65 (not_65_out, e1);
  not not_66 (not_66_out, e0);
  not not_67 (not_67_out, e6);
  not not_68 (not_68_out, e4);
  not not_69 (not_69_out, e3);
  not not_70 (not_70_out, e2);
  not not_71 (not_71_out, e1);
  not not_72 (not_72_out, e0);
  and and_1 (and_1_out, not_1_out, not_2_out, not_3_out, e3, not_4_out, not_5_out, not_6_out);
  and and_2 (and_2_out, not_7_out, not_8_out, e4, not_9_out, not_10_out, not_11_out, not_12_out);
  and and_3 (and_3_out, not_13_out, e5, not_14_out, not_15_out, not_16_out, not_17_out, not_18_out);
  and and_4 (and_4_out, e6, not_19_out, not_20_out, not_21_out, not_22_out, not_23_out, not_24_out);
  and and_5 (and_5_out, not_25_out, not_26_out, not_27_out, not_28_out, not_29_out, e1, not_30_out);
  and and_6 (and_6_out, not_31_out, not_32_out, not_33_out, not_34_out, e2, not_35_out, not_36_out);
  and and_7 (and_7_out, not_37_out, not_38_out, not_39_out, e3, not_40_out, not_41_out, not_42_out);
  and and_8 (and_8_out, not_43_out, not_44_out, e4, not_45_out, not_46_out, not_47_out, not_48_out);
  and and_9 (and_9_out, not_49_out, not_50_out, not_51_out, not_52_out, not_53_out, not_54_out, e0);
  and and_10 (and_10_out, not_55_out, not_56_out, not_57_out, not_58_out, not_59_out, e1, not_60_out);
  and and_11 (and_11_out, not_61_out, not_62_out, e4, not_63_out, not_64_out, not_65_out, not_66_out);
  and and_12 (and_12_out, not_67_out, e5, not_68_out, not_69_out, not_70_out, not_71_out, not_72_out);
  or or_1 (s2, and_1_out, and_2_out, and_3_out, and_4_out);
  or or_2 (s1, and_5_out, and_6_out, and_7_out, and_8_out);
  or or_3 (s0, and_9_out, and_10_out, and_11_out, and_12_out);

  assign s3 = 1'b0;
  assign s4 = 1'b0;
  assign s5 = 1'b0;
endmodule

module Conversor1 (
  input  e6,
  input  e5,
  input  e4,
  input  e3,
  input  e2,
  input  e1,
  input  e0,
  output s5,
  output s4,
  output s3,
  output s2,
  output s1,
  output s0
);

  wire and_1_out, and_2_out, and_3_out, and_4_out, and_5_out, and_6_out, and_7_out, and_8_out, and_9_out,
       and_10_out, and_11_out, and_12_out, and_13_out, and_14_out, and_15_out, and_16_out, and_17_out,
       and_18_out, and_19_out, not_1_out, not_2_out, not_3_out, not_4_out, not_5_out, not_6_out, not_7_out,
       not_8_out, not_9_out, not_10_out, not_11_out, not_12_out, not_13_out, not_14_out, not_15_out,
       not_16_out, not_17_out, not_18_out, not_19_out, not_20_out, not_21_out, not_22_out, not_23_out,
       not_24_out, not_25_out, not_26_out, not_27_out, not_28_out, not_29_out, not_30_out, not_31_out,
       not_32_out, not_33_out, not_34_out, not_35_out, not_36_out, not_37_out, not_38_out, not_39_out,
       not_40_out, not_41_out, not_42_out, not_43_out, not_44_out, not_45_out, not_46_out, not_47_out,
       not_48_out, not_49_out, not_50_out, not_51_out, not_52_out, not_53_out, not_54_out, not_55_out,
       not_56_out, not_57_out, not_58_out, not_59_out, not_60_out, not_61_out, not_62_out, not_63_out,
       not_64_out, not_65_out, not_66_out, not_67_out, not_68_out, not_69_out, not_70_out, not_71_out,
       not_72_out, not_73_out, not_74_out, not_75_out, not_76_out, not_77_out, not_78_out, not_79_out,
       not_80_out, not_81_out, not_82_out, not_83_out, not_84_out, not_85_out, not_86_out, not_87_out,
       not_88_out, not_89_out, not_90_out, not_91_out, not_92_out, not_93_out, not_94_out, not_95_out,
       not_96_out, not_97_out, not_98_out, not_99_out, not_100_out, not_101_out, not_102_out, not_103_out,
       not_104_out, not_105_out, not_106_out, not_107_out, not_108_out, not_109_out, not_110_out,
       not_111_out, not_112_out, not_113_out, not_114_out;

  not not_1 (not_1_out, e6);
  not not_2 (not_2_out, e5);
  not not_3 (not_3_out, e4);
  not not_4 (not_4_out, e3);
  not not_5 (not_5_out, e2);
  not not_6 (not_6_out, e1);
  not not_7 (not_7_out, e6);
  not not_8 (not_8_out, e5);
  not not_9 (not_9_out, e4);
  not not_10 (not_10_out, e3);
  not not_11 (not_11_out, e2);
  not not_12 (not_12_out, e0);
  not not_13 (not_13_out, e6);
  not not_14 (not_14_out, e5);
  not not_15 (not_15_out, e4);
  not not_16 (not_16_out, e3);
  not not_17 (not_17_out, e1);
  not not_18 (not_18_out, e0);
  not not_19 (not_19_out, e6);
  not not_20 (not_20_out, e5);
  not not_21 (not_21_out, e4);
  not not_22 (not_22_out, e2);
  not not_23 (not_23_out, e1);
  not not_24 (not_24_out, e0);
  not not_25 (not_25_out, e6);
  not not_26 (not_26_out, e5);
  not not_27 (not_27_out, e3);
  not not_28 (not_28_out, e2);
  not not_29 (not_29_out, e1);
  not not_30 (not_30_out, e0);
  not not_31 (not_31_out, e6);
  not not_32 (not_32_out, e4);
  not not_33 (not_33_out, e3);
  not not_34 (not_34_out, e2);
  not not_35 (not_35_out, e1);
  not not_36 (not_36_out, e0);
  not not_37 (not_37_out, e5);
  not not_38 (not_38_out, e4);
  not not_39 (not_39_out, e3);
  not not_40 (not_40_out, e2);
  not not_41 (not_41_out, e1);
  not not_42 (not_42_out, e0);
  not not_43 (not_43_out, e6);
  not not_44 (not_44_out, e5);
  not not_45 (not_45_out, e4);
  not not_46 (not_46_out, e3);
  not not_47 (not_47_out, e2);
  not not_48 (not_48_out, e1);
  not not_49 (not_49_out, e6);
  not not_50 (not_50_out, e5);
  not not_51 (not_51_out, e4);
  not not_52 (not_52_out, e3);
  not not_53 (not_53_out, e2);
  not not_54 (not_54_out, e0);
  not not_55 (not_55_out, e6);
  not not_56 (not_56_out, e5);
  not not_57 (not_57_out, e4);
  not not_58 (not_58_out, e3);
  not not_59 (not_59_out, e1);
  not not_60 (not_60_out, e0);
  not not_61 (not_61_out, e6);
  not not_62 (not_62_out, e5);
  not not_63 (not_63_out, e4);
  not not_64 (not_64_out, e2);
  not not_65 (not_65_out, e1);
  not not_66 (not_66_out, e0);
  not not_67 (not_67_out, e6);
  not not_68 (not_68_out, e5);
  not not_69 (not_69_out, e4);
  not not_70 (not_70_out, e3);
  not not_71 (not_71_out, e1);
  not not_72 (not_72_out, e0);
  not not_73 (not_73_out, e6);
  not not_74 (not_74_out, e5);
  not not_75 (not_75_out, e4);
  not not_76 (not_76_out, e2);
  not not_77 (not_77_out, e1);
  not not_78 (not_78_out, e0);
  not not_79 (not_79_out, e6);
  not not_80 (not_80_out, e5);
  not not_81 (not_81_out, e3);
  not not_82 (not_82_out, e2);
  not not_83 (not_83_out, e1);
  not not_84 (not_84_out, e0);
  not not_85 (not_85_out, e6);
  not not_86 (not_86_out, e4);
  not not_87 (not_87_out, e3);
  not not_88 (not_88_out, e2);
  not not_89 (not_89_out, e1);
  not not_90 (not_90_out, e0);
  not not_91 (not_91_out, e6);
  not not_92 (not_92_out, e5);
  not not_93 (not_93_out, e4);
  not not_94 (not_94_out, e3);
  not not_95 (not_95_out, e2);
  not not_96 (not_96_out, e0);
  not not_97 (not_97_out, e6);
  not not_98 (not_98_out, e5);
  not not_99 (not_99_out, e4);
  not not_100 (not_100_out, e3);
  not not_101 (not_101_out, e1);
  not not_102 (not_102_out, e0);
  not not_103 (not_103_out, e6);
  not not_104 (not_104_out, e4);
  not not_105 (not_105_out, e3);
  not not_106 (not_106_out, e2);
  not not_107 (not_107_out, e1);
  not not_108 (not_108_out, e0);
  not not_109 (not_109_out, e5);
  not not_110 (not_110_out, e4);
  not not_111 (not_111_out, e3);
  not not_112 (not_112_out, e2);
  not not_113 (not_113_out, e1);
  not not_114 (not_114_out, e0);
  and and_1 (and_1_out, not_1_out, not_2_out, not_3_out, not_4_out, not_5_out, not_6_out, e0);
  and and_2 (and_2_out, not_7_out, not_8_out, not_9_out, not_10_out, not_11_out, e1, not_12_out);
  and and_3 (and_3_out, not_13_out, not_14_out, not_15_out, not_16_out, e2, not_17_out, not_18_out);
  and and_4 (and_4_out, not_19_out, not_20_out, not_21_out, e3, not_22_out, not_23_out, not_24_out);
  and and_5 (and_5_out, not_25_out, not_26_out, e4, not_27_out, not_28_out, not_29_out, not_30_out);
  and and_6 (and_6_out, not_31_out, e5, not_32_out, not_33_out, not_34_out, not_35_out, not_36_out);
  and and_7 (and_7_out, e6, not_37_out, not_38_out, not_39_out, not_40_out, not_41_out, not_42_out);
  and and_8 (and_8_out, not_43_out, not_44_out, not_45_out, not_46_out, not_47_out, not_48_out, e0);
  and and_9 (and_9_out, not_49_out, not_50_out, not_51_out, not_52_out, not_53_out, e1, not_54_out);
  and and_10 (and_10_out, not_55_out, not_56_out, not_57_out, not_58_out, e2, not_59_out, not_60_out);
  and and_11 (and_11_out, not_61_out, not_62_out, not_63_out, e3, not_64_out, not_65_out, not_66_out);
  and and_12 (and_12_out, not_67_out, not_68_out, not_69_out, not_70_out, e2, not_71_out, not_72_out);
  and and_13 (and_13_out, not_73_out, not_74_out, not_75_out, e3, not_76_out, not_77_out, not_78_out);
  and and_14 (and_14_out, not_79_out, not_80_out, e4, not_81_out, not_82_out, not_83_out, not_84_out);
  and and_15 (and_15_out, not_85_out, e5, not_86_out, not_87_out, not_88_out, not_89_out, not_90_out);
  and and_16 (and_16_out, not_91_out, not_92_out, not_93_out, not_94_out, not_95_out, e1, not_96_out);
  and and_17 (and_17_out, not_97_out, not_98_out, not_99_out, not_100_out, e2, not_101_out, not_102_out);
  and and_18 (and_18_out, not_103_out, e5, not_104_out, not_105_out, not_106_out, not_107_out, not_108_out);
  and and_19 (and_19_out, e6, not_109_out, not_110_out, not_111_out, not_112_out, not_113_out, not_114_out);
  or or_1 (s2, and_8_out, and_9_out, and_10_out, and_11_out);
  or or_2 (s1, and_12_out, and_13_out, and_14_out, and_15_out);
  or or_3 (s0, and_16_out, and_17_out, and_18_out, and_19_out);
  or or_4 (s3, and_1_out, and_2_out, and_3_out, and_4_out, and_5_out, and_6_out, and_7_out);

  assign s4 = 1'b0;
  assign s5 = 1'b0;
endmodule

module Conversor2 (
  input  e6,
  input  e5,
  input  e4,
  input  e3,
  input  e2,
  input  e1,
  input  e0,
  output s5,
  output s4,
  output s3,
  output s2,
  output s1,
  output s0
);

  wire and_1_out, and_2_out, and_3_out, and_4_out, and_5_out, and_6_out, and_7_out, and_8_out, and_9_out,
       and_10_out, and_11_out, and_12_out, and_13_out, and_14_out, and_15_out, and_16_out, and_17_out,
       and_18_out, and_19_out, and_20_out, and_21_out, and_22_out, not_1_out, not_2_out, not_3_out,
       not_4_out, not_5_out, not_6_out, not_7_out, not_8_out, not_9_out, not_10_out, not_11_out, not_12_out,
       not_13_out, not_14_out, not_15_out, not_16_out, not_17_out, not_18_out, not_19_out, not_20_out,
       not_21_out, not_22_out, not_23_out, not_24_out, not_25_out, not_26_out, not_27_out, not_28_out,
       not_29_out, not_30_out, not_31_out, not_32_out, not_33_out, not_34_out, not_35_out, not_36_out,
       not_37_out, not_38_out, not_39_out, not_40_out, not_41_out, not_42_out, not_43_out, not_44_out,
       not_45_out, not_46_out, not_47_out, not_48_out, not_49_out, not_50_out, not_51_out, not_52_out,
       not_53_out, not_54_out, not_55_out, not_56_out, not_57_out, not_58_out, not_59_out, not_60_out,
       not_61_out, not_62_out, not_63_out, not_64_out, not_65_out, not_66_out, not_67_out, not_68_out,
       not_69_out, not_70_out, not_71_out, not_72_out, not_73_out, not_74_out, not_75_out, not_76_out,
       not_77_out, not_78_out, not_79_out, not_80_out, not_81_out, not_82_out, not_83_out, not_84_out,
       not_85_out, not_86_out, not_87_out, not_88_out, not_89_out, not_90_out, not_91_out, not_92_out,
       not_93_out, not_94_out, not_95_out, not_96_out, not_97_out, not_98_out, not_99_out, not_100_out,
       not_101_out, not_102_out, not_103_out, not_104_out, not_105_out, not_106_out, not_107_out,
       not_108_out, not_109_out, not_110_out, not_111_out, not_112_out, not_113_out, not_114_out,
       not_115_out, not_116_out, not_117_out, not_118_out, not_119_out, not_120_out, not_121_out,
       not_122_out, not_123_out, not_124_out, not_125_out, not_126_out, not_127_out, not_128_out,
       not_129_out, not_130_out, not_131_out, not_132_out;

  not not_1 (not_1_out, e6);
  not not_2 (not_2_out, e5);
  not not_3 (not_3_out, e4);
  not not_4 (not_4_out, e3);
  not not_5 (not_5_out, e2);
  not not_6 (not_6_out, e0);
  not not_7 (not_7_out, e6);
  not not_8 (not_8_out, e5);
  not not_9 (not_9_out, e4);
  not not_10 (not_10_out, e3);
  not not_11 (not_11_out, e1);
  not not_12 (not_12_out, e0);
  not not_13 (not_13_out, e6);
  not not_14 (not_14_out, e5);
  not not_15 (not_15_out, e4);
  not not_16 (not_16_out, e2);
  not not_17 (not_17_out, e1);
  not not_18 (not_18_out, e0);
  not not_19 (not_19_out, e6);
  not not_20 (not_20_out, e5);
  not not_21 (not_21_out, e3);
  not not_22 (not_22_out, e2);
  not not_23 (not_23_out, e1);
  not not_24 (not_24_out, e0);
  not not_25 (not_25_out, e6);
  not not_26 (not_26_out, e4);
  not not_27 (not_27_out, e3);
  not not_28 (not_28_out, e2);
  not not_29 (not_29_out, e1);
  not not_30 (not_30_out, e0);
  not not_31 (not_31_out, e5);
  not not_32 (not_32_out, e4);
  not not_33 (not_33_out, e3);
  not not_34 (not_34_out, e2);
  not not_35 (not_35_out, e1);
  not not_36 (not_36_out, e0);
  not not_37 (not_37_out, e6);
  not not_38 (not_38_out, e5);
  not not_39 (not_39_out, e4);
  not not_40 (not_40_out, e3);
  not not_41 (not_41_out, e2);
  not not_42 (not_42_out, e1);
  not not_43 (not_43_out, e6);
  not not_44 (not_44_out, e5);
  not not_45 (not_45_out, e4);
  not not_46 (not_46_out, e3);
  not not_47 (not_47_out, e2);
  not not_48 (not_48_out, e0);
  not not_49 (not_49_out, e6);
  not not_50 (not_50_out, e5);
  not not_51 (not_51_out, e4);
  not not_52 (not_52_out, e3);
  not not_53 (not_53_out, e1);
  not not_54 (not_54_out, e0);
  not not_55 (not_55_out, e6);
  not not_56 (not_56_out, e5);
  not not_57 (not_57_out, e4);
  not not_58 (not_58_out, e2);
  not not_59 (not_59_out, e1);
  not not_60 (not_60_out, e0);
  not not_61 (not_61_out, e6);
  not not_62 (not_62_out, e5);
  not not_63 (not_63_out, e3);
  not not_64 (not_64_out, e2);
  not not_65 (not_65_out, e1);
  not not_66 (not_66_out, e0);
  not not_67 (not_67_out, e6);
  not not_68 (not_68_out, e4);
  not not_69 (not_69_out, e3);
  not not_70 (not_70_out, e2);
  not not_71 (not_71_out, e1);
  not not_72 (not_72_out, e0);
  not not_73 (not_73_out, e5);
  not not_74 (not_74_out, e4);
  not not_75 (not_75_out, e3);
  not not_76 (not_76_out, e2);
  not not_77 (not_77_out, e1);
  not not_78 (not_78_out, e0);
  not not_79 (not_79_out, e6);
  not not_80 (not_80_out, e4);
  not not_81 (not_81_out, e3);
  not not_82 (not_82_out, e2);
  not not_83 (not_83_out, e1);
  not not_84 (not_84_out, e0);
  not not_85 (not_85_out, e5);
  not not_86 (not_86_out, e4);
  not not_87 (not_87_out, e3);
  not not_88 (not_88_out, e2);
  not not_89 (not_89_out, e1);
  not not_90 (not_90_out, e0);
  not not_91 (not_91_out, e6);
  not not_92 (not_92_out, e5);
  not not_93 (not_93_out, e4);
  not not_94 (not_94_out, e2);
  not not_95 (not_95_out, e1);
  not not_96 (not_96_out, e0);
  not not_97 (not_97_out, e6);
  not not_98 (not_98_out, e5);
  not not_99 (not_99_out, e3);
  not not_100 (not_100_out, e2);
  not not_101 (not_101_out, e1);
  not not_102 (not_102_out, e0);
  not not_103 (not_103_out, e6);
  not not_104 (not_104_out, e4);
  not not_105 (not_105_out, e3);
  not not_106 (not_106_out, e2);
  not not_107 (not_107_out, e1);
  not not_108 (not_108_out, e0);
  not not_109 (not_109_out, e5);
  not not_110 (not_110_out, e4);
  not not_111 (not_111_out, e3);
  not not_112 (not_112_out, e2);
  not not_113 (not_113_out, e1);
  not not_114 (not_114_out, e0);
  not not_115 (not_115_out, e6);
  not not_116 (not_116_out, e5);
  not not_117 (not_117_out, e4);
  not not_118 (not_118_out, e3);
  not not_119 (not_119_out, e1);
  not not_120 (not_120_out, e0);
  not not_121 (not_121_out, e6);
  not not_122 (not_122_out, e5);
  not not_123 (not_123_out, e4);
  not not_124 (not_124_out, e2);
  not not_125 (not_125_out, e1);
  not not_126 (not_126_out, e0);
  not not_127 (not_127_out, e5);
  not not_128 (not_128_out, e4);
  not not_129 (not_129_out, e3);
  not not_130 (not_130_out, e2);
  not not_131 (not_131_out, e1);
  not not_132 (not_132_out, e0);
  and and_1 (and_1_out, not_1_out, not_2_out, not_3_out, not_4_out, not_5_out, e1, not_6_out);
  and and_2 (and_2_out, not_7_out, not_8_out, not_9_out, not_10_out, e2, not_11_out, not_12_out);
  and and_3 (and_3_out, not_13_out, not_14_out, not_15_out, e3, not_16_out, not_17_out, not_18_out);
  and and_4 (and_4_out, not_19_out, not_20_out, e4, not_21_out, not_22_out, not_23_out, not_24_out);
  and and_5 (and_5_out, not_25_out, e5, not_26_out, not_27_out, not_28_out, not_29_out, not_30_out);
  and and_6 (and_6_out, e6, not_31_out, not_32_out, not_33_out, not_34_out, not_35_out, not_36_out);
  and and_7 (and_7_out, not_37_out, not_38_out, not_39_out, not_40_out, not_41_out, not_42_out, e0);
  and and_8 (and_8_out, not_43_out, not_44_out, not_45_out, not_46_out, not_47_out, e1, not_48_out);
  and and_9 (and_9_out, not_49_out, not_50_out, not_51_out, not_52_out, e2, not_53_out, not_54_out);
  and and_10 (and_10_out, not_55_out, not_56_out, not_57_out, e3, not_58_out, not_59_out, not_60_out);
  and and_11 (and_11_out, not_61_out, not_62_out, e4, not_63_out, not_64_out, not_65_out, not_66_out);
  and and_12 (and_12_out, not_67_out, e5, not_68_out, not_69_out, not_70_out, not_71_out, not_72_out);
  and and_13 (and_13_out, e6, not_73_out, not_74_out, not_75_out, not_76_out, not_77_out, not_78_out);
  and and_14 (and_14_out, not_79_out, e5, not_80_out, not_81_out, not_82_out, not_83_out, not_84_out);
  and and_15 (and_15_out, e6, not_85_out, not_86_out, not_87_out, not_88_out, not_89_out, not_90_out);
  and and_16 (and_16_out, not_91_out, not_92_out, not_93_out, e3, not_94_out, not_95_out, not_96_out);
  and and_17 (and_17_out, not_97_out, not_98_out, e4, not_99_out, not_100_out, not_101_out, not_102_out);
  and and_18 (and_18_out, not_103_out, e5, not_104_out, not_105_out, not_106_out, not_107_out, not_108_out);
  and and_19 (and_19_out, e6, not_109_out, not_110_out, not_111_out, not_112_out, not_113_out, not_114_out);
  and and_20 (and_20_out, not_115_out, not_116_out, not_117_out, not_118_out, e2, not_119_out, not_120_out);
  and and_21 (and_21_out, not_121_out, not_122_out, not_123_out, e3, not_124_out, not_125_out, not_126_out);
  and and_22 (and_22_out, e6, not_127_out, not_128_out, not_129_out, not_130_out, not_131_out, not_132_out);
  or or_1 (s2, and_14_out, and_15_out);
  or or_2 (s1, and_16_out, and_17_out, and_18_out, and_19_out);
  or or_3 (s0, and_20_out, and_21_out, and_22_out);
  or or_4 (s4, and_1_out, and_2_out, and_3_out, and_4_out, and_5_out, and_6_out);
  or or_5 (s3, and_7_out, and_8_out, and_9_out, and_10_out, and_11_out, and_12_out, and_13_out);

  assign s5 = 1'b0;
endmodule

module Conversor3 (
  input  e6,
  input  e5,
  input  e4,
  input  e3,
  input  e2,
  input  e1,
  input  e0,
  output s5,
  output s4,
  output s3,
  output s2,
  output s1,
  output s0
);

  wire and_1_out, and_2_out, and_3_out, and_4_out, and_5_out, and_6_out, and_7_out, and_8_out, and_9_out,
       and_10_out, and_11_out, and_12_out, and_13_out, and_14_out, and_15_out, and_16_out, and_17_out,
       and_18_out, and_19_out, and_20_out, and_21_out, not_1_out, not_2_out, not_3_out, not_4_out, not_5_out,
       not_6_out, not_7_out, not_8_out, not_9_out, not_10_out, not_11_out, not_12_out, not_13_out,
       not_14_out, not_15_out, not_16_out, not_17_out, not_18_out, not_19_out, not_20_out, not_21_out,
       not_22_out, not_23_out, not_24_out, not_25_out, not_26_out, not_27_out, not_28_out, not_29_out,
       not_30_out, not_31_out, not_32_out, not_33_out, not_34_out, not_35_out, not_36_out, not_37_out,
       not_38_out, not_39_out, not_40_out, not_41_out, not_42_out, not_43_out, not_44_out, not_45_out,
       not_46_out, not_47_out, not_48_out, not_49_out, not_50_out, not_51_out, not_52_out, not_53_out,
       not_54_out, not_55_out, not_56_out, not_57_out, not_58_out, not_59_out, not_60_out, not_61_out,
       not_62_out, not_63_out, not_64_out, not_65_out, not_66_out, not_67_out, not_68_out, not_69_out,
       not_70_out, not_71_out, not_72_out, not_73_out, not_74_out, not_75_out, not_76_out, not_77_out,
       not_78_out, not_79_out, not_80_out, not_81_out, not_82_out, not_83_out, not_84_out, not_85_out,
       not_86_out, not_87_out, not_88_out, not_89_out, not_90_out, not_91_out, not_92_out, not_93_out,
       not_94_out, not_95_out, not_96_out, not_97_out, not_98_out, not_99_out, not_100_out, not_101_out,
       not_102_out, not_103_out, not_104_out, not_105_out, not_106_out, not_107_out, not_108_out,
       not_109_out, not_110_out, not_111_out, not_112_out, not_113_out, not_114_out, not_115_out,
       not_116_out, not_117_out, not_118_out, not_119_out, not_120_out, not_121_out, not_122_out,
       not_123_out, not_124_out, not_125_out, not_126_out;

  not not_1 (not_1_out, e6);
  not not_2 (not_2_out, e5);
  not not_3 (not_3_out, e4);
  not not_4 (not_4_out, e3);
  not not_5 (not_5_out, e2);
  not not_6 (not_6_out, e1);
  not not_7 (not_7_out, e6);
  not not_8 (not_8_out, e5);
  not not_9 (not_9_out, e4);
  not not_10 (not_10_out, e3);
  not not_11 (not_11_out, e2);
  not not_12 (not_12_out, e0);
  not not_13 (not_13_out, e6);
  not not_14 (not_14_out, e5);
  not not_15 (not_15_out, e4);
  not not_16 (not_16_out, e3);
  not not_17 (not_17_out, e1);
  not not_18 (not_18_out, e0);
  not not_19 (not_19_out, e6);
  not not_20 (not_20_out, e5);
  not not_21 (not_21_out, e4);
  not not_22 (not_22_out, e2);
  not not_23 (not_23_out, e1);
  not not_24 (not_24_out, e0);
  not not_25 (not_25_out, e6);
  not not_26 (not_26_out, e5);
  not not_27 (not_27_out, e3);
  not not_28 (not_28_out, e2);
  not not_29 (not_29_out, e1);
  not not_30 (not_30_out, e0);
  not not_31 (not_31_out, e6);
  not not_32 (not_32_out, e4);
  not not_33 (not_33_out, e3);
  not not_34 (not_34_out, e2);
  not not_35 (not_35_out, e1);
  not not_36 (not_36_out, e0);
  not not_37 (not_37_out, e5);
  not not_38 (not_38_out, e4);
  not not_39 (not_39_out, e3);
  not not_40 (not_40_out, e2);
  not not_41 (not_41_out, e1);
  not not_42 (not_42_out, e0);
  not not_43 (not_43_out, e6);
  not not_44 (not_44_out, e5);
  not not_45 (not_45_out, e4);
  not not_46 (not_46_out, e3);
  not not_47 (not_47_out, e2);
  not not_48 (not_48_out, e1);
  not not_49 (not_49_out, e6);
  not not_50 (not_50_out, e5);
  not not_51 (not_51_out, e4);
  not not_52 (not_52_out, e3);
  not not_53 (not_53_out, e2);
  not not_54 (not_54_out, e0);
  not not_55 (not_55_out, e6);
  not not_56 (not_56_out, e5);
  not not_57 (not_57_out, e4);
  not not_58 (not_58_out, e3);
  not not_59 (not_59_out, e2);
  not not_60 (not_60_out, e1);
  not not_61 (not_61_out, e6);
  not not_62 (not_62_out, e5);
  not not_63 (not_63_out, e4);
  not not_64 (not_64_out, e3);
  not not_65 (not_65_out, e2);
  not not_66 (not_66_out, e0);
  not not_67 (not_67_out, e6);
  not not_68 (not_68_out, e5);
  not not_69 (not_69_out, e4);
  not not_70 (not_70_out, e3);
  not not_71 (not_71_out, e1);
  not not_72 (not_72_out, e0);
  not not_73 (not_73_out, e6);
  not not_74 (not_74_out, e5);
  not not_75 (not_75_out, e4);
  not not_76 (not_76_out, e2);
  not not_77 (not_77_out, e1);
  not not_78 (not_78_out, e0);
  not not_79 (not_79_out, e6);
  not not_80 (not_80_out, e5);
  not not_81 (not_81_out, e3);
  not not_82 (not_82_out, e2);
  not not_83 (not_83_out, e1);
  not not_84 (not_84_out, e0);
  not not_85 (not_85_out, e6);
  not not_86 (not_86_out, e4);
  not not_87 (not_87_out, e3);
  not not_88 (not_88_out, e2);
  not not_89 (not_89_out, e1);
  not not_90 (not_90_out, e0);
  not not_91 (not_91_out, e6);
  not not_92 (not_92_out, e5);
  not not_93 (not_93_out, e3);
  not not_94 (not_94_out, e2);
  not not_95 (not_95_out, e1);
  not not_96 (not_96_out, e0);
  not not_97 (not_97_out, e6);
  not not_98 (not_98_out, e4);
  not not_99 (not_99_out, e3);
  not not_100 (not_100_out, e2);
  not not_101 (not_101_out, e1);
  not not_102 (not_102_out, e0);
  not not_103 (not_103_out, e5);
  not not_104 (not_104_out, e4);
  not not_105 (not_105_out, e3);
  not not_106 (not_106_out, e2);
  not not_107 (not_107_out, e1);
  not not_108 (not_108_out, e0);
  not not_109 (not_109_out, e6);
  not not_110 (not_110_out, e5);
  not not_111 (not_111_out, e4);
  not not_112 (not_112_out, e3);
  not not_113 (not_113_out, e2);
  not not_114 (not_114_out, e1);
  not not_115 (not_115_out, e6);
  not not_116 (not_116_out, e5);
  not not_117 (not_117_out, e4);
  not not_118 (not_118_out, e2);
  not not_119 (not_119_out, e1);
  not not_120 (not_120_out, e0);
  not not_121 (not_121_out, e6);
  not not_122 (not_122_out, e5);
  not not_123 (not_123_out, e3);
  not not_124 (not_124_out, e2);
  not not_125 (not_125_out, e1);
  not not_126 (not_126_out, e0);
  and and_1 (and_1_out, not_1_out, not_2_out, not_3_out, not_4_out, not_5_out, not_6_out, e0);
  and and_2 (and_2_out, not_7_out, not_8_out, not_9_out, not_10_out, not_11_out, e1, not_12_out);
  and and_3 (and_3_out, not_13_out, not_14_out, not_15_out, not_16_out, e2, not_17_out, not_18_out);
  and and_4 (and_4_out, not_19_out, not_20_out, not_21_out, e3, not_22_out, not_23_out, not_24_out);
  and and_5 (and_5_out, not_25_out, not_26_out, e4, not_27_out, not_28_out, not_29_out, not_30_out);
  and and_6 (and_6_out, not_31_out, e5, not_32_out, not_33_out, not_34_out, not_35_out, not_36_out);
  and and_7 (and_7_out, e6, not_37_out, not_38_out, not_39_out, not_40_out, not_41_out, not_42_out);
  and and_8 (and_8_out, not_43_out, not_44_out, not_45_out, not_46_out, not_47_out, not_48_out, e0);
  and and_9 (and_9_out, not_49_out, not_50_out, not_51_out, not_52_out, not_53_out, e1, not_54_out);
  and and_10 (and_10_out, not_55_out, not_56_out, not_57_out, not_58_out, not_59_out, not_60_out, e0);
  and and_11 (and_11_out, not_61_out, not_62_out, not_63_out, not_64_out, not_65_out, e1, not_66_out);
  and and_12 (and_12_out, not_67_out, not_68_out, not_69_out, not_70_out, e2, not_71_out, not_72_out);
  and and_13 (and_13_out, not_73_out, not_74_out, not_75_out, e3, not_76_out, not_77_out, not_78_out);
  and and_14 (and_14_out, not_79_out, not_80_out, e4, not_81_out, not_82_out, not_83_out, not_84_out);
  and and_15 (and_15_out, not_85_out, e5, not_86_out, not_87_out, not_88_out, not_89_out, not_90_out);
  and and_16 (and_16_out, not_91_out, not_92_out, e4, not_93_out, not_94_out, not_95_out, not_96_out);
  and and_17 (and_17_out, not_97_out, e5, not_98_out, not_99_out, not_100_out, not_101_out, not_102_out);
  and and_18 (and_18_out, e6, not_103_out, not_104_out, not_105_out, not_106_out, not_107_out, not_108_out);
  and and_19 (and_19_out, not_109_out, not_110_out, not_111_out, not_112_out, not_113_out, not_114_out, e0);
  and and_20 (and_20_out, not_115_out, not_116_out, not_117_out, e3, not_118_out, not_119_out, not_120_out);
  and and_21 (and_21_out, not_121_out, not_122_out, e4, not_123_out, not_124_out, not_125_out, not_126_out);
  or or_1 (s3, and_8_out, and_9_out);
  or or_2 (s1, and_16_out, and_17_out, and_18_out);
  or or_3 (s0, and_19_out, and_20_out, and_21_out);
  or or_4 (s4, and_1_out, and_2_out, and_3_out, and_4_out, and_5_out, and_6_out, and_7_out);
  or or_5 (s2, and_10_out, and_11_out, and_12_out, and_13_out, and_14_out, and_15_out);

  assign s5 = 1'b0;
endmodule

module Conversor4 (
  input  e6,
  input  e5,
  input  e4,
  input  e3,
  input  e2,
  input  e1,
  input  e0,
  output s5,
  output s4,
  output s3,
  output s2,
  output s1,
  output s0
);

  wire and_1_out, and_2_out, and_3_out, and_4_out, and_5_out, and_6_out, and_7_out, and_8_out, and_9_out,
       and_10_out, and_11_out, and_12_out, and_13_out, and_14_out, and_15_out, and_16_out, and_17_out,
       and_18_out, not_1_out, not_2_out, not_3_out, not_4_out, not_5_out, not_6_out, not_7_out, not_8_out,
       not_9_out, not_10_out, not_11_out, not_12_out, not_13_out, not_14_out, not_15_out, not_16_out,
       not_17_out, not_18_out, not_19_out, not_20_out, not_21_out, not_22_out, not_23_out, not_24_out,
       not_25_out, not_26_out, not_27_out, not_28_out, not_29_out, not_30_out, not_31_out, not_32_out,
       not_33_out, not_34_out, not_35_out, not_36_out, not_37_out, not_38_out, not_39_out, not_40_out,
       not_41_out, not_42_out, not_43_out, not_44_out, not_45_out, not_46_out, not_47_out, not_48_out,
       not_49_out, not_50_out, not_51_out, not_52_out, not_53_out, not_54_out, not_55_out, not_56_out,
       not_57_out, not_58_out, not_59_out, not_60_out, not_61_out, not_62_out, not_63_out, not_64_out,
       not_65_out, not_66_out, not_67_out, not_68_out, not_69_out, not_70_out, not_71_out, not_72_out,
       not_73_out, not_74_out, not_75_out, not_76_out, not_77_out, not_78_out, not_79_out, not_80_out,
       not_81_out, not_82_out, not_83_out, not_84_out, not_85_out, not_86_out, not_87_out, not_88_out,
       not_89_out, not_90_out, not_91_out, not_92_out, not_93_out, not_94_out, not_95_out, not_96_out,
       not_97_out, not_98_out, not_99_out, not_100_out, not_101_out, not_102_out, not_103_out, not_104_out,
       not_105_out, not_106_out, not_107_out, not_108_out;

  not not_1 (not_1_out, e6);
  not not_2 (not_2_out, e5);
  not not_3 (not_3_out, e4);
  not not_4 (not_4_out, e2);
  not not_5 (not_5_out, e1);
  not not_6 (not_6_out, e0);
  not not_7 (not_7_out, e6);
  not not_8 (not_8_out, e5);
  not not_9 (not_9_out, e3);
  not not_10 (not_10_out, e2);
  not not_11 (not_11_out, e1);
  not not_12 (not_12_out, e0);
  not not_13 (not_13_out, e6);
  not not_14 (not_14_out, e4);
  not not_15 (not_15_out, e3);
  not not_16 (not_16_out, e2);
  not not_17 (not_17_out, e1);
  not not_18 (not_18_out, e0);
  not not_19 (not_19_out, e5);
  not not_20 (not_20_out, e4);
  not not_21 (not_21_out, e3);
  not not_22 (not_22_out, e2);
  not not_23 (not_23_out, e1);
  not not_24 (not_24_out, e0);
  not not_25 (not_25_out, e6);
  not not_26 (not_26_out, e5);
  not not_27 (not_27_out, e4);
  not not_28 (not_28_out, e3);
  not not_29 (not_29_out, e2);
  not not_30 (not_30_out, e1);
  not not_31 (not_31_out, e6);
  not not_32 (not_32_out, e5);
  not not_33 (not_33_out, e4);
  not not_34 (not_34_out, e3);
  not not_35 (not_35_out, e2);
  not not_36 (not_36_out, e0);
  not not_37 (not_37_out, e6);
  not not_38 (not_38_out, e5);
  not not_39 (not_39_out, e4);
  not not_40 (not_40_out, e3);
  not not_41 (not_41_out, e1);
  not not_42 (not_42_out, e0);
  not not_43 (not_43_out, e6);
  not not_44 (not_44_out, e5);
  not not_45 (not_45_out, e4);
  not not_46 (not_46_out, e2);
  not not_47 (not_47_out, e1);
  not not_48 (not_48_out, e0);
  not not_49 (not_49_out, e6);
  not not_50 (not_50_out, e5);
  not not_51 (not_51_out, e3);
  not not_52 (not_52_out, e2);
  not not_53 (not_53_out, e1);
  not not_54 (not_54_out, e0);
  not not_55 (not_55_out, e6);
  not not_56 (not_56_out, e4);
  not not_57 (not_57_out, e3);
  not not_58 (not_58_out, e2);
  not not_59 (not_59_out, e1);
  not not_60 (not_60_out, e0);
  not not_61 (not_61_out, e5);
  not not_62 (not_62_out, e4);
  not not_63 (not_63_out, e3);
  not not_64 (not_64_out, e2);
  not not_65 (not_65_out, e1);
  not not_66 (not_66_out, e0);
  not not_67 (not_67_out, e6);
  not not_68 (not_68_out, e5);
  not not_69 (not_69_out, e4);
  not not_70 (not_70_out, e3);
  not not_71 (not_71_out, e2);
  not not_72 (not_72_out, e1);
  not not_73 (not_73_out, e6);
  not not_74 (not_74_out, e4);
  not not_75 (not_75_out, e3);
  not not_76 (not_76_out, e2);
  not not_77 (not_77_out, e1);
  not not_78 (not_78_out, e0);
  not not_79 (not_79_out, e5);
  not not_80 (not_80_out, e4);
  not not_81 (not_81_out, e3);
  not not_82 (not_82_out, e2);
  not not_83 (not_83_out, e1);
  not not_84 (not_84_out, e0);
  not not_85 (not_85_out, e6);
  not not_86 (not_86_out, e5);
  not not_87 (not_87_out, e4);
  not not_88 (not_88_out, e3);
  not not_89 (not_89_out, e2);
  not not_90 (not_90_out, e1);
  not not_91 (not_91_out, e6);
  not not_92 (not_92_out, e5);
  not not_93 (not_93_out, e4);
  not not_94 (not_94_out, e3);
  not not_95 (not_95_out, e2);
  not not_96 (not_96_out, e0);
  not not_97 (not_97_out, e6);
  not not_98 (not_98_out, e5);
  not not_99 (not_99_out, e3);
  not not_100 (not_100_out, e2);
  not not_101 (not_101_out, e1);
  not not_102 (not_102_out, e0);
  not not_103 (not_103_out, e6);
  not not_104 (not_104_out, e4);
  not not_105 (not_105_out, e3);
  not not_106 (not_106_out, e2);
  not not_107 (not_107_out, e1);
  not not_108 (not_108_out, e0);
  and and_1 (and_1_out, not_1_out, not_2_out, not_3_out, e3, not_4_out, not_5_out, not_6_out);
  and and_2 (and_2_out, not_7_out, not_8_out, e4, not_9_out, not_10_out, not_11_out, not_12_out);
  and and_3 (and_3_out, not_13_out, e5, not_14_out, not_15_out, not_16_out, not_17_out, not_18_out);
  and and_4 (and_4_out, e6, not_19_out, not_20_out, not_21_out, not_22_out, not_23_out, not_24_out);
  and and_5 (and_5_out, not_25_out, not_26_out, not_27_out, not_28_out, not_29_out, not_30_out, e0);
  and and_6 (and_6_out, not_31_out, not_32_out, not_33_out, not_34_out, not_35_out, e1, not_36_out);
  and and_7 (and_7_out, not_37_out, not_38_out, not_39_out, not_40_out, e2, not_41_out, not_42_out);
  and and_8 (and_8_out, not_43_out, not_44_out, not_45_out, e3, not_46_out, not_47_out, not_48_out);
  and and_9 (and_9_out, not_49_out, not_50_out, e4, not_51_out, not_52_out, not_53_out, not_54_out);
  and and_10 (and_10_out, not_55_out, e5, not_56_out, not_57_out, not_58_out, not_59_out, not_60_out);
  and and_11 (and_11_out, e6, not_61_out, not_62_out, not_63_out, not_64_out, not_65_out, not_66_out);
  and and_12 (and_12_out, not_67_out, not_68_out, not_69_out, not_70_out, not_71_out, not_72_out, e0);
  and and_13 (and_13_out, not_73_out, e5, not_74_out, not_75_out, not_76_out, not_77_out, not_78_out);
  and and_14 (and_14_out, e6, not_79_out, not_80_out, not_81_out, not_82_out, not_83_out, not_84_out);
  and and_15 (and_15_out, not_85_out, not_86_out, not_87_out, not_88_out, not_89_out, not_90_out, e0);
  and and_16 (and_16_out, not_91_out, not_92_out, not_93_out, not_94_out, not_95_out, e1, not_96_out);
  and and_17 (and_17_out, not_97_out, not_98_out, e4, not_99_out, not_100_out, not_101_out, not_102_out);
  and and_18 (and_18_out, not_103_out, e5, not_104_out, not_105_out, not_106_out, not_107_out, not_108_out);
  or or_1 (s5, and_1_out, and_2_out, and_3_out, and_4_out);
  or or_2 (s1, and_12_out, and_13_out, and_14_out);
  or or_3 (s0, and_15_out, and_16_out, and_17_out, and_18_out);
  or or_4 (s4, and_5_out, and_6_out, and_7_out, and_8_out, and_9_out, and_10_out, and_11_out);

  assign s2 = 1'b0;
  assign s3 = 1'b0;
endmodule

module Conversor5 (
  input  e2,
  input  e1,
  input  e0,
  output s5,
  output s4,
  output s3,
  output s2,
  output s1,
  output s0
);

  wire and_1_out, and_2_out, and_3_out, and_4_out, and_5_out, and_6_out, and_7_out, and_8_out, and_9_out,
       and_10_out, and_11_out, and_12_out, and_13_out, not_1_out, not_2_out, not_3_out, not_4_out, not_5_out,
       not_6_out, not_7_out, not_8_out, not_9_out, not_10_out, not_11_out, not_12_out, not_13_out,
       not_14_out, not_15_out, not_16_out, not_17_out, not_18_out, not_19_out, not_20_out, not_21_out,
       not_22_out, not_23_out, not_24_out, not_25_out, not_26_out;

  not not_1 (not_1_out, e2);
  not not_2 (not_2_out, e1);
  not not_3 (not_3_out, e2);
  not not_4 (not_4_out, e0);
  not not_5 (not_5_out, e1);
  not not_6 (not_6_out, e0);
  not not_7 (not_7_out, e2);
  not not_8 (not_8_out, e1);
  not not_9 (not_9_out, e2);
  not not_10 (not_10_out, e0);
  not not_11 (not_11_out, e1);
  not not_12 (not_12_out, e0);
  not not_13 (not_13_out, e2);
  not not_14 (not_14_out, e1);
  not not_15 (not_15_out, e2);
  not not_16 (not_16_out, e0);
  not not_17 (not_17_out, e1);
  not not_18 (not_18_out, e0);
  not not_19 (not_19_out, e2);
  not not_20 (not_20_out, e1);
  not not_21 (not_21_out, e2);
  not not_22 (not_22_out, e0);
  not not_23 (not_23_out, e2);
  not not_24 (not_24_out, e0);
  not not_25 (not_25_out, e1);
  not not_26 (not_26_out, e0);
  and and_1 (and_1_out, not_1_out, not_2_out, e0);
  and and_2 (and_2_out, not_3_out, e1, not_4_out);
  and and_3 (and_3_out, e2, not_5_out, not_6_out);
  and and_4 (and_4_out, not_7_out, not_8_out, e0);
  and and_5 (and_5_out, not_9_out, e1, not_10_out);
  and and_6 (and_6_out, e2, not_11_out, not_12_out);
  and and_7 (and_7_out, not_13_out, not_14_out, e0);
  and and_8 (and_8_out, not_15_out, e1, not_16_out);
  and and_9 (and_9_out, e2, not_17_out, not_18_out);
  and and_10 (and_10_out, not_19_out, not_20_out, e0);
  and and_11 (and_11_out, not_21_out, e1, not_22_out);
  and and_12 (and_12_out, not_23_out, e1, not_24_out);
  and and_13 (and_13_out, e2, not_25_out, not_26_out);
  or or_1 (s5, and_1_out, and_2_out, and_3_out);
  or or_2 (s4, and_4_out, and_5_out, and_6_out);
  or or_3 (s2, and_7_out, and_8_out, and_9_out);
  or or_4 (s1, and_10_out, and_11_out);
  or or_5 (s0, and_12_out, and_13_out);

  assign s3 = 1'b0;
endmodule

module GrayToBin (
  input  a,
  input  b,
  input  c,
  input  d,
  input  e,
  input  f,
  output A_2,
  output B_2,
  output C_2,
  output D_2,
  output E_2,
  output F_2
);

  wire and_2_out, and_3_out, and_4_out, and_5_out, and_6_out, and_7_out, and_8_out, and_9_out, and_10_out,
       and_11_out, and_12_out, and_13_out, and_14_out, and_15_out, and_16_out, and_17_out, and_18_out,
       and_19_out, and_20_out, and_21_out, and_22_out, and_23_out, and_24_out, and_25_out, and_26_out,
       and_27_out, and_28_out, and_29_out, and_30_out, and_31_out, and_32_out, and_33_out, and_34_out,
       and_35_out, and_36_out, and_37_out, not_1_out, not_2_out, not_3_out, not_4_out, not_5_out, not_6_out,
       not_7_out, not_8_out, not_9_out, not_10_out, not_11_out, not_12_out, not_13_out, not_14_out,
       not_15_out, not_16_out, not_17_out, not_18_out, not_19_out, not_20_out, not_21_out, not_22_out,
       not_23_out, not_24_out, not_25_out, not_26_out, not_27_out, not_28_out, not_29_out, not_30_out,
       not_31_out, not_32_out, not_33_out, not_34_out, not_35_out, not_36_out, not_37_out, not_38_out,
       not_39_out, not_40_out, not_41_out, not_42_out, not_43_out, not_44_out, not_45_out, not_46_out,
       not_47_out, not_48_out, not_49_out, not_50_out, not_51_out, not_52_out, not_53_out, not_54_out,
       not_55_out, not_56_out, not_57_out, not_58_out, not_59_out, not_60_out, not_61_out, not_62_out,
       not_63_out, not_64_out, not_65_out, not_66_out, not_67_out, not_68_out, not_69_out, not_70_out,
       not_71_out, not_72_out, not_73_out, not_74_out, not_75_out, not_76_out, not_77_out, not_78_out,
       not_79_out;

  not not_1 (not_1_out, a);
  not not_2 (not_2_out, b);
  not not_3 (not_3_out, a);
  not not_4 (not_4_out, c);
  not not_5 (not_5_out, b);
  not not_6 (not_6_out, c);
  not not_7 (not_7_out, b);
  not not_8 (not_8_out, d);
  not not_9 (not_9_out, a);
  not not_10 (not_10_out, c);
  not not_11 (not_11_out, d);
  not not_12 (not_12_out, b);
  not not_13 (not_13_out, c);
  not not_14 (not_14_out, d);
  not not_15 (not_15_out, b);
  not not_16 (not_16_out, c);
  not not_17 (not_17_out, e);
  not not_18 (not_18_out, b);
  not not_19 (not_19_out, d);
  not not_20 (not_20_out, e);
  not not_21 (not_21_out, b);
  not not_22 (not_22_out, a);
  not not_23 (not_23_out, c);
  not not_24 (not_24_out, d);
  not not_25 (not_25_out, e);
  not not_26 (not_26_out, a);
  not not_27 (not_27_out, c);
  not not_28 (not_28_out, d);
  not not_29 (not_29_out, e);
  not not_30 (not_30_out, d);
  not not_31 (not_31_out, e);
  not not_32 (not_32_out, b);
  not not_33 (not_33_out, c);
  not not_34 (not_34_out, d);
  not not_35 (not_35_out, e);
  not not_36 (not_36_out, b);
  not not_37 (not_37_out, c);
  not not_38 (not_38_out, d);
  not not_39 (not_39_out, f);
  not not_40 (not_40_out, b);
  not not_41 (not_41_out, c);
  not not_42 (not_42_out, e);
  not not_43 (not_43_out, f);
  not not_44 (not_44_out, b);
  not not_45 (not_45_out, c);
  not not_46 (not_46_out, b);
  not not_47 (not_47_out, d);
  not not_48 (not_48_out, e);
  not not_49 (not_49_out, f);
  not not_50 (not_50_out, b);
  not not_51 (not_51_out, d);
  not not_52 (not_52_out, b);
  not not_53 (not_53_out, e);
  not not_54 (not_54_out, b);
  not not_55 (not_55_out, f);
  not not_56 (not_56_out, a);
  not not_57 (not_57_out, c);
  not not_58 (not_58_out, d);
  not not_59 (not_59_out, e);
  not not_60 (not_60_out, f);
  not not_61 (not_61_out, a);
  not not_62 (not_62_out, c);
  not not_63 (not_63_out, d);
  not not_64 (not_64_out, a);
  not not_65 (not_65_out, c);
  not not_66 (not_66_out, e);
  not not_67 (not_67_out, a);
  not not_68 (not_68_out, c);
  not not_69 (not_69_out, f);
  not not_70 (not_70_out, d);
  not not_71 (not_71_out, e);
  not not_72 (not_72_out, d);
  not not_73 (not_73_out, f);
  not not_74 (not_74_out, e);
  not not_75 (not_75_out, f);
  not not_76 (not_76_out, d);
  not not_77 (not_77_out, e);
  not not_78 (not_78_out, d);
  not not_79 (not_79_out, f);
  and and_1 (B_2, not_1_out, b);
  and and_2 (and_2_out, not_2_out, c);
  and and_3 (and_3_out, not_3_out, b, not_4_out);
  and and_4 (and_4_out, not_5_out, not_6_out, d);
  and and_5 (and_5_out, not_7_out, c, not_8_out);
  and and_6 (and_6_out, not_9_out, b, not_10_out, not_11_out);
  and and_7 (and_7_out, b, c, d);
  and and_8 (and_8_out, a, d);
  and and_9 (and_9_out, not_12_out, not_13_out, not_14_out, e);
  and and_10 (and_10_out, not_15_out, not_16_out, d, not_17_out);
  and and_11 (and_11_out, not_18_out, c, not_19_out, not_20_out);
  and and_12 (and_12_out, not_21_out, c, d, e);
  and and_13 (and_13_out, not_22_out, b, not_23_out, not_24_out, not_25_out);
  and and_14 (and_14_out, not_26_out, b, not_27_out, d, e);
  and and_15 (and_15_out, b, c, not_28_out, e);
  and and_16 (and_16_out, b, c, d, not_29_out);
  and and_17 (and_17_out, a, not_30_out, e);
  and and_18 (and_18_out, a, d, not_31_out);
  and and_19 (and_19_out, not_32_out, not_33_out, not_34_out, not_35_out, f);
  and and_20 (and_20_out, not_36_out, not_37_out, not_38_out, e, not_39_out);
  and and_21 (and_21_out, not_40_out, not_41_out, d, not_42_out, not_43_out);
  and and_22 (and_22_out, not_44_out, not_45_out, d, e, f);
  and and_23 (and_23_out, not_46_out, c, not_47_out, not_48_out, not_49_out);
  and and_24 (and_24_out, not_50_out, c, not_51_out, e, f);
  and and_25 (and_25_out, not_52_out, c, d, not_53_out, f);
  and and_26 (and_26_out, not_54_out, c, d, e, not_55_out);
  and and_27 (and_27_out, not_56_out, b, not_57_out, not_58_out, not_59_out, not_60_out);
  and and_28 (and_28_out, not_61_out, b, not_62_out, not_63_out, e, f);
  and and_29 (and_29_out, not_64_out, b, not_65_out, d, not_66_out, f);
  and and_30 (and_30_out, not_67_out, b, not_68_out, d, e, not_69_out);
  and and_31 (and_31_out, b, c, not_70_out, not_71_out, f);
  and and_32 (and_32_out, b, c, not_72_out, e, not_73_out);
  and and_33 (and_33_out, b, c, d, not_74_out, not_75_out);
  and and_34 (and_34_out, b, c, d, e, f);
  and and_35 (and_35_out, a, not_76_out, not_77_out, f);
  and and_36 (and_36_out, a, not_78_out, e, not_79_out);
  and and_37 (and_37_out, a, d, e, f);
  or or_1 (C_2, and_2_out, and_3_out);
  or or_2 (D_2, and_4_out, and_5_out, and_6_out, and_7_out, and_8_out);
  or or_3 (E_2, and_9_out, and_10_out, and_11_out, and_12_out, and_13_out, and_14_out, and_15_out, and_16_out, and_17_out, and_18_out);
  or or_4 (F_2, and_19_out, and_20_out, and_21_out, and_22_out, and_23_out, and_24_out, and_25_out, and_26_out, and_27_out, and_28_out, and_29_out, and_30_out, and_31_out, and_32_out, and_33_out, and_34_out, and_35_out, and_36_out, and_37_out);

  assign A_2 = a;
endmodule

module Circuito (
  input  [5:0] Sensor,
  input  [5:0] Letra_1,
  input  [5:0] Letra_2,
  input  [5:0] Letra_3,
  input  [5:0] Letra_4,
  input  [5:0] Letra_5,
  input  [5:0] Letra_6,
  input  [5:0] Letra_7,
  input  [5:0] Letra_8,
  input  [5:0] Letra_9,
  input  [5:0] Letra_10,
  input  [5:0] Letra_11,
  input  [5:0] Letra_12,
  input  [5:0] Letra_13,
  input  [5:0] Letra_14,
  input  [5:0] Letra_15,
  input  [5:0] Letra_16,
  input  [5:0] Letra_17,
  input  [5:0] Letra_18,
  input  [5:0] Letra_19,
  input  [5:0] Letra_20,
  output M1,
  output M2,
  output M3,
  output M4,
  output M5,
  output M6,
  output M7,
  output M8,
  output M9,
  output M10,
  output M11,
  output M12,
  output M13,
  output M14,
  output M15,
  output M16,
  output M17,
  output M18,
  output M19,
  output M20
);

  wire [5:0] \operações_1_saida , \operações_2_saida , \operações_3_saida , \operações_4_saida ,
       \operações_5_saida , \operações_6_saida , \operações_7_saida , \operações_8_saida ,
       \operações_9_saida , \operações_10_saida , \operações_11_saida , \operações_12_saida ,
       \operações_13_saida , \operações_14_saida , \operações_15_saida , \operações_16_saida ,
       \operações_17_saida , \operações_18_saida , \operações_19_saida , \operações_20_saida ;

  \Operações  \operações_1  (.Pos_Martelete(6'b000010), .Sensor(Sensor), .Saida(\operações_1_saida ));
  \Operações  \operações_2  (.Pos_Martelete(6'b000011), .Sensor(Sensor), .Saida(\operações_2_saida ));
  \Operações  \operações_3  (.Pos_Martelete(6'b000100), .Sensor(Sensor), .Saida(\operações_3_saida ));
  \Operações  \operações_4  (.Pos_Martelete(6'b000101), .Sensor(Sensor), .Saida(\operações_4_saida ));
  \Operações  \operações_5  (.Pos_Martelete(6'b000110), .Sensor(Sensor), .Saida(\operações_5_saida ));
  \Operações  \operações_6  (.Pos_Martelete(6'b000111), .Sensor(Sensor), .Saida(\operações_6_saida ));
  \Operações  \operações_7  (.Pos_Martelete(6'b001000), .Sensor(Sensor), .Saida(\operações_7_saida ));
  \Operações  \operações_8  (.Pos_Martelete(6'b001001), .Sensor(Sensor), .Saida(\operações_8_saida ));
  \Operações  \operações_9  (.Pos_Martelete(6'b001010), .Sensor(Sensor), .Saida(\operações_9_saida ));
  \Operações  \operações_10  (.Pos_Martelete(6'b001011), .Sensor(Sensor), .Saida(\operações_10_saida ));
  \Operações  \operações_11  (.Pos_Martelete(6'b001100), .Sensor(Sensor), .Saida(\operações_11_saida ));
  \Operações  \operações_12  (.Pos_Martelete(6'b001101), .Sensor(Sensor), .Saida(\operações_12_saida ));
  \Operações  \operações_13  (.Pos_Martelete(6'b001110), .Sensor(Sensor), .Saida(\operações_13_saida ));
  \Operações  \operações_14  (.Pos_Martelete(6'b001111), .Sensor(Sensor), .Saida(\operações_14_saida ));
  \Operações  \operações_15  (.Pos_Martelete(6'b010000), .Sensor(Sensor), .Saida(\operações_15_saida ));
  \Operações  \operações_16  (.Pos_Martelete(6'b010001), .Sensor(Sensor), .Saida(\operações_16_saida ));
  \Operações  \operações_17  (.Pos_Martelete(6'b010010), .Sensor(Sensor), .Saida(\operações_17_saida ));
  \Operações  \operações_18  (.Pos_Martelete(6'b010011), .Sensor(Sensor), .Saida(\operações_18_saida ));
  \Operações  \operações_19  (.Pos_Martelete(6'b010100), .Sensor(Sensor), .Saida(\operações_19_saida ));
  \Operações  \operações_20  (.Pos_Martelete(6'b000001), .Sensor(Sensor), .Saida(\operações_20_saida ));
  Comparador comparador_1 (.Letra1(\operações_15_saida ), .Letra2(Letra_16), .out_3(M16));
  Comparador comparador_2 (.Letra1(\operações_20_saida ), .Letra2(Letra_1), .out_3(M1));
  Comparador comparador_3 (.Letra1(\operações_1_saida ), .Letra2(Letra_2), .out_3(M2));
  Comparador comparador_4 (.Letra1(\operações_2_saida ), .Letra2(Letra_3), .out_3(M3));
  Comparador comparador_5 (.Letra1(\operações_3_saida ), .Letra2(Letra_4), .out_3(M4));
  Comparador comparador_6 (.Letra1(\operações_4_saida ), .Letra2(Letra_5), .out_3(M5));
  Comparador comparador_7 (.Letra1(\operações_5_saida ), .Letra2(Letra_6), .out_3(M6));
  Comparador comparador_8 (.Letra1(\operações_6_saida ), .Letra2(Letra_7), .out_3(M7));
  Comparador comparador_9 (.Letra1(\operações_7_saida ), .Letra2(Letra_8), .out_3(M8));
  Comparador comparador_10 (.Letra1(\operações_8_saida ), .Letra2(Letra_9), .out_3(M9));
  Comparador comparador_11 (.Letra1(\operações_9_saida ), .Letra2(Letra_10), .out_3(M10));
  Comparador comparador_12 (.Letra1(\operações_10_saida ), .Letra2(Letra_11), .out_3(M11));
  Comparador comparador_13 (.Letra1(\operações_11_saida ), .Letra2(Letra_12), .out_3(M12));
  Comparador comparador_14 (.Letra1(\operações_12_saida ), .Letra2(Letra_13), .out_3(M13));
  Comparador comparador_15 (.Letra1(\operações_13_saida ), .Letra2(Letra_14), .out_3(M14));
  Comparador comparador_16 (.Letra1(\operações_14_saida ), .Letra2(Letra_15), .out_3(M15));
  Comparador comparador_17 (.Letra1(\operações_16_saida ), .Letra2(Letra_17), .out_3(M17));
  Comparador comparador_18 (.Letra1(\operações_17_saida ), .Letra2(Letra_18), .out_3(M18));
  Comparador comparador_19 (.Letra1(\operações_18_saida ), .Letra2(Letra_19), .out_3(M19));
  Comparador comparador_20 (.Letra1(\operações_19_saida ), .Letra2(Letra_20), .out_3(M20));
endmodule

module Deslocador (
  input  E0,
  input  E1,
  input  E2,
  input  E3,
  input  E4,
  input  E5,
  output S0,
  output S1,
  output S2,
  output S3,
  output S4,
  output S5
);

  wire and_1_out, and_2_out, and_3_out, and_4_out, and_5_out, and_6_out, and_7_out, and_8_out, and_9_out,
       and_10_out, and_11_out, and_12_out, and_13_out, and_14_out, and_15_out, and_16_out, and_17_out,
       and_18_out, and_19_out, and_20_out, not_1_out, not_2_out, not_3_out, not_4_out, not_5_out, not_6_out,
       not_7_out, not_8_out, not_9_out, not_10_out, not_11_out, not_12_out, not_13_out, not_14_out,
       not_15_out, not_16_out, not_17_out, not_18_out, not_19_out, not_20_out, not_21_out, not_22_out,
       not_23_out, not_24_out, not_25_out, not_26_out, not_27_out, not_28_out, not_29_out, not_30_out,
       not_31_out;

  not not_1 (not_1_out, E1);
  not not_2 (not_2_out, E2);
  not not_3 (not_3_out, E3);
  not not_4 (not_4_out, E1);
  not not_5 (not_5_out, E2);
  not not_6 (not_6_out, E4);
  not not_7 (not_7_out, E1);
  not not_8 (not_8_out, E2);
  not not_9 (not_9_out, E5);
  not not_10 (not_10_out, E0);
  not not_11 (not_11_out, E0);
  not not_12 (not_12_out, E2);
  not not_13 (not_13_out, E3);
  not not_14 (not_14_out, E2);
  not not_15 (not_15_out, E4);
  not not_16 (not_16_out, E0);
  not not_17 (not_17_out, E1);
  not not_18 (not_18_out, E2);
  not not_19 (not_19_out, E5);
  not not_20 (not_20_out, E4);
  not not_21 (not_21_out, E3);
  not not_22 (not_22_out, E3);
  not not_23 (not_23_out, E0);
  not not_24 (not_24_out, E1);
  not not_25 (not_25_out, E2);
  not not_26 (not_26_out, E3);
  not not_27 (not_27_out, E1);
  not not_28 (not_28_out, E2);
  not not_29 (not_29_out, E5);
  not not_30 (not_30_out, E4);
  not not_31 (not_31_out, E4);
  and and_1 (and_1_out, E0, not_1_out, not_2_out, not_3_out);
  and and_2 (and_2_out, E0, not_4_out, not_5_out, not_6_out);
  and and_3 (and_3_out, E0, not_7_out, not_8_out, not_9_out);
  and and_4 (and_4_out, not_10_out, E1);
  and and_5 (and_5_out, E1, E3, E4);
  and and_6 (and_6_out, E1, E2);
  and and_7 (and_7_out, not_11_out, E2);
  and and_8 (and_8_out, E2, E3, E4);
  and and_9 (and_9_out, E0, E1, not_12_out, not_13_out);
  and and_10 (and_10_out, E0, E1, not_14_out, not_15_out);
  and and_11 (and_11_out, not_16_out, E3);
  and and_12 (and_12_out, not_17_out, not_18_out, E3, not_19_out);
  and and_13 (and_13_out, E3, not_20_out);
  and and_14 (and_14_out, E0, E2, not_21_out, E4);
  and and_15 (and_15_out, E0, E1, not_22_out, E4);
  and and_16 (and_16_out, not_23_out, E4);
  and and_17 (and_17_out, not_24_out, not_25_out, not_26_out, E4);
  and and_18 (and_18_out, not_27_out, not_28_out, E4, not_29_out);
  and and_19 (and_19_out, E0, E2, not_30_out);
  and and_20 (and_20_out, E0, E1, not_31_out);
  or or_1 (S0, and_1_out, and_2_out, and_3_out);
  or or_2 (S1, and_4_out, and_5_out, and_6_out);
  or or_3 (S2, and_7_out, and_8_out, and_9_out, and_10_out);
  or or_4 (S3, and_11_out, and_12_out, and_13_out, and_14_out, and_15_out);
  or or_5 (S4, and_16_out, and_17_out, and_18_out, and_19_out, and_20_out);

  assign S5 = E5;
endmodule

module Subtrator (
  input  A0,
  input  A1,
  input  A2,
  input  A3,
  input  A4,
  input  A5,
  input  B0,
  input  B1,
  input  B2,
  input  B3,
  input  B4,
  input  B5,
  output OUT0,
  output OUT1,
  output OUT2,
  output OUT3,
  output OUT4,
  output OUT5,
  output B_OUT
);

  wire and_1_out, and_2_out, and_3_out, and_4_out, and_5_out, and_6_out, and_7_out, and_8_out, and_9_out,
       and_10_out, and_11_out, and_12_out, or_1_out, or_2_out, or_3_out, or_4_out, or_5_out, xor_1_out,
       xor_2_out, xor_3_out, xor_4_out, xor_5_out, xor_6_out;

  and and_1 (and_1_out, ~B1, A1);  // AND_Gate
  and and_2 (and_2_out, ~B2, A2);  // AND_Gate
  and and_3 (and_3_out, ~B3, A3);  // AND_Gate
  and and_4 (and_4_out, ~B0, A0);  // AND_Gate
  xor xor_1 (xor_1_out, A1, B1);
  or or_1 (or_1_out, and_1_out, and_8_out);
  xor xor_2 (xor_2_out, A2, B2);
  or or_2 (or_2_out, and_2_out, and_9_out);
  xor xor_3 (xor_3_out, A3, B3);
  or or_3 (or_3_out, and_3_out, and_10_out);
  and and_5 (and_5_out, ~B4, A4);  // AND_Gate
  and and_6 (and_6_out, ~B5, A5);  // AND_Gate
  xor xor_4 (xor_4_out, A0, B0);
  and and_7 (and_7_out, ~xor_4_out, 1'b0);  // AND_Gate
  or or_4 (or_4_out, and_4_out, and_7_out);
  and and_8 (and_8_out, ~xor_1_out, or_4_out);  // AND_Gate
  and and_9 (and_9_out, ~xor_2_out, or_1_out);  // AND_Gate
  and and_10 (and_10_out, ~xor_3_out, or_2_out);  // AND_Gate
  xor xor_5 (xor_5_out, A4, B4);
  and and_11 (and_11_out, ~xor_5_out, or_3_out);  // AND_Gate
  or or_5 (or_5_out, and_5_out, and_11_out);
  xor xor_6 (xor_6_out, A5, B5);
  or or_6 (B_OUT, and_6_out, and_12_out);
  xor xor_7 (OUT0, 1'b0, xor_4_out);
  xor xor_8 (OUT1, or_4_out, xor_1_out);
  xor xor_9 (OUT2, or_1_out, xor_2_out);
  xor xor_10 (OUT3, or_2_out, xor_3_out);
  xor xor_11 (OUT4, or_3_out, xor_5_out);
  and and_12 (and_12_out, ~xor_6_out, or_5_out);  // AND_Gate
  xor xor_12 (OUT5, or_5_out, xor_6_out);
endmodule

module \Operações  (
  input  [5:0] Pos_Martelete,
  input  [5:0] Sensor,
  output [5:0] Saida
);

  wire [5:0] somador_1_saida_0, subtrator_1_out0;

  Subtrator subtrator_1 (
    .A0(Sensor[0]), .A1(Sensor[1]), .A2(Sensor[2]), .A3(Sensor[3]), .A4(Sensor[4]), .A5(Sensor[5]),
    .B0(1'b0), .B1(1'b1), .B2(1'b1), .B3(1'b0), .B4(1'b0), .B5(1'b1), .OUT0(subtrator_1_out0[0]),
    .OUT1(subtrator_1_out0[1]), .OUT2(subtrator_1_out0[2]), .OUT3(subtrator_1_out0[3]),
    .OUT4(subtrator_1_out0[4]), .OUT5(subtrator_1_out0[5]));  // open: B_OUT
  Somador somador_1 (
    .A0(subtrator_1_out0[0]), .A1(subtrator_1_out0[1]), .A2(subtrator_1_out0[2]), .A3(subtrator_1_out0[3]),
    .A4(subtrator_1_out0[4]), .A5(subtrator_1_out0[5]), .B0(Pos_Martelete[0]), .B1(Pos_Martelete[1]),
    .B2(Pos_Martelete[2]), .B3(Pos_Martelete[3]), .B4(Pos_Martelete[4]), .B5(Pos_Martelete[5]),
    .SAIDA_0(somador_1_saida_0[0]), .SAIDA_1(somador_1_saida_0[1]), .SAIDA_2(somador_1_saida_0[2]),
    .SAIDA_3(somador_1_saida_0[3]), .SAIDA_4(somador_1_saida_0[4]), .SAIDA_5(somador_1_saida_0[5]));  // open: C
  Deslocador deslocador_1 (
    .E0(somador_1_saida_0[5]), .E1(somador_1_saida_0[4]), .E2(somador_1_saida_0[3]),
    .E3(somador_1_saida_0[2]), .E4(somador_1_saida_0[1]), .E5(somador_1_saida_0[0]), .S0(Saida[5]),
    .S1(Saida[4]), .S2(Saida[3]), .S3(Saida[2]), .S4(Saida[1]), .S5(Saida[0]));
endmodule

module display (
  input  [5:0] Num,
  output g1,
  output f1,
  output a1,
  output b1,
  output g2,
  output f2,
  output a2,
  output b2,
  output e2,
  output d2,
  output c2,
  output e1,
  output d1,
  output c1
);

  display2 display2_1 (
    .E5(Num[5]), .E4(Num[4]), .E3(Num[3]), .E2(Num[2]), .E1(Num[1]), .E0(Num[0]), .a(a2), .b(b2), .c(c2),
    .d(d2), .e(e2), .f(f2), .g(g2));
  display1 display1_1 (
    .E5(Num[5]), .E4(Num[4]), .E3(Num[3]), .E2(Num[2]), .E1(Num[1]), .E0(Num[0]), .a(a1), .b(b1), .c(c1),
    .d(d1), .e(e1), .f(f1), .g(g1));
  _7_Segment_Display u_7_segment_display_1 (.g(g2), .f(f2), .a(a2), .b(b2), .e(e2), .d(d2), .c(c2));  // open: dp
  _7_Segment_Display u_7_segment_display_2 (.g(g1), .f(f1), .a(a1), .b(b1), .e(e1), .d(d1), .c(c1));  // open: dp
endmodule

module display2 (
  input  E5,
  input  E4,
  input  E3,
  input  E2,
  input  E1,
  input  E0,
  output a,
  output b,
  output c,
  output d,
  output e,
  output f,
  output g
);

  wire and_1_out, and_2_out, and_3_out, and_4_out, and_5_out, and_6_out, and_7_out, and_8_out, and_9_out,
       and_10_out, and_11_out, and_12_out, and_13_out, and_14_out, and_15_out, and_16_out, and_17_out,
       and_18_out, and_19_out, and_20_out, and_21_out, and_22_out, and_23_out, and_24_out, and_25_out,
       and_26_out, and_27_out, and_28_out, and_29_out, and_30_out, and_31_out, and_32_out, and_33_out,
       and_34_out, and_35_out, and_36_out, and_37_out, and_38_out, and_39_out, and_40_out, and_41_out,
       and_42_out, and_43_out, and_44_out, and_45_out, and_46_out, and_47_out, and_48_out, not_1_out,
       not_2_out, not_3_out, not_4_out, not_5_out, not_6_out, not_7_out, not_8_out, not_9_out, not_10_out,
       not_11_out, not_12_out, not_13_out, not_14_out, not_15_out, not_16_out, not_17_out, not_18_out,
       not_19_out, not_20_out, not_21_out, not_22_out, not_23_out, not_24_out, not_25_out, not_26_out,
       not_27_out, not_28_out, not_29_out, not_30_out, not_31_out, not_32_out, not_33_out, not_34_out,
       not_35_out, not_36_out, not_37_out, not_38_out, not_39_out, not_40_out, not_41_out, not_42_out,
       not_43_out, not_44_out, not_45_out, not_46_out, not_47_out, not_48_out, not_49_out, not_50_out,
       not_51_out, not_52_out, not_53_out, not_54_out, not_55_out, not_56_out, not_57_out, not_58_out,
       not_59_out, not_60_out, not_61_out, not_62_out, not_63_out, not_64_out, not_65_out, not_66_out,
       not_67_out, not_68_out, not_69_out, not_70_out, not_71_out, not_72_out, not_73_out, not_74_out,
       not_75_out, not_76_out, not_77_out, not_78_out, not_79_out, not_80_out, not_81_out;

  not not_1 (not_1_out, E5);
  not not_2 (not_2_out, E4);
  not not_3 (not_3_out, E2);
  not not_4 (not_4_out, E1);
  not not_5 (not_5_out, E4);
  not not_6 (not_6_out, E3);
  not not_7 (not_7_out, E5);
  not not_8 (not_8_out, E3);
  not not_9 (not_9_out, E5);
  not not_10 (not_10_out, E2);
  not not_11 (not_11_out, E0);
  not not_12 (not_12_out, E4);
  not not_13 (not_13_out, E3);
  not not_14 (not_14_out, E1);
  not not_15 (not_15_out, E0);
  not not_16 (not_16_out, E5);
  not not_17 (not_17_out, E4);
  not not_18 (not_18_out, E5);
  not not_19 (not_19_out, E3);
  not not_20 (not_20_out, E2);
  not not_21 (not_21_out, E4);
  not not_22 (not_22_out, E3);
  not not_23 (not_23_out, E1);
  not not_24 (not_24_out, E5);
  not not_25 (not_25_out, E4);
  not not_26 (not_26_out, E2);
  not not_27 (not_27_out, E1);
  not not_28 (not_28_out, E4);
  not not_29 (not_29_out, E3);
  not not_30 (not_30_out, E5);
  not not_31 (not_31_out, E3);
  not not_32 (not_32_out, E5);
  not not_33 (not_33_out, E2);
  not not_34 (not_34_out, E0);
  not not_35 (not_35_out, E2);
  not not_36 (not_36_out, E0);
  not not_37 (not_37_out, E1);
  not not_38 (not_38_out, E5);
  not not_39 (not_39_out, E4);
  not not_40 (not_40_out, E3);
  not not_41 (not_41_out, E5);
  not not_42 (not_42_out, E4);
  not not_43 (not_43_out, E2);
  not not_44 (not_44_out, E1);
  not not_45 (not_45_out, E5);
  not not_46 (not_46_out, E3);
  not not_47 (not_47_out, E2);
  not not_48 (not_48_out, E1);
  not not_49 (not_49_out, E0);
  not not_50 (not_50_out, E5);
  not not_51 (not_51_out, E2);
  not not_52 (not_52_out, E5);
  not not_53 (not_53_out, E1);
  not not_54 (not_54_out, E0);
  not not_55 (not_55_out, E2);
  not not_56 (not_56_out, E0);
  not not_57 (not_57_out, E0);
  not not_58 (not_58_out, E5);
  not not_59 (not_59_out, E4);
  not not_60 (not_60_out, E3);
  not not_61 (not_61_out, E5);
  not not_62 (not_62_out, E4);
  not not_63 (not_63_out, E2);
  not not_64 (not_64_out, E1);
  not not_65 (not_65_out, E1);
  not not_66 (not_66_out, E0);
  not not_67 (not_67_out, E1);
  not not_68 (not_68_out, E0);
  not not_69 (not_69_out, E1);
  not not_70 (not_70_out, E0);
  not not_71 (not_71_out, E1);
  not not_72 (not_72_out, E0);
  not not_73 (not_73_out, E5);
  not not_74 (not_74_out, E5);
  not not_75 (not_75_out, E4);
  not not_76 (not_76_out, E3);
  not not_77 (not_77_out, E2);
  not not_78 (not_78_out, E1);
  not not_79 (not_79_out, E0);
  and and_1 (and_1_out, not_1_out, not_2_out, not_3_out, not_4_out);
  and and_2 (and_2_out, not_5_out, not_6_out);
  and and_3 (and_3_out, not_7_out, not_8_out, E2);
  and and_4 (and_4_out, not_9_out, E4, E3);
  and and_5 (and_5_out, E5, not_10_out, not_11_out);
  and and_6 (and_6_out, E5, E1);
  and and_7 (and_7_out, E5, E2, E0);
  not not_80 (not_80_out, E5);
  and and_8 (and_8_out, not_12_out, not_13_out);
  not not_81 (not_81_out, E2);
  and and_9 (and_9_out, not_14_out, not_15_out);
  and and_10 (and_10_out, E1, E0);
  and and_11 (and_11_out, not_16_out, not_17_out);
  and and_12 (and_12_out, not_18_out, not_19_out, not_20_out);
  and and_13 (and_13_out, not_21_out, not_22_out);
  and and_14 (and_14_out, E3, E2, E1);
  and and_15 (and_15_out, E5, not_23_out);
  and and_16 (and_16_out, E5, E0);
  and and_17 (and_17_out, E5, E2);
  and and_18 (and_18_out, not_24_out, not_25_out, not_26_out, not_27_out);
  and and_19 (and_19_out, not_28_out, not_29_out);
  and and_20 (and_20_out, not_30_out, not_31_out, E2);
  and and_21 (and_21_out, not_32_out, E4, E3);
  and and_22 (and_22_out, E5, not_33_out, not_34_out);
  and and_23 (and_23_out, E5, not_35_out, E1);
  and and_24 (and_24_out, E5, E1, not_36_out);
  and and_25 (and_25_out, E5, E2, not_37_out, E0);
  and and_26 (and_26_out, not_38_out, not_39_out, not_40_out);
  and and_27 (and_27_out, not_41_out, not_42_out, not_43_out, not_44_out);
  and and_28 (and_28_out, not_45_out, not_46_out, E2);
  and and_29 (and_29_out, E3, not_47_out, not_48_out, not_49_out);
  and and_30 (and_30_out, not_50_out, E4, E3, not_51_out);
  and and_31 (and_31_out, not_52_out, E4, E3, not_53_out);
  and and_32 (and_32_out, E5, E3, E1, not_54_out);
  and and_33 (and_33_out, E5, E4, not_55_out, not_56_out);
  and and_34 (and_34_out, E5, E4, E1, not_57_out);
  and and_35 (and_35_out, not_58_out, not_59_out, not_60_out);
  and and_36 (and_36_out, not_61_out, not_62_out, not_63_out, not_64_out);
  and and_37 (and_37_out, E5, E3, not_65_out, not_66_out);
  and and_38 (and_38_out, E5, E3, E2, not_67_out);
  and and_39 (and_39_out, E5, E3, E2, not_68_out);
  and and_40 (and_40_out, E5, E4, not_69_out, not_70_out);
  and and_41 (and_41_out, E5, E4, E2, not_71_out);
  and and_42 (and_42_out, E5, E4, E2, not_72_out);
  and and_43 (and_43_out, not_73_out, E4, E2);
  and and_44 (and_44_out, not_74_out, E4, E3);
  and and_45 (and_45_out, E5, not_75_out, not_76_out);
  and and_46 (and_46_out, E5, not_77_out, E1);
  and and_47 (and_47_out, E5, E2, not_78_out);
  and and_48 (and_48_out, E5, E2, not_79_out);
  or or_1 (a, and_1_out, and_2_out, and_3_out, and_4_out, and_5_out, and_6_out, and_7_out);
  or or_2 (b, not_80_out, and_8_out, not_81_out, and_9_out, and_10_out);
  or or_3 (c, and_11_out, and_12_out, and_13_out, and_14_out, and_15_out, and_16_out, and_17_out);
  or or_4 (d, and_18_out, and_19_out, and_20_out, and_21_out, and_22_out, and_23_out, and_24_out, and_25_out);
  or or_5 (e, and_26_out, and_27_out, and_28_out, and_29_out, and_30_out, and_31_out, and_32_out, and_33_out, and_34_out);
  or or_6 (f, and_35_out, and_36_out, and_37_out, and_38_out, and_39_out, and_40_out, and_41_out, and_42_out);
  or or_7 (g, and_43_out, and_44_out, and_45_out, and_46_out, and_47_out, and_48_out);
endmodule
module display1 (
  input  E5,
  input  E4,
  input  E3,
  input  E2,
  input  E1,
  input  E0,
  output a,
  output b,
  output c,
  output d,
  output e,
  output f,
  output g
);

  wire and_1_out, and_2_out, and_3_out, and_4_out, and_5_out, and_6_out, and_7_out, and_8_out, and_9_out,
       and_10_out, and_11_out, and_12_out, and_13_out, and_14_out, and_15_out, and_16_out, and_17_out,
       and_18_out, and_19_out, and_20_out, and_21_out, and_22_out, and_23_out, and_24_out, and_25_out,
       and_26_out, and_27_out, and_28_out, and_29_out, and_30_out, and_31_out, and_32_out, and_33_out,
       and_34_out, and_35_out, and_36_out, and_37_out, and_38_out, and_39_out, and_40_out, and_41_out,
       and_42_out, and_43_out, and_44_out, and_45_out, and_46_out, and_47_out, and_48_out, and_49_out,
       and_50_out, and_51_out, and_52_out, and_53_out, and_54_out, and_55_out, and_56_out, and_57_out,
       and_58_out, and_59_out, and_60_out, and_61_out, and_62_out, and_63_out, and_64_out, and_65_out,
       and_66_out, and_67_out, and_68_out, and_69_out, and_70_out, and_71_out, and_72_out, and_73_out,
       and_74_out, and_75_out, and_76_out, and_77_out, and_78_out, and_79_out, and_80_out, and_81_out,
       and_82_out, and_83_out, and_84_out, and_85_out, and_86_out, and_87_out, and_88_out, and_89_out,
       and_90_out, and_91_out, and_92_out, and_93_out, and_94_out, not_1_out, not_2_out, not_3_out,
       not_4_out, not_5_out, not_6_out, not_7_out, not_8_out, not_9_out, not_10_out, not_11_out, not_12_out,
       not_13_out, not_14_out, not_15_out, not_16_out, not_17_out, not_18_out, not_19_out, not_20_out,
       not_21_out, not_22_out, not_23_out, not_24_out, not_25_out, not_26_out, not_27_out, not_28_out,
       not_29_out, not_30_out, not_31_out, not_32_out, not_33_out, not_34_out, not_35_out, not_36_out,
       not_37_out, not_38_out, not_39_out, not_40_out, not_41_out, not_42_out, not_43_out, not_44_out,
       not_45_out, not_46_out, not_47_out, not_48_out, not_49_out, not_50_out, not_51_out, not_52_out,
       not_53_out, not_54_out, not_55_out, not_56_out, not_57_out, not_58_out, not_59_out, not_60_out,
       not_61_out, not_62_out, not_63_out, not_64_out, not_65_out, not_66_out, not_67_out, not_68_out,
       not_69_out, not_70_out, not_71_out, not_72_out, not_73_out, not_74_out, not_75_out, not_76_out,
       not_77_out, not_78_out, not_79_out, not_80_out, not_81_out, not_82_out, not_83_out, not_84_out,
       not_85_out, not_86_out, not_87_out, not_88_out, not_89_out, not_90_out, not_91_out, not_92_out,
       not_93_out, not_94_out, not_95_out, not_96_out, not_97_out, not_98_out, not_99_out, not_100_out,
       not_101_out, not_102_out, not_103_out, not_104_out, not_105_out, not_106_out, not_107_out,
       not_108_out, not_109_out, not_110_out, not_111_out, not_112_out, not_113_out, not_114_out,
       not_115_out, not_116_out, not_117_out, not_118_out, not_119_out, not_120_out, not_121_out,
       not_122_out, not_123_out, not_124_out, not_125_out, not_126_out, not_127_out, not_128_out,
       not_129_out, not_130_out, not_131_out, not_132_out, not_133_out, not_134_out, not_135_out,
       not_136_out, not_137_out, not_138_out, not_139_out, not_140_out, not_141_out, not_142_out,
       not_143_out, not_144_out, not_145_out, not_146_out, not_147_out, not_148_out, not_149_out,
       not_150_out, not_151_out, not_152_out, not_153_out, not_154_out, not_155_out, not_156_out,
       not_157_out, not_158_out, not_159_out, not_160_out, not_161_out, not_162_out, not_163_out,
       not_164_out, not_165_out, not_166_out, not_167_out, not_168_out, not_169_out, not_170_out,
       not_171_out, not_172_out, not_173_out, not_174_out, not_175_out, not_176_out, not_177_out,
       not_178_out, not_179_out, not_180_out, not_181_out, not_182_out, not_183_out, not_184_out,
       not_185_out, not_186_out, not_187_out, not_188_out, not_189_out, not_190_out, not_191_out,
       not_192_out, not_193_out, not_194_out, not_195_out, not_196_out, not_197_out, not_198_out,
       not_199_out, not_200_out, not_201_out, not_202_out, not_203_out, not_204_out;

  not not_1 (not_1_out, E5);
  not not_2 (not_2_out, E4);
  not not_3 (not_3_out, E2);
  not not_4 (not_4_out, E0);
  not not_5 (not_5_out, E4);
  not not_6 (not_6_out, E2);
  not not_7 (not_7_out, E1);
  not not_8 (not_8_out, E0);
  not not_9 (not_9_out, E5);
  not not_10 (not_10_out, E3);
  not not_11 (not_11_out, E3);
  not not_12 (not_12_out, E4);
  not not_13 (not_13_out, E3);
  not not_14 (not_14_out, E5);
  not not_15 (not_15_out, E1);
  not not_16 (not_16_out, E5);
  not not_17 (not_17_out, E1);
  not not_18 (not_18_out, E5);
  not not_19 (not_19_out, E3);
  not not_20 (not_20_out, E2);
  not not_21 (not_21_out, E2);
  not not_22 (not_22_out, E5);
  not not_23 (not_23_out, E0);
  not not_24 (not_24_out, E4);
  not not_25 (not_25_out, E3);
  not not_26 (not_26_out, E1);
  not not_27 (not_27_out, E2);
  not not_28 (not_28_out, E1);
  not not_29 (not_29_out, E0);
  not not_30 (not_30_out, E5);
  not not_31 (not_31_out, E4);
  not not_32 (not_32_out, E2);
  not not_33 (not_33_out, E5);
  not not_34 (not_34_out, E4);
  not not_35 (not_35_out, E1);
  not not_36 (not_36_out, E0);
  not not_37 (not_37_out, E5);
  not not_38 (not_38_out, E3);
  not not_39 (not_39_out, E2);
  not not_40 (not_40_out, E5);
  not not_41 (not_41_out, E3);
  not not_42 (not_42_out, E2);
  not not_43 (not_43_out, E3);
  not not_44 (not_44_out, E5);
  not not_45 (not_45_out, E4);
  not not_46 (not_46_out, E1);
  not not_47 (not_47_out, E5);
  not not_48 (not_48_out, E4);
  not not_49 (not_49_out, E0);
  not not_50 (not_50_out, E1);
  not not_51 (not_51_out, E0);
  not not_52 (not_52_out, E5);
  not not_53 (not_53_out, E2);
  not not_54 (not_54_out, E1);
  not not_55 (not_55_out, E2);
  not not_56 (not_56_out, E0);
  not not_57 (not_57_out, E4);
  not not_58 (not_58_out, E3);
  not not_59 (not_59_out, E1);
  not not_60 (not_60_out, E4);
  not not_61 (not_61_out, E3);
  not not_62 (not_62_out, E0);
  not not_63 (not_63_out, E1);
  not not_64 (not_64_out, E0);
  not not_65 (not_65_out, E5);
  not not_66 (not_66_out, E2);
  not not_67 (not_67_out, E1);
  not not_68 (not_68_out, E4);
  not not_69 (not_69_out, E3);
  not not_70 (not_70_out, E2);
  not not_71 (not_71_out, E1);
  not not_72 (not_72_out, E5);
  not not_73 (not_73_out, E5);
  not not_74 (not_74_out, E2);
  not not_75 (not_75_out, E1);
  not not_76 (not_76_out, E4);
  not not_77 (not_77_out, E3);
  not not_78 (not_78_out, E5);
  not not_79 (not_79_out, E4);
  not not_80 (not_80_out, E2);
  not not_81 (not_81_out, E0);
  not not_82 (not_82_out, E5);
  not not_83 (not_83_out, E3);
  not not_84 (not_84_out, E2);
  not not_85 (not_85_out, E5);
  not not_86 (not_86_out, E4);
  not not_87 (not_87_out, E1);
  not not_88 (not_88_out, E3);
  not not_89 (not_89_out, E0);
  not not_90 (not_90_out, E5);
  not not_91 (not_91_out, E1);
  not not_92 (not_92_out, E5);
  not not_93 (not_93_out, E1);
  not not_94 (not_94_out, E5);
  not not_95 (not_95_out, E4);
  not not_96 (not_96_out, E1);
  not not_97 (not_97_out, E5);
  not not_98 (not_98_out, E3);
  not not_99 (not_99_out, E0);
  not not_100 (not_100_out, E5);
  not not_101 (not_101_out, E3);
  not not_102 (not_102_out, E0);
  not not_103 (not_103_out, E4);
  not not_104 (not_104_out, E3);
  not not_105 (not_105_out, E2);
  not not_106 (not_106_out, E1);
  not not_107 (not_107_out, E4);
  not not_108 (not_108_out, E3);
  not not_109 (not_109_out, E1);
  not not_110 (not_110_out, E0);
  not not_111 (not_111_out, E2);
  not not_112 (not_112_out, E1);
  not not_113 (not_113_out, E0);
  not not_114 (not_114_out, E2);
  not not_115 (not_115_out, E4);
  not not_116 (not_116_out, E3);
  not not_117 (not_117_out, E0);
  not not_118 (not_118_out, E1);
  not not_119 (not_119_out, E5);
  not not_120 (not_120_out, E4);
  not not_121 (not_121_out, E2);
  not not_122 (not_122_out, E0);
  not not_123 (not_123_out, E4);
  not not_124 (not_124_out, E2);
  not not_125 (not_125_out, E1);
  not not_126 (not_126_out, E0);
  not not_127 (not_127_out, E3);
  not not_128 (not_128_out, E2);
  not not_129 (not_129_out, E1);
  not not_130 (not_130_out, E0);
  not not_131 (not_131_out, E3);
  not not_132 (not_132_out, E0);
  not not_133 (not_133_out, E5);
  not not_134 (not_134_out, E4);
  not not_135 (not_135_out, E1);
  not not_136 (not_136_out, E0);
  not not_137 (not_137_out, E0);
  not not_138 (not_138_out, E5);
  not not_139 (not_139_out, E0);
  not not_140 (not_140_out, E4);
  not not_141 (not_141_out, E3);
  not not_142 (not_142_out, E1);
  not not_143 (not_143_out, E0);
  not not_144 (not_144_out, E2);
  not not_145 (not_145_out, E0);
  not not_146 (not_146_out, E0);
  not not_147 (not_147_out, E5);
  not not_148 (not_148_out, E3);
  not not_149 (not_149_out, E1);
  not not_150 (not_150_out, E0);
  not not_151 (not_151_out, E5);
  not not_152 (not_152_out, E4);
  not not_153 (not_153_out, E3);
  not not_154 (not_154_out, E1);
  not not_155 (not_155_out, E4);
  not not_156 (not_156_out, E3);
  not not_157 (not_157_out, E0);
  not not_158 (not_158_out, E5);
  not not_159 (not_159_out, E2);
  not not_160 (not_160_out, E1);
  not not_161 (not_161_out, E2);
  not not_162 (not_162_out, E1);
  not not_163 (not_163_out, E0);
  not not_164 (not_164_out, E5);
  not not_165 (not_165_out, E0);
  not not_166 (not_166_out, E5);
  not not_167 (not_167_out, E4);
  not not_168 (not_168_out, E1);
  not not_169 (not_169_out, E0);
  not not_170 (not_170_out, E5);
  not not_171 (not_171_out, E3);
  not not_172 (not_172_out, E2);
  not not_173 (not_173_out, E5);
  not not_174 (not_174_out, E1);
  not not_175 (not_175_out, E4);
  not not_176 (not_176_out, E3);
  not not_177 (not_177_out, E0);
  not not_178 (not_178_out, E1);
  not not_179 (not_179_out, E1);
  not not_180 (not_180_out, E3);
  not not_181 (not_181_out, E2);
  not not_182 (not_182_out, E5);
  not not_183 (not_183_out, E4);
  not not_184 (not_184_out, E1);
  not not_185 (not_185_out, E4);
  not not_186 (not_186_out, E0);
  not not_187 (not_187_out, E5);
  not not_188 (not_188_out, E1);
  not not_189 (not_189_out, E5);
  not not_190 (not_190_out, E4);
  not not_191 (not_191_out, E1);
  not not_192 (not_192_out, E5);
  not not_193 (not_193_out, E2);
  not not_194 (not_194_out, E0);
  not not_195 (not_195_out, E5);
  not not_196 (not_196_out, E3);
  not not_197 (not_197_out, E4);
  not not_198 (not_198_out, E3);
  not not_199 (not_199_out, E2);
  not not_200 (not_200_out, E4);
  not not_201 (not_201_out, E3);
  not not_202 (not_202_out, E2);
  not not_203 (not_203_out, E0);
  not not_204 (not_204_out, E1);
  and and_1 (and_1_out, not_1_out, not_2_out, not_3_out, not_4_out);
  and and_2 (and_2_out, not_5_out, not_6_out, not_7_out, not_8_out);
  and and_3 (and_3_out, not_9_out, not_10_out, E1);
  and and_4 (and_4_out, not_11_out, E1, E0);
  and and_5 (and_5_out, not_12_out, E2, E0);
  and and_6 (and_6_out, not_13_out, E2, E1);
  and and_7 (and_7_out, not_14_out, E3, not_15_out, E0);
  and and_8 (and_8_out, not_16_out, E3, E2, not_17_out);
  and and_9 (and_9_out, not_18_out, E4, not_19_out, not_20_out);
  and and_10 (and_10_out, E4, not_21_out, E1);
  and and_11 (and_11_out, not_22_out, E4, E2, not_23_out);
  and and_12 (and_12_out, E5, not_24_out, not_25_out, not_26_out);
  and and_13 (and_13_out, E5, not_27_out, not_28_out, not_29_out);
  and and_14 (and_14_out, E5, E2, E0);
  and and_15 (and_15_out, E5, E3, E1);
  and and_16 (and_16_out, not_30_out, not_31_out, not_32_out);
  and and_17 (and_17_out, not_33_out, not_34_out, not_35_out, not_36_out);
  and and_18 (and_18_out, not_37_out, not_38_out, not_39_out, E0);
  and and_19 (and_19_out, not_40_out, not_41_out, not_42_out, E1);
  and and_20 (and_20_out, not_43_out, E2, E1, E0);
  and and_21 (and_21_out, not_44_out, not_45_out, E3, not_46_out);
  and and_22 (and_22_out, not_47_out, not_48_out, E3, not_49_out);
  and and_23 (and_23_out, E3, not_50_out, not_51_out);
  and and_24 (and_24_out, E4, E1, E0);
  and and_25 (and_25_out, not_52_out, E4, E2);
  and and_26 (and_26_out, E5, not_53_out, not_54_out);
  and and_27 (and_27_out, E5, not_55_out, not_56_out);
  and and_28 (and_28_out, E5, not_57_out, not_58_out, not_59_out, E0);
  and and_29 (and_29_out, E5, not_60_out, not_61_out, E1, not_62_out);
  and and_30 (and_30_out, E5, E3, E1, E0);
  and and_31 (and_31_out, E5, E4, not_63_out, not_64_out);
  and and_32 (and_32_out, not_65_out, not_66_out, not_67_out);
  and and_33 (and_33_out, not_68_out, not_69_out, E2);
  and and_34 (and_34_out, E3, not_70_out, not_71_out);
  and and_35 (and_35_out, not_72_out, E3, E1);
  and and_36 (and_36_out, not_73_out, E4, not_74_out);
  and and_37 (and_37_out, E4, not_75_out);
  and and_38 (and_38_out, E5, not_76_out, not_77_out, E1);
  and and_39 (and_39_out, E5, E2);
  and and_40 (and_40_out, not_78_out, not_79_out, not_80_out, not_81_out);
  and and_41 (and_41_out, not_82_out, not_83_out, not_84_out, E1);
  and and_42 (and_42_out, not_85_out, not_86_out, E2, not_87_out, E0);
  and and_43 (and_43_out, not_88_out, E2, E1, not_89_out);
  and and_44 (and_44_out, not_90_out, E3, not_91_out, E0);
  and and_45 (and_45_out, not_92_out, E3, E2, not_93_out);
  and and_46 (and_46_out, not_94_out, not_95_out, E3, E2, E0);
  and and_47 (and_47_out, E3, E2, not_96_out, E0);
  and and_48 (and_48_out, not_97_out, E4, not_98_out, not_99_out);
  and and_49 (and_49_out, not_100_out, E4, not_101_out, E1);
  and and_50 (and_50_out, E4, E1, not_102_out);
  and and_51 (and_51_out, E5, not_103_out, not_104_out, not_105_out, not_106_out);
  and and_52 (and_52_out, E5, not_107_out, not_108_out, not_109_out, not_110_out);
  and and_53 (and_53_out, E5, not_111_out, not_112_out, not_113_out);
  and and_54 (and_54_out, E5, not_114_out, E1, E0);
  and and_55 (and_55_out, E5, not_115_out, not_116_out, E2, E1);
  and and_56 (and_56_out, E5, E3, E1, not_117_out);
  and and_57 (and_57_out, E5, E4, E2, not_118_out, E0);
  and and_58 (and_58_out, not_119_out, not_120_out, not_121_out, not_122_out);
  and and_59 (and_59_out, not_123_out, not_124_out, not_125_out, not_126_out);
  and and_60 (and_60_out, not_127_out, not_128_out, not_129_out, not_130_out);
  and and_61 (and_61_out, not_131_out, E2, E1, not_132_out);
  and and_62 (and_62_out, not_133_out, not_134_out, E3, not_135_out, not_136_out);
  and and_63 (and_63_out, E4, E1, not_137_out);
  and and_64 (and_64_out, not_138_out, E4, E2, not_139_out);
  and and_65 (and_65_out, E5, not_140_out, not_141_out, not_142_out, not_143_out);
  and and_66 (and_66_out, E5, E3, not_144_out, not_145_out);
  and and_67 (and_67_out, E5, E3, E1, not_146_out);
  and and_68 (and_68_out, not_147_out, not_148_out, not_149_out, not_150_out);
  and and_69 (and_69_out, not_151_out, not_152_out, not_153_out, E2, not_154_out);
  and and_70 (and_70_out, not_155_out, not_156_out, E2, not_157_out);
  and and_71 (and_71_out, not_158_out, E3, not_159_out, not_160_out);
  and and_72 (and_72_out, E3, not_161_out, not_162_out, not_163_out);
  and and_73 (and_73_out, not_164_out, E3, E1, not_165_out);
  and and_74 (and_74_out, not_166_out, not_167_out, E3, E2, E1);
  and and_75 (and_75_out, E4, not_168_out, not_169_out);
  and and_76 (and_76_out, not_170_out, E4, not_171_out, not_172_out, E1);
  and and_77 (and_77_out, not_173_out, E4, E3, not_174_out);
  and and_78 (and_78_out, E5, not_175_out, not_176_out, E1);
  and and_79 (and_79_out, E5, E2, not_177_out);
  and and_80 (and_80_out, E5, E3, E2, not_178_out);
  and and_81 (and_81_out, E5, E4, E2, not_179_out);
  and and_82 (and_82_out, not_180_out, not_181_out, E1);
  and and_83 (and_83_out, not_182_out, not_183_out, E2, not_184_out);
  and and_84 (and_84_out, not_185_out, E2, not_186_out);
  and and_85 (and_85_out, not_187_out, E3, not_188_out);
  and and_86 (and_86_out, not_189_out, not_190_out, E3, E2);
  and and_87 (and_87_out, E3, E2, not_191_out);
  and and_88 (and_88_out, not_192_out, E4, not_193_out, not_194_out);
  and and_89 (and_89_out, not_195_out, E4, not_196_out, E1);
  and and_90 (and_90_out, E5, not_197_out, not_198_out, not_199_out);
  and and_91 (and_91_out, E5, not_200_out, not_201_out, E1);
  and and_92 (and_92_out, E5, not_202_out, E1);
  and and_93 (and_93_out, E5, E2, not_203_out);
  and and_94 (and_94_out, E5, E4, E2, not_204_out);
  or or_1 (c, and_32_out, E0, and_33_out, and_34_out, and_35_out, and_36_out, and_37_out, and_38_out, and_39_out);
  or or_2 (e, and_58_out, and_59_out, and_60_out, and_61_out, and_62_out, and_63_out, and_64_out, and_65_out, and_66_out, and_67_out);
  or or_3 (a, and_1_out, and_2_out, and_3_out, and_4_out, and_5_out, and_6_out, and_7_out, and_8_out, and_9_out, and_10_out, and_11_out, and_12_out, and_13_out, and_14_out, and_15_out);
  or or_4 (b, and_16_out, and_17_out, and_18_out, and_19_out, and_20_out, and_21_out, and_22_out, and_23_out, and_24_out, and_25_out, and_26_out, and_27_out, and_28_out, and_29_out, and_30_out, and_31_out);
  or or_5 (d, and_40_out, and_41_out, and_42_out, and_43_out, and_44_out, and_45_out, and_46_out, and_47_out, and_48_out, and_49_out, and_50_out, and_51_out, and_52_out, and_53_out, and_54_out, and_55_out, and_56_out, and_57_out);
  or or_6 (f, and_68_out, and_69_out, and_70_out, and_71_out, and_72_out, and_73_out, and_74_out, and_75_out, and_76_out, and_77_out, and_78_out, and_79_out, and_80_out, and_81_out);
  or or_7 (g, and_82_out, and_83_out, and_84_out, and_85_out, and_86_out, and_87_out, and_88_out, and_89_out, and_90_out, and_91_out, and_92_out, and_93_out, and_94_out);
endmodule

module LEDS (
);

  wire undriven, undriven_2, undriven_3, undriven_4, undriven_5, undriven_6, undriven_7, undriven_8,
       undriven_9, undriven_10, undriven_11, undriven_12, undriven_13, undriven_14, undriven_15, undriven_16,
       undriven_17, undriven_18, undriven_19, undriven_20;

  LED M1 (.in(undriven));
  LED M2 (.in(undriven_20));
  LED M3 (.in(undriven_2));
  LED M4 (.in(undriven_3));
  LED M5 (.in(undriven_4));
  LED M6 (.in(undriven_5));
  LED M7 (.in(undriven_6));
  LED M8 (.in(undriven_7));
  LED M9 (.in(undriven_8));
  LED M10 (.in(undriven_9));
  LED M11 (.in(undriven_10));
  LED M12 (.in(undriven_11));
  LED M13 (.in(undriven_12));
  LED M14 (.in(undriven_13));
  LED M15 (.in(undriven_14));
  LED M16 (.in(undriven_15));
  LED M17 (.in(undriven_16));
  LED M18 (.in(undriven_17));
  LED M19 (.in(undriven_18));
  LED M20 (.in(undriven_19));
endmodule

module Somador (
  input  A0,
  input  A1,
  input  A2,
  input  A3,
  input  A4,
  input  A5,
  input  B0,
  input  B1,
  input  B2,
  input  B3,
  input  B4,
  input  B5,
  output SAIDA_0,
  output SAIDA_1,
  output SAIDA_2,
  output SAIDA_3,
  output SAIDA_4,
  output SAIDA_5,
  output C
);

  wire and_1_out, and_2_out, and_3_out, and_4_out, and_5_out, and_6_out, and_7_out, and_8_out, and_9_out,
       and_10_out, and_11_out, and_12_out, or_1_out, or_2_out, or_3_out, or_4_out, or_5_out, xor_1_out,
       xor_2_out, xor_3_out, xor_4_out, xor_5_out, xor_6_out;

  and and_1 (and_1_out, A0, B0);
  and and_2 (and_2_out, A1, B1);
  and and_3 (and_3_out, A2, B2);
  and and_4 (and_4_out, A3, B3);
  and and_5 (and_5_out, A4, B4);
  and and_6 (and_6_out, A5, B5);
  or or_1 (or_1_out, and_1_out, and_8_out);
  or or_2 (or_2_out, and_2_out, and_7_out);
  or or_3 (or_3_out, and_3_out, and_9_out);
  or or_4 (or_4_out, and_4_out, and_10_out);
  or or_5 (or_5_out, and_5_out, and_11_out);
  or or_6 (C, and_6_out, and_12_out);
  xor xor_1 (xor_1_out, A0, B0);
  xor xor_2 (xor_2_out, A1, B1);
  and and_7 (and_7_out, xor_2_out, or_1_out);
  xor xor_3 (xor_3_out, A2, B2);
  xor xor_4 (xor_4_out, A3, B3);
  xor xor_5 (xor_5_out, A4, B4);
  xor xor_6 (xor_6_out, A5, B5);
  and and_8 (and_8_out, xor_1_out, 1'b0);
  and and_9 (and_9_out, xor_3_out, or_2_out);
  and and_10 (and_10_out, xor_4_out, or_3_out);
  and and_11 (and_11_out, xor_5_out, or_4_out);
  and and_12 (and_12_out, xor_6_out, or_5_out);
  xor xor_7 (SAIDA_0, xor_1_out, 1'b0);
  xor xor_8 (SAIDA_1, xor_2_out, or_1_out);
  xor xor_9 (SAIDA_2, xor_3_out, or_2_out);
  xor xor_10 (SAIDA_3, xor_4_out, or_3_out);
  xor xor_11 (SAIDA_4, xor_5_out, or_4_out);
  xor xor_12 (SAIDA_5, xor_6_out, or_5_out);
endmodule
