// Logisim project contador.circ as structural Verilog: 4 circuits, main circuit main
module main (
  input  S,
  input  S_2,
  input  S_3
);

  wire CLK_2_out, CLK_3_out, CLK_out, j_k_ff_1_q, j_k_ff_2_q, j_k_ff_3_q, j_k_ff_4_q, j_k_ff_5_q, j_k_ff_6_q,
       j_k_ff_7_q, j_k_ff_8_q, j_k_ff_9_q, j_k_ff_10_q, j_k_ff_11_q, j_k_ff_12_q, simpl_jk_1_j0,
       simpl_jk_1_j1, simpl_jk_1_j2, simpl_jk_1_j3, simpl_jk_1_k0, simpl_jk_1_k1, simpl_jk_1_k2,
       simpl_jk_1_k3, simpl_jk_2_j0, simpl_jk_2_j1, simpl_jk_2_j2, simpl_jk_2_j3, simpl_jk_2_k0,
       simpl_jk_2_k1, simpl_jk_2_k2, simpl_jk_2_k3, simpl_jk_3_j0, simpl_jk_3_j1, simpl_jk_3_j2,
       simpl_jk_3_j3, simpl_jk_3_k0, simpl_jk_3_k1, simpl_jk_3_k2, simpl_jk_3_k3;

  Clock CLK (.out(CLK_out));
  Clock CLK_2 (.out(CLK_2_out));
  Clock CLK_3 (.out(CLK_3_out));
  simpl_jk simpl_jk_1 (
    .S(S), .E3(j_k_ff_1_q), .E2(j_k_ff_4_q), .E1(j_k_ff_7_q), .E0(j_k_ff_10_q), .J3(simpl_jk_1_j3),
    .K3(simpl_jk_1_k3), .J2(simpl_jk_1_j2), .K2(simpl_jk_1_k2), .J1(simpl_jk_1_j1), .K1(simpl_jk_1_k1),
    .J0(simpl_jk_1_j0), .K0(simpl_jk_1_k0));
  simpl_jk simpl_jk_2 (
    .S(S_2), .E3(j_k_ff_2_q), .E2(j_k_ff_5_q), .E1(j_k_ff_8_q), .E0(j_k_ff_11_q), .J3(simpl_jk_2_j3),
    .K3(simpl_jk_2_k3), .J2(simpl_jk_2_j2), .K2(simpl_jk_2_k2), .J1(simpl_jk_2_j1), .K1(simpl_jk_2_k1),
    .J0(simpl_jk_2_j0), .K0(simpl_jk_2_k0));
  simpl_jk simpl_jk_3 (
    .S(S_3), .E3(j_k_ff_3_q), .E2(j_k_ff_6_q), .E1(j_k_ff_9_q), .E0(j_k_ff_12_q), .J3(simpl_jk_3_j3),
    .K3(simpl_jk_3_k3), .J2(simpl_jk_3_j2), .K2(simpl_jk_3_k2), .J1(simpl_jk_3_j1), .K1(simpl_jk_3_k1),
    .J0(simpl_jk_3_j0), .K0(simpl_jk_3_k0));
  J_K_Flip_Flop j_k_ff_1 (
    .J(simpl_jk_1_j3), .clk(CLK_out), .K(simpl_jk_1_k3), .Q(j_k_ff_1_q));  // open: Qn, preset, en, reset
  J_K_Flip_Flop j_k_ff_2 (
    .J(simpl_jk_2_j3), .clk(CLK_2_out), .K(simpl_jk_2_k3), .Q(j_k_ff_2_q));  // open: Qn, preset, en, reset
  J_K_Flip_Flop j_k_ff_3 (
    .J(simpl_jk_3_j3), .clk(CLK_3_out), .K(simpl_jk_3_k3), .Q(j_k_ff_3_q));  // open: Qn, preset, en, reset
  J_K_Flip_Flop j_k_ff_4 (
    .J(simpl_jk_1_j2), .clk(CLK_out), .K(simpl_jk_1_k2), .Q(j_k_ff_4_q));  // open: Qn, preset, en, reset
  J_K_Flip_Flop j_k_ff_5 (
    .J(simpl_jk_2_j2), .clk(CLK_2_out), .K(simpl_jk_2_k2), .Q(j_k_ff_5_q));  // open: Qn, preset, en, reset
  J_K_Flip_Flop j_k_ff_6 (
    .J(simpl_jk_3_j2), .clk(CLK_3_out), .K(simpl_jk_3_k2), .Q(j_k_ff_6_q));  // open: Qn, preset, en, reset
  J_K_Flip_Flop j_k_ff_7 (
    .J(simpl_jk_1_j1), .clk(CLK_out), .K(simpl_jk_1_k1), .Q(j_k_ff_7_q));  // open: Qn, preset, en, reset
  J_K_Flip_Flop j_k_ff_8 (
    .J(simpl_jk_2_j1), .clk(CLK_2_out), .K(simpl_jk_2_k1), .Q(j_k_ff_8_q));  // open: Qn, preset, en, reset
  J_K_Flip_Flop j_k_ff_9 (
    .J(simpl_jk_3_j1), .clk(CLK_3_out), .K(simpl_jk_3_k1), .Q(j_k_ff_9_q));  // open: Qn, preset, en, reset
  J_K_Flip_Flop j_k_ff_10 (
    .J(simpl_jk_1_j0), .clk(CLK_out), .K(simpl_jk_1_k0), .Q(j_k_ff_10_q));  // open: Qn, preset, en, reset
  J_K_Flip_Flop j_k_ff_11 (
    .J(simpl_jk_2_j0), .clk(CLK_2_out), .K(simpl_jk_2_k0), .Q(j_k_ff_11_q));  // open: Qn, preset, en, reset
  J_K_Flip_Flop j_k_ff_12 (
    .J(simpl_jk_3_j0), .clk(CLK_3_out), .K(simpl_jk_3_k0), .Q(j_k_ff_12_q));  // open: Qn, preset, en, reset
endmodule

// D
module maquina_de_estado_D (
  input  S,
  input  E3,
  input  E2,
  input  E1,
  input  E0,
  output S3,
  output S2,
  output S1,
  output S0
);

  wire and_1_out, and_2_out, and_3_out, and_4_out, and_5_out, and_6_out, and_7_out, and_8_out, and_9_out,
       and_10_out, and_11_out, and_12_out, and_13_out, and_14_out, and_15_out, and_16_out, and_17_out,
       and_18_out, and_19_out, and_20_out, and_21_out, and_22_out, and_23_out, and_24_out, and_25_out,
       and_26_out, and_27_out, and_28_out, and_29_out, and_30_out, and_31_out, and_32_out, and_33_out,
       and_34_out, and_35_out, and_36_out, and_37_out, and_38_out, and_39_out, and_40_out, and_41_out,
       and_42_out, and_43_out, and_44_out, and_45_out, and_46_out, and_47_out, and_48_out, and_49_out,
       and_50_out, and_51_out, and_52_out, and_53_out, not_1_out, not_2_out, not_3_out, not_4_out, not_5_out,
       not_6_out, not_7_out, not_8_out, not_9_out, not_10_out, not_11_out, not_12_out, not_13_out,
       not_14_out, not_15_out, not_16_out, not_17_out, not_18_out, not_19_out, not_20_out, not_21_out,
       not_22_out, not_23_out, not_24_out, not_25_out, not_26_out, not_27_out, not_28_out, not_29_out,
       not_30_out, not_31_out, not_32_out, not_33_out, not_34_out, not_35_out, not_36_out, not_37_out,
       not_38_out, not_39_out, not_40_out, not_41_out, not_42_out, not_43_out, or_1_out, or_3_out, or_4_out,
       or_5_out, or_6_out, or_7_out, or_10_out, or_11_out;

  not not_1 (not_1_out, S);
  not not_2 (not_2_out, E3);
  not not_3 (not_3_out, S);
  not not_4 (not_4_out, E3);
  not not_5 (not_5_out, S);
  not not_6 (not_6_out, E3);
  not not_7 (not_7_out, E3);
  not not_8 (not_8_out, E0);
  not not_9 (not_9_out, S);
  not not_10 (not_10_out, E3);
  not not_11 (not_11_out, S);
  not not_12 (not_12_out, E3);
  not not_13 (not_13_out, E2);
  not not_14 (not_14_out, E1);
  and and_1 (and_1_out, not_1_out, not_2_out);
  not not_15 (not_15_out, E2);
  not not_16 (not_16_out, E1);
  not not_17 (not_17_out, E0);
  and and_2 (and_2_out, not_3_out, E3);
  not not_18 (not_18_out, E2);
  not not_19 (not_19_out, E1);
  and and_3 (and_3_out, S, not_4_out);
  and and_4 (and_4_out, S, E3);
  not not_20 (not_20_out, E2);
  not not_21 (not_21_out, E1);
  not not_22 (not_22_out, E0);
  and and_5 (and_5_out, not_5_out, not_6_out);
  and and_6 (and_6_out, E2, E0);
  and and_7 (and_7_out, not_7_out, E2);
  and and_8 (and_8_out, E1, not_8_out);
  and and_9 (and_9_out, not_9_out, E3);
  not not_23 (not_23_out, E2);
  not not_24 (not_24_out, E1);
  not not_25 (not_25_out, E0);
  and and_10 (and_10_out, S, not_10_out);
  not not_26 (not_26_out, E2);
  not not_27 (not_27_out, E3);
  not not_28 (not_28_out, E1);
  not not_29 (not_29_out, S);
  not not_30 (not_30_out, E3);
  and and_11 (and_11_out, not_11_out, not_12_out);
  not not_31 (not_31_out, E1);
  not not_32 (not_32_out, E0);
  not not_33 (not_33_out, S);
  not not_34 (not_34_out, E3);
  not not_35 (not_35_out, E0);
  and and_12 (and_12_out, not_13_out, not_14_out);
  not not_36 (not_36_out, E0);
  and and_13 (and_13_out, and_1_out, not_15_out);
  and and_14 (and_14_out, and_13_out, and_15_out);
  and and_15 (and_15_out, not_16_out, not_17_out);
  and and_16 (and_16_out, and_2_out, not_18_out);
  and and_17 (and_17_out, and_16_out, and_18_out);
  and and_18 (and_18_out, not_19_out, E0);
  and and_19 (and_19_out, and_3_out, E2);
  and and_20 (and_20_out, and_19_out, and_21_out);
  and and_21 (and_21_out, E1, E0);
  and and_22 (and_22_out, and_4_out, not_20_out);
  and and_23 (and_23_out, and_22_out, and_24_out);
  and and_24 (and_24_out, not_21_out, not_22_out);
  and and_25 (and_25_out, and_5_out, and_6_out);
  or or_1 (or_1_out, and_25_out, and_26_out);
  and and_26 (and_26_out, and_7_out, and_8_out);
  and and_27 (and_27_out, and_9_out, not_23_out);
  and and_28 (and_28_out, and_27_out, and_29_out);
  and and_29 (and_29_out, not_24_out, not_25_out);
  and and_30 (and_30_out, and_10_out, not_26_out);
  and and_31 (and_31_out, and_30_out, and_32_out);
  and and_32 (and_32_out, E1, E0);
  and and_33 (and_33_out, S, not_27_out);
  and and_34 (and_34_out, and_33_out, and_35_out);
  and and_35 (and_35_out, E2, not_28_out);
  and and_36 (and_36_out, not_29_out, not_30_out);
  and and_37 (and_37_out, and_36_out, and_38_out);
  and and_38 (and_38_out, E1, E0);
  and and_39 (and_39_out, and_11_out, E2);
  and and_40 (and_40_out, and_39_out, and_41_out);
  and and_41 (and_41_out, not_31_out, not_32_out);
  and and_42 (and_42_out, not_33_out, E3);
  and and_43 (and_43_out, and_42_out, not_37_out);
  not not_37 (not_37_out, E2);
  not not_38 (not_38_out, E1);
  and and_44 (and_44_out, not_38_out, not_39_out);
  not not_39 (not_39_out, E0);
  and and_45 (and_45_out, S, not_40_out);
  not not_40 (not_40_out, E3);
  not not_41 (not_41_out, E1);
  and and_46 (and_46_out, not_41_out, E0);
  and and_47 (and_47_out, S, not_42_out);
  not not_42 (not_42_out, E3);
  and and_48 (and_48_out, E1, not_43_out);
  not not_43 (not_43_out, E0);
  and and_49 (and_49_out, not_34_out, not_35_out);
  or or_2 (S0, and_49_out, and_50_out);
  and and_50 (and_50_out, and_12_out, not_36_out);
  or or_3 (or_3_out, and_14_out, and_17_out);
  or or_4 (or_4_out, and_20_out, and_23_out);
  or or_5 (or_5_out, or_1_out, and_28_out);
  or or_6 (or_6_out, and_31_out, and_34_out);
  or or_7 (or_7_out, and_37_out, and_40_out);
  and and_51 (and_51_out, and_43_out, and_44_out);
  and and_52 (and_52_out, and_45_out, and_46_out);
  and and_53 (and_53_out, and_47_out, and_48_out);
  or or_8 (S3, or_3_out, or_4_out);
  or or_9 (S2, or_5_out, or_6_out);
  or or_10 (or_10_out, or_7_out, and_51_out);
  or or_11 (or_11_out, and_52_out, and_53_out);
  or or_12 (S1, or_10_out, or_11_out);
endmodule

// JK
module maquina_de_estado_JK (
  input  S,
  input  E3,
  input  E2,
  input  E1,
  input  E0,
  output J3,
  output K3,
  output J2,
  output K2,
  output J1,
  output K1,
  output J0,
  output K0
);

  wire and_1_out, and_2_out, and_3_out, and_4_out, and_5_out, and_6_out, and_7_out, and_8_out, and_9_out,
       and_10_out, and_11_out, and_12_out, and_13_out, and_14_out, and_15_out, and_16_out, and_17_out,
       and_18_out, and_19_out, and_20_out, and_21_out, and_22_out, and_23_out, and_24_out, and_25_out,
       and_26_out, and_27_out, and_28_out, and_29_out, and_30_out, and_31_out, and_32_out, and_33_out,
       and_34_out, not_1_out, not_2_out, not_3_out, not_4_out, not_5_out, not_6_out, not_7_out, not_8_out,
       not_9_out, not_10_out, not_11_out, not_12_out, not_14_out, not_15_out, not_16_out, not_17_out,
       not_18_out, not_19_out, not_20_out, not_21_out, not_22_out, not_23_out, not_24_out, not_25_out,
       not_26_out, not_27_out, not_28_out, not_29_out, or_1_out, or_2_out, or_4_out, or_5_out, or_10_out;

  not not_1 (not_1_out, E3);
  not not_2 (not_2_out, E2);
  not not_3 (not_3_out, E1);
  not not_4 (not_4_out, S);
  not not_5 (not_5_out, E1);
  not not_6 (not_6_out, E0);
  not not_7 (not_7_out, E3);
  not not_8 (not_8_out, S);
  not not_9 (not_9_out, E1);
  not not_10 (not_10_out, S);
  not not_11 (not_11_out, S);
  not not_12 (not_12_out, E0);
  not not_13 (J0, E0);
  not not_14 (not_14_out, S);
  not not_15 (not_15_out, E2);
  not not_16 (not_16_out, E1);
  not not_17 (not_17_out, E0);
  and and_1 (and_1_out, S, not_1_out);
  not not_18 (not_18_out, S);
  not not_19 (not_19_out, E0);
  not not_20 (not_20_out, S);
  not not_21 (not_21_out, S);
  and and_2 (and_2_out, S, not_2_out);
  and and_3 (and_3_out, not_3_out, E0);
  and and_4 (and_4_out, not_4_out, E3);
  and and_5 (and_5_out, not_5_out, not_6_out);
  and and_6 (and_6_out, S, not_7_out);
  and and_7 (and_7_out, E1, E0);
  and and_8 (and_8_out, not_8_out, not_9_out);
  not not_22 (not_22_out, E0);
  not not_23 (not_23_out, S);
  not not_24 (not_24_out, E3);
  not not_25 (not_25_out, E0);
  and and_9 (and_9_out, not_10_out, E3);
  not not_26 (not_26_out, E2);
  not not_27 (not_27_out, E1);
  not not_28 (not_28_out, E0);
  and and_10 (and_10_out, not_11_out, not_12_out);
  and and_11 (and_11_out, not_14_out, not_15_out);
  and and_12 (and_12_out, and_11_out, and_13_out);
  and and_13 (and_13_out, not_16_out, not_17_out);
  and and_14 (and_14_out, and_1_out, E2);
  and and_15 (and_15_out, and_14_out, and_16_out);
  and and_16 (and_16_out, E1, E0);
  and and_17 (and_17_out, not_18_out, not_19_out);
  or or_1 (or_1_out, and_17_out, and_18_out);
  and and_18 (and_18_out, not_20_out, E1);
  and and_19 (and_19_out, not_21_out, E2);
  or or_2 (or_2_out, and_19_out, and_20_out);
  and and_20 (and_20_out, and_2_out, and_3_out);
  and and_21 (and_21_out, and_4_out, and_5_out);
  or or_3 (J2, and_21_out, and_22_out);
  and and_22 (and_22_out, and_6_out, and_7_out);
  and and_23 (and_23_out, and_8_out, not_22_out);
  or or_4 (or_4_out, and_23_out, E3);
  and and_24 (and_24_out, S, E1);
  and and_25 (and_25_out, and_24_out, E0);
  and and_26 (and_26_out, not_23_out, not_24_out);
  and and_27 (and_27_out, and_26_out, and_28_out);
  and and_28 (and_28_out, E2, not_25_out);
  and and_29 (and_29_out, and_9_out, not_26_out);
  and and_30 (and_30_out, and_29_out, and_31_out);
  and and_31 (and_31_out, not_27_out, not_28_out);
  and and_32 (and_32_out, S, not_29_out);
  not not_29 (not_29_out, E3);
  or or_5 (or_5_out, and_10_out, E3);
  or or_6 (K1, or_5_out, and_33_out);
  and and_33 (and_33_out, S, E0);
  or or_7 (J3, and_12_out, and_15_out);
  or or_8 (K3, or_1_out, or_2_out);
  or or_9 (K2, or_4_out, and_25_out);
  or or_10 (or_10_out, and_27_out, and_30_out);
  and and_34 (and_34_out, and_32_out, E0);
  or or_11 (J1, or_10_out, and_34_out);

  assign K0 = 1'b1;
endmodule

// Maq. Estados
module simpl_jk (
  input  S,
  input  E3,
  input  E2,
  input  E1,
  input  E0,
  output J3,
  output K3,
  output J2,
  output K2,
  output J1,
  output K1,
  output J0,
  output K0
);

  wire a_out, and_1_out, and_2_out, and_3_out, and_4_out, and_5_out, and_6_out, and_7_out, and_8_out,
       and_9_out, and_10_out, and_11_out, and_12_out, b_out, c_out, d_out, e_out, f_out, g_out, not_1_out,
       not_2_out, not_3_out, not_4_out, or_2_out, or_3_out, or_4_out, or_5_out, or_9_out;

  not not_1 (not_1_out, S);
  not not_2 (not_2_out, E3);
  not not_3 (not_3_out, E2);
  not not_4 (not_4_out, E1);
  not not_5 (J0, E0);
  and a (a_out, not_1_out, J0);
  and b (b_out, E1, E0);
  and c (c_out, not_3_out, not_4_out);
  and d (d_out, S, not_2_out);
  and e (e_out, S, E0);
  and f (f_out, b_out, d_out);
  and g (g_out, a_out, not_4_out);
  and and_1 (and_1_out, a_out, c_out);
  and and_2 (and_2_out, f_out, E2);
  or or_1 (J3, and_1_out, and_2_out);
  or or_2 (or_2_out, a_out, and_3_out);
  and and_3 (and_3_out, not_1_out, E1);
  and and_4 (and_4_out, not_1_out, E2);
  or or_3 (or_3_out, and_4_out, and_5_out);
  and and_5 (and_5_out, c_out, e_out);
  and and_6 (and_6_out, g_out, E3);
  or or_4 (or_4_out, g_out, E3);
  and and_7 (and_7_out, S, b_out);
  and and_8 (and_8_out, a_out, not_2_out);
  and and_9 (and_9_out, and_8_out, E2);
  and and_10 (and_10_out, a_out, E3);
  and and_11 (and_11_out, and_10_out, c_out);
  or or_5 (or_5_out, a_out, E3);
  or or_6 (K3, or_2_out, or_3_out);
  or or_7 (J2, and_6_out, f_out);
  or or_8 (K2, or_4_out, and_7_out);
  or or_9 (or_9_out, and_9_out, and_11_out);
  or or_10 (J1, or_9_out, and_12_out);
  and and_12 (and_12_out, d_out, E0);
  or or_11 (K1, or_5_out, e_out);

  assign K0 = 1'b1;
endmodule
