// Logisim project maquina-lavar.circ as structural Verilog: 7 circuits, main circuit main
module main (
  input  SC,
  input  SV,
  output Motor_1,
  output Motor_0,
  output Bomba_esgotamento,
  output \Válvula_admissão 
);

  wire and_1_out, and_2_out, button_1_out, clock_1_out, Cont__2m, Cont__20s, funcao_simpl_1_ena, j_k_ff_1_q,
       j_k_ff_1_qn, j_k_ff_2_q, j_k_ff_3_q, maq_estado_simpl_1_j0, maq_estado_simpl_1_j1,
       maq_estado_simpl_1_k0, maq_estado_simpl_1_k1;

  Clock clock_1 (.out(clock_1_out));
  Button button_1 (.out(button_1_out));
  and and_1 (and_1_out, clock_1_out, j_k_ff_1_q);
  J_K_Flip_Flop j_k_ff_1 (
    .J(button_1_out), .clk(clock_1_out), .K(1'b0), .Q(j_k_ff_1_q), .Qn(j_k_ff_1_qn), .reset(and_2_out));  // open: preset, en
  Contador Cont (
    .CLK(and_1_out), .ENA(funcao_simpl_1_ena), .BTN(button_1_out), ._20s(Cont__20s), ._2m(Cont__2m));  // open: seg, _10s
  maq_estado_simpl maq_estado_simpl_1 (
    .E1(j_k_ff_2_q), .E0(j_k_ff_3_q), .SC(SC), .SV(SV), .Cont_2M(Cont__2m), .J1(maq_estado_simpl_1_j1),
    .K1(maq_estado_simpl_1_k1), .J0(maq_estado_simpl_1_j0), .K0(maq_estado_simpl_1_k0));
  J_K_Flip_Flop j_k_ff_2 (
    .J(maq_estado_simpl_1_j1), .clk(and_1_out), .K(maq_estado_simpl_1_k1), .Q(j_k_ff_2_q), .reset(j_k_ff_1_qn));  // open: Qn, preset, en
  funcao_simpl funcao_simpl_1 (
    .E1(j_k_ff_2_q), .E0(j_k_ff_3_q), .C20S(Cont__20s), .M1(Motor_1), .M0(Motor_0), .B(Bomba_esgotamento),
    .V(\Válvula_admissão ), .ENA(funcao_simpl_1_ena));
  J_K_Flip_Flop j_k_ff_3 (
    .J(maq_estado_simpl_1_j0), .clk(and_1_out), .K(maq_estado_simpl_1_k0), .Q(j_k_ff_3_q), .reset(j_k_ff_1_qn));  // open: Qn, preset, en
  and and_2 (and_2_out, j_k_ff_2_q, j_k_ff_3_q, SV);
endmodule

module Contador (
  input  CLK,
  input  ENA,
  input  BTN,
  output _10s,
  output [3:0] seg,
  output _20s,
  output _2m
);

  wire and_2_out, j_k_ff_1_q, maquina_de_estado_d_1_s0, maquina_de_estado_d_1_s1, maquina_de_estado_d_1_s2,
       maquina_de_estado_d_1_s3, not_1_out, shift_register_1_q0, shift_register_1_q1, shift_register_1_q2;

  not not_1 (not_1_out, ENA);
  maquina_de_estado_D maquina_de_estado_d_1 (
    .S(1'b1), .E3(seg[3]), .E2(seg[2]), .E1(seg[1]), .E0(seg[0]), .S3(maquina_de_estado_d_1_s3),
    .S2(maquina_de_estado_d_1_s2), .S1(maquina_de_estado_d_1_s1), .S0(maquina_de_estado_d_1_s0));
  D_Flip_Flop d_ff_1 (.clk(CLK), .D(maquina_de_estado_d_1_s3), .Q(seg[3]), .reset(not_1_out));  // open: Qn, preset, en
  D_Flip_Flop d_ff_2 (.clk(CLK), .D(maquina_de_estado_d_1_s2), .Q(seg[2]), .reset(not_1_out));  // open: Qn, preset, en
  D_Flip_Flop d_ff_3 (.clk(CLK), .D(maquina_de_estado_d_1_s1), .Q(seg[1]), .reset(not_1_out));  // open: Qn, preset, en
  D_Flip_Flop d_ff_4 (.clk(CLK), .D(maquina_de_estado_d_1_s0), .Q(seg[0]), .reset(not_1_out));  // open: Qn, preset, en
  and and_1 (_10s, seg[0], ~seg[1], ~seg[2], seg[3]);  // AND_Gate
  J_K_Flip_Flop j_k_ff_1 (.J(1'b1), .clk(_10s), .K(1'b1), .Q(j_k_ff_1_q));  // open: Qn, preset, en, reset
  J_K_Flip_Flop j_k_ff_2 (.J(1'b1), .clk(j_k_ff_1_q), .K(1'b1), .Q(_20s));  // open: Qn, preset, en, reset
  Shift_Register shift_register_1 (
    .in(_20s), .clk(_20s), .clr(not_1_out), .q0(shift_register_1_q0), .q1(shift_register_1_q1),
    .q2(shift_register_1_q2));  // open: shift, out, load, d0, d1, d2, d3, q3, d4, q4, d5, q5, d6, q6, d7, q7
  and and_2 (and_2_out, shift_register_1_q0, shift_register_1_q1, shift_register_1_q2);
  J_K_Flip_Flop j_k_ff_3 (.J(and_2_out), .clk(and_2_out), .K(and_2_out), .Q(_2m), .reset(BTN));  // open: Qn, preset, en
endmodule

module Maquina_de_estado (
  input  E1,
  input  E0,
  input  SC,
  input  SV,
  input  Cont_2M,
  output S1,
  output S0
);

  wire and_1_out, and_2_out, and_3_out, and_4_out, and_5_out, and_6_out, and_7_out, and_8_out, and_9_out,
       and_10_out, and_11_out, and_12_out, and_13_out, and_14_out, and_15_out, and_16_out, and_17_out,
       and_18_out, and_19_out, and_20_out, and_21_out, and_22_out, not_1_out, not_2_out, not_3_out,
       not_4_out, not_5_out, not_6_out, not_7_out, not_8_out, not_9_out, not_10_out, not_11_out, not_12_out,
       not_13_out, not_14_out, or_1_out, or_2_out, or_3_out, or_4_out, or_5_out, or_6_out, or_7_out, or_8_out;

  not not_1 (not_1_out, SV);
  not not_2 (not_2_out, Cont_2M);
  not not_3 (not_3_out, E1);
  not not_4 (not_4_out, SC);
  not not_5 (not_5_out, Cont_2M);
  not not_6 (not_6_out, E1);
  not not_7 (not_7_out, E1);
  not not_8 (not_8_out, E0);
  and and_1 (and_1_out, E0, SC);
  and and_2 (and_2_out, not_1_out, not_2_out);
  not not_9 (not_9_out, E0);
  and and_3 (and_3_out, not_3_out, not_4_out);
  and and_4 (and_4_out, SV, not_5_out);
  and and_5 (and_5_out, not_6_out, E0);
  not not_10 (not_10_out, SC);
  and and_6 (and_6_out, not_7_out, E0);
  and and_7 (and_7_out, E0, SV);
  not not_11 (not_11_out, Cont_2M);
  and and_8 (and_8_out, E1, not_8_out);
  and and_9 (and_9_out, E1, E0);
  not not_12 (not_12_out, SV);
  and and_10 (and_10_out, and_1_out, and_2_out);
  or or_1 (or_1_out, and_10_out, and_11_out);
  and and_11 (and_11_out, E1, not_9_out);
  and and_12 (and_12_out, E1, not_13_out);
  not not_13 (not_13_out, SV);
  and and_13 (and_13_out, E1, not_14_out);
  not not_14 (not_14_out, Cont_2M);
  and and_14 (and_14_out, E1, SC);
  and and_15 (and_15_out, and_3_out, and_4_out);
  or or_2 (or_2_out, and_15_out, and_16_out);
  and and_16 (and_16_out, and_5_out, not_10_out);
  and and_17 (and_17_out, and_6_out, Cont_2M);
  or or_3 (or_3_out, and_17_out, and_18_out);
  and and_18 (and_18_out, and_7_out, not_11_out);
  and and_19 (and_19_out, and_8_out, Cont_2M);
  or or_4 (or_4_out, and_19_out, and_20_out);
  and and_20 (and_20_out, and_9_out, not_12_out);
  and and_21 (and_21_out, E1, E0);
  and and_22 (and_22_out, and_21_out, SC);
  or or_5 (or_5_out, or_1_out, and_12_out);
  or or_6 (or_6_out, and_13_out, and_14_out);
  or or_7 (or_7_out, or_2_out, or_3_out);
  or or_8 (or_8_out, or_4_out, and_22_out);
  or or_9 (S1, or_5_out, or_6_out);
  or or_10 (S0, or_7_out, or_8_out);
endmodule

module funcao (
  input  E1,
  input  E0,
  input  C20S,
  output M1,
  output M0,
  output B,
  output V,
  output ENA
);

  wire and_2_out, and_3_out, not_1_out, not_2_out, not_3_out, not_4_out, not_5_out;

  not not_1 (not_1_out, E0);
  not not_2 (not_2_out, E0);
  and and_1 (B, E1, E0);
  not not_3 (not_3_out, E1);
  not not_4 (not_4_out, E0);
  and and_2 (and_2_out, E1, not_1_out);
  and and_3 (and_3_out, E1, not_2_out);
  not not_5 (not_5_out, C20S);
  and and_4 (V, not_3_out, E0);
  and and_5 (ENA, E1, not_4_out);
  and and_6 (M1, and_2_out, C20S);
  and and_7 (M0, and_3_out, not_5_out);
endmodule

module Maquina_de_estadoJK (
  input  E1,
  input  E0,
  input  SC,
  input  SV,
  input  Cont_2M,
  output J1,
  output K1,
  output J0,
  output K0
);

  wire and_1_out, and_2_out, and_3_out, and_5_out, and_6_out, and_7_out, and_8_out, and_9_out, and_11_out,
       and_12_out, and_13_out, and_14_out, not_1_out, not_2_out, not_3_out, not_4_out, not_5_out, not_6_out,
       not_7_out, not_8_out;

  not not_1 (not_1_out, SV);
  not not_2 (not_2_out, Cont_2M);
  and and_1 (and_1_out, E0, SV);
  not not_3 (not_3_out, E1);
  not not_4 (not_4_out, SC);
  not not_5 (not_5_out, Cont_2M);
  not not_6 (not_6_out, E1);
  not not_7 (not_7_out, SV);
  not not_8 (not_8_out, Cont_2M);
  and and_2 (and_2_out, E0, SC);
  and and_3 (and_3_out, not_1_out, not_2_out);
  and and_4 (K1, and_1_out, Cont_2M);
  and and_5 (and_5_out, not_3_out, not_4_out);
  and and_6 (and_6_out, SV, not_5_out);
  and and_7 (and_7_out, not_6_out, SC);
  and and_8 (and_8_out, not_7_out, not_8_out);
  and and_9 (and_9_out, E1, SV);
  and and_10 (J1, and_2_out, and_3_out);
  and and_11 (and_11_out, and_5_out, and_6_out);
  or or_1 (J0, and_11_out, and_12_out);
  and and_12 (and_12_out, E1, Cont_2M);
  and and_13 (and_13_out, and_7_out, and_8_out);
  or or_2 (K0, and_13_out, and_14_out);
  and and_14 (and_14_out, and_9_out, Cont_2M);
endmodule

module maq_estado_simpl (
  input  E1,
  input  E0,
  input  SC,
  input  SV,
  input  Cont_2M,
  output J1,
  output K1,
  output J0,
  output K0
);

  wire a_out, and_1_out, and_2_out, and_3_out, c_out, not_3_out, not_4_out, not_5_out, not_6_out;

  // NOT_Gate not_1 has open pins: in=E1, out=open
  // NOT_Gate not_2 has open pins: in=E0, out=open
  not not_3 (not_3_out, SC);
  not not_4 (not_4_out, SV);
  not not_5 (not_5_out, Cont_2M);
  and a (a_out, E1, Cont_2M);
  not not_6 (not_6_out, a_out);
  and c (c_out, SC, not_4_out);
  and and_1 (and_1_out, not_6_out, not_3_out, SV);
  and and_2 (and_2_out, not_6_out, c_out);
  and and_3 (and_3_out, a_out, SV);
  and and_4 (J1, E0, c_out, not_5_out);
  and and_5 (K1, E0, SV, Cont_2M);
  or or_1 (J0, and_1_out, a_out);
  or or_2 (K0, and_2_out, and_3_out);
endmodule

module funcao_simpl (
  input  E1,
  input  E0,
  input  C20S,
  output M1,
  output M0,
  output B,
  output V,
  output ENA
);

  wire not_1_out, not_2_out, not_3_out;

  not not_1 (not_1_out, E1);
  not not_2 (not_2_out, E0);
  not not_3 (not_3_out, C20S);
  and a (ENA, E1, not_2_out);
  and and_1 (B, E1, E0);
  and and_2 (V, not_1_out, E0);
  and and_3 (M1, ENA, C20S);
  and and_4 (M0, ENA, not_3_out);
endmodule
