// Logisim project deslocador.circ as structural Verilog: 2 circuits, main circuit main
module main (
  input  [7:0] IN,
  input  [1:0] D,
  output [7:0] OUT
);

  wire [7:0] deslocador_1_out_17;

  deslocador deslocador_1 (
    .in_9(D[0]), .in_1(IN[7]), .in_2(IN[6]), .in_3(IN[5]), .in_4(IN[4]), .in_5(IN[3]), .in_6(IN[2]),
    .in_7(IN[1]), .in_8(IN[0]), .out_10(deslocador_1_out_17[7]), .out_11(deslocador_1_out_17[6]),
    .out_12(deslocador_1_out_17[5]), .out_13(deslocador_1_out_17[4]), .out_14(deslocador_1_out_17[3]),
    .out_15(deslocador_1_out_17[2]), .out_16(deslocador_1_out_17[1]), .out_17(deslocador_1_out_17[0]));
  Multiplexer #(.width(8), .enable("false")) multiplexer_1 (.in0(IN), .in1(deslocador_1_out_17), .out(OUT), .sel(D[1]));
endmodule

module deslocador (
  input  in_1,
  input  in_2,
  input  in_3,
  input  in_4,
  input  in_5,
  input  in_6,
  input  in_7,
  input  in_8,
  input  in_9,
  output out_10,
  output out_11,
  output out_12,
  output out_13,
  output out_14,
  output out_15,
  output out_16,
  output out_17
);

  wire and_1_out, and_3_out, and_4_out, and_5_out, and_6_out, and_7_out, and_8_out, and_9_out, and_10_out,
       and_11_out, and_12_out, and_13_out, not_1_out;

  not not_1 (not_1_out, in_9);
  and and_1 (and_1_out, in_1, in_9);
  and and_2 (out_10, not_1_out, in_2);
  and and_3 (and_3_out, in_2, in_9);
  or or_1 (out_11, and_1_out, and_4_out);
  and and_4 (and_4_out, not_1_out, in_3);
  and and_5 (and_5_out, in_3, in_9);
  or or_2 (out_12, and_3_out, and_6_out);
  and and_6 (and_6_out, not_1_out, in_4);
  and and_7 (and_7_out, in_4, in_9);
  or or_3 (out_13, and_5_out, and_8_out);
  and and_8 (and_8_out, not_1_out, in_5);
  or or_4 (out_14, and_7_out, and_9_out);
  and and_9 (and_9_out, not_1_out, in_6);
  and and_10 (and_10_out, in_5, in_9);
  or or_5 (out_15, and_10_out, and_12_out);
  and and_11 (and_11_out, in_6, in_9);
  and and_12 (and_12_out, not_1_out, in_7);
  and and_13 (and_13_out, not_1_out, in_8);
  and and_14 (out_17, in_7, in_9);
  or or_6 (out_16, and_11_out, and_13_out);
endmodule
