// Logisim project multiplicador.circ as structural Verilog: 2 circuits, main circuit main
module main (
  input  X1,
  input  X0,
  input  Y1,
  input  Y0,
  output Z3,
  output Z2,
  output Z1,
  output Z0,
  output Z0_2,
  output Z0_3,
  output Z0_4
);

  wire [1:1] multiplier_1_cout;

  multi multi_1 (.X1(X1), .X0(X0), .Y1(Y1), .Y0(Y0), .Z3(Z3), .Z2(Z2), .Z1(Z1), .Z0(Z0));
  Multiplier #(.width(2)) multiplier_1 (
    .a({X0, X1}), .b({Y0, Y1}), .out({Z0_3, Z0_4}), .cout({multiplier_1_cout[1], Z0_2}));  // open: cin
endmodule

module multi (
  input  X1,
  input  X0,
  input  Y1,
  input  Y0,
  output Z3,
  output Z2,
  output Z1,
  output Z0
);

  wire and_3_out, and_4_out, and_5_out, and_6_out, and_7_out, and_8_out, not_1_out, not_2_out, not_3_out,
       not_4_out, not_5_out, not_6_out;

  and and_1 (Z3, X1, X0, Y1, Y0);
  not not_1 (not_1_out, X0);
  not not_2 (not_2_out, Y0);
  not not_3 (not_3_out, X1);
  not not_4 (not_4_out, Y0);
  not not_5 (not_5_out, X0);
  not not_6 (not_6_out, Y1);
  and and_2 (Z0, X0, Y0);
  and and_3 (and_3_out, X1, not_1_out, Y1);
  and and_4 (and_4_out, X1, Y1, not_2_out);
  and and_5 (and_5_out, not_3_out, X0, Y1);
  and and_6 (and_6_out, X0, Y1, not_4_out);
  and and_7 (and_7_out, X1, not_5_out, Y0);
  and and_8 (and_8_out, X1, not_6_out, Y0);
  or or_1 (Z2, and_3_out, and_4_out);
  or or_2 (Z1, and_5_out, and_6_out, and_7_out, and_8_out);
endmodule
