// Logisim project Exercícios - Lista 4.circ as structural Verilog: 23 circuits, main circuit P2575
module main (
  input  in_1,
  input  in_2
);

  wire and_1_out, and_2_out, and_3_out, and_4_out, and_5_out, and_6_out, and_7_out, and_8_out, clock_1_out,
       j_k_ff_1_q, j_k_ff_2_q, j_k_ff_3_q, j_k_ff_4_q, nor_1_out, not_1_out, not_2_out, not_3_out, not_4_out,
       not_5_out, not_6_out, not_7_out, not_8_out, or_1_out, or_2_out, shift_register_1_q0,
       shift_register_1_q1, shift_register_1_q2, shift_register_1_q3, shift_register_1_q4,
       shift_register_1_q5, shift_register_1_q6, shift_register_1_q7;

  and and_1 (and_1_out, ~in_1, ~in_2);  // AND_Gate
  and and_2 (and_2_out, in_1, ~in_2);  // AND_Gate
  and and_3 (and_3_out, ~in_1, in_2);  // AND_Gate
  and and_4 (and_4_out, in_1, in_2);
  Clock clock_1 (.out(clock_1_out));
  J_K_Flip_Flop j_k_ff_1 (.J(1'b1), .clk(clock_1_out), .K(1'b1), .Q(j_k_ff_1_q));  // open: Qn, preset, en, reset
  and and_5 (and_5_out, j_k_ff_2_q, and_1_out, j_k_ff_1_q);
  nor nor_1 (nor_1_out, j_k_ff_4_q, j_k_ff_3_q, j_k_ff_2_q, j_k_ff_1_q);
  or or_1 (or_1_out, j_k_ff_4_q, j_k_ff_3_q, j_k_ff_2_q);
  J_K_Flip_Flop j_k_ff_2 (.J(1'b1), .clk(j_k_ff_1_q), .K(1'b1), .Q(j_k_ff_2_q));  // open: Qn, preset, en, reset
  _7_Segment_Display u_7_segment_display_1 (.a(shift_register_1_q0), .d(not_2_out));  // open: g, f, b, e, c, dp
  and and_6 (and_6_out, nor_1_out, and_2_out);
  and and_7 (and_7_out, j_k_ff_4_q, j_k_ff_3_q, j_k_ff_2_q, j_k_ff_1_q, and_3_out);
  and and_8 (and_8_out, or_1_out, and_4_out);
  J_K_Flip_Flop j_k_ff_3 (.J(1'b1), .clk(j_k_ff_2_q), .K(1'b1), .Q(j_k_ff_3_q));  // open: Qn, preset, en, reset
  _7_Segment_Display u_7_segment_display_2 (.a(shift_register_1_q1), .d(not_1_out));  // open: g, f, b, e, c, dp
  _7_Segment_Display u_7_segment_display_3 (.a(shift_register_1_q2), .d(not_8_out));  // open: g, f, b, e, c, dp
  _7_Segment_Display u_7_segment_display_4 (.a(shift_register_1_q4), .d(not_6_out));  // open: g, f, b, e, c, dp
  _7_Segment_Display u_7_segment_display_5 (.a(shift_register_1_q3), .d(not_7_out));  // open: g, f, b, e, c, dp
  or or_2 (or_2_out, and_5_out, and_6_out, and_7_out, and_8_out);
  J_K_Flip_Flop j_k_ff_4 (.J(1'b1), .clk(j_k_ff_3_q), .K(1'b1), .Q(j_k_ff_4_q));  // open: Qn, preset, en, reset
  _7_Segment_Display u_7_segment_display_6 (.a(shift_register_1_q6), .d(not_4_out));  // open: g, f, b, e, c, dp
  _7_Segment_Display u_7_segment_display_7 (.a(shift_register_1_q5), .d(not_5_out));  // open: g, f, b, e, c, dp
  Shift_Register shift_register_1 (
    .in(or_2_out), .clk(clock_1_out), .q0(shift_register_1_q0), .q1(shift_register_1_q1),
    .q2(shift_register_1_q2), .q3(shift_register_1_q3), .q4(shift_register_1_q4), .q5(shift_register_1_q5),
    .q6(shift_register_1_q6), .q7(shift_register_1_q7));  // open: shift, out, load, clr, d0, d1, d2, d3, d4, d5, d6, d7
  _7_Segment_Display u_7_segment_display_8 (.a(shift_register_1_q7), .d(not_3_out));  // open: g, f, b, e, c, dp
  not not_1 (not_1_out, shift_register_1_q1);
  not not_2 (not_2_out, shift_register_1_q0);
  not not_3 (not_3_out, shift_register_1_q7);
  not not_4 (not_4_out, shift_register_1_q6);
  not not_5 (not_5_out, shift_register_1_q5);
  not not_6 (not_6_out, shift_register_1_q4);
  not not_7 (not_7_out, shift_register_1_q3);
  not not_8 (not_8_out, shift_register_1_q2);
endmodule

module P2575 (
);

  wire and_1_out, and_2_out, clock_1_out, clock_2_out, j_k_ff_1_q, j_k_ff_1_qn, j_k_ff_2_q, j_k_ff_3_q,
       j_k_ff_3_qn, j_k_ff_4_q, j_k_ff_4_qn, j_k_ff_5_q, j_k_ff_5_qn, j_k_ff_6_q, j_k_ff_6_qn, j_k_ff_7_q,
       shift_register_2_q0, shift_register_2_q1, shift_register_2_q2, shift_register_2_q3,
       shift_register_2_q4, shift_register_2_q5, shift_register_2_q6;

  Clock clock_1 (.out(clock_1_out));
  Clock clock_2 (.out(clock_2_out));
  J_K_Flip_Flop j_k_ff_1 (
    .J(1'b1), .clk(clock_1_out), .K(1'b1), .Q(j_k_ff_1_q), .Qn(j_k_ff_1_qn));  // open: preset, en, reset
  J_K_Flip_Flop j_k_ff_2 (.J(1'b1), .clk(j_k_ff_1_qn), .K(1'b1), .Q(j_k_ff_2_q));  // open: Qn, preset, en, reset
  J_K_Flip_Flop j_k_ff_3 (
    .J(1'b1), .clk(clock_2_out), .K(1'b1), .Q(j_k_ff_3_q), .Qn(j_k_ff_3_qn));  // open: preset, en, reset
  Shift_Register #(.length(32)) shift_register_1 (
    .in(and_2_out), .clk(clock_2_out));  // open: shift, out, load, clr, d0, q0, d1, q1, d2, q2, d3, q3, d4, q4, d5, q5, d6, q6, d7, q7, d8, q8, d9, q9, d10, q10, d11, q11, d12, q12, d13, q13, d14, q14, d15, q15, d16, q16, d17, q17, d18, q18, d19, q19, d20, q20, d21, q21, d22, q22, d23, q23, d24, q24, d25, q25, d26, q26, d27, q27, d28, q28, d29, q29, d30, q30, d31, q31
  and and_1 (and_1_out, j_k_ff_1_q, j_k_ff_2_q);
  J_K_Flip_Flop j_k_ff_4 (
    .J(1'b1), .clk(j_k_ff_3_qn), .K(1'b1), .Q(j_k_ff_4_q), .Qn(j_k_ff_4_qn));  // open: preset, en, reset
  Shift_Register shift_register_2 (
    .in(and_1_out), .clk(clock_1_out), .q0(shift_register_2_q0), .q1(shift_register_2_q1),
    .q2(shift_register_2_q2), .q3(shift_register_2_q3), .q4(shift_register_2_q4), .q5(shift_register_2_q5),
    .q6(shift_register_2_q6));  // open: shift, out, load, clr, d0, d1, d2, d3, d4, d5, d6, d7, q7
  LED led_1 (.in(shift_register_2_q1));
  LED led_2 (.in(shift_register_2_q2));
  LED led_3 (.in(shift_register_2_q0));
  LED led_4 (.in(shift_register_2_q3));
  LED led_5 (.in(shift_register_2_q5));
  LED led_6 (.in(shift_register_2_q4));
  LED led_7 (.in(shift_register_2_q6));
  J_K_Flip_Flop j_k_ff_5 (
    .J(1'b1), .clk(j_k_ff_4_qn), .K(1'b1), .Q(j_k_ff_5_q), .Qn(j_k_ff_5_qn));  // open: preset, en, reset
  J_K_Flip_Flop j_k_ff_6 (
    .J(1'b1), .clk(j_k_ff_5_qn), .K(1'b1), .Q(j_k_ff_6_q), .Qn(j_k_ff_6_qn));  // open: preset, en, reset
  J_K_Flip_Flop j_k_ff_7 (.J(1'b1), .clk(j_k_ff_6_qn), .K(1'b1), .Q(j_k_ff_7_q));  // open: Qn, preset, en, reset
  and and_2 (and_2_out, j_k_ff_7_q, j_k_ff_6_q, j_k_ff_5_q, j_k_ff_4_q, j_k_ff_3_q);

  // Notes on the sheet:
  //   7,8125 Hz
endmodule

module CntM12 (
);

  wire and_1_out, clock_1_out, dech7s_1_a_2, dech7s_1_b_2, dech7s_1_c_2, dech7s_1_d_2, dech7s_1_e,
       dech7s_1_f, dech7s_1_g, j_k_ff_1_q, j_k_ff_1_qn, j_k_ff_2_q, j_k_ff_2_qn, j_k_ff_3_q, j_k_ff_3_qn,
       j_k_ff_4_q;

  Clock clock_1 (.out(clock_1_out));
  J_K_Flip_Flop j_k_ff_1 (
    .J(1'b1), .clk(clock_1_out), .K(1'b1), .Q(j_k_ff_1_q), .Qn(j_k_ff_1_qn), .reset(and_1_out));  // open: preset, en
  J_K_Flip_Flop j_k_ff_2 (
    .J(1'b1), .clk(j_k_ff_1_qn), .K(1'b1), .Q(j_k_ff_2_q), .Qn(j_k_ff_2_qn), .reset(and_1_out));  // open: preset, en
  J_K_Flip_Flop j_k_ff_3 (
    .J(1'b1), .clk(j_k_ff_2_qn), .K(1'b1), .Q(j_k_ff_3_q), .Qn(j_k_ff_3_qn), .reset(and_1_out));  // open: preset, en
  DecH7S dech7s_1 (
    .A(j_k_ff_4_q), .B(j_k_ff_3_q), .C(j_k_ff_2_q), .D(j_k_ff_1_q), .a_2(dech7s_1_a_2), .b_2(dech7s_1_b_2),
    .c_2(dech7s_1_c_2), .d_2(dech7s_1_d_2), .e(dech7s_1_e), .f(dech7s_1_f), .g(dech7s_1_g));
  J_K_Flip_Flop j_k_ff_4 (
    .J(1'b1), .clk(j_k_ff_3_qn), .K(1'b1), .Q(j_k_ff_4_q), .reset(and_1_out));  // open: Qn, preset, en
  _7_Segment_Display u_7_segment_display_1 (
    .g(dech7s_1_g), .f(dech7s_1_f), .a(dech7s_1_a_2), .b(dech7s_1_b_2), .e(dech7s_1_e), .d(dech7s_1_d_2),
    .c(dech7s_1_c_2));  // open: dp
  and and_1 (and_1_out, ~j_k_ff_1_q, ~j_k_ff_2_q, j_k_ff_3_q, j_k_ff_4_q);  // AND_Gate

  // Notes on the sheet:
  //   1100b - 12d
endmodule

module CntM19 (
);

  wire and_1_out, clock_1_out, decbcd7s_1_b_2, decbcd7s_1_c_2, dech7s_1_a_2, dech7s_1_b_2, dech7s_1_c_2,
       dech7s_1_d_2, dech7s_1_e, dech7s_1_f, dech7s_1_g, j_k_ff_1_q, j_k_ff_1_qn, j_k_ff_2_q, j_k_ff_2_qn,
       j_k_ff_3_q, j_k_ff_3_qn, j_k_ff_4_q, j_k_ff_4_qn, j_k_ff_5_q, not_1_out;

  Clock clock_1 (.out(clock_1_out));
  J_K_Flip_Flop j_k_ff_1 (
    .J(1'b1), .clk(clock_1_out), .K(1'b1), .Q(j_k_ff_1_q), .Qn(j_k_ff_1_qn), .reset(and_1_out));  // open: preset, en
  not not_1 (not_1_out, j_k_ff_5_q);
  J_K_Flip_Flop j_k_ff_2 (
    .J(1'b1), .clk(j_k_ff_1_qn), .K(1'b1), .Q(j_k_ff_2_q), .Qn(j_k_ff_2_qn), .reset(and_1_out));  // open: preset, en
  DecBCD7S decbcd7s_1 (
    .A(not_1_out), .B(not_1_out), .C(not_1_out), .D(j_k_ff_5_q), .b_2(decbcd7s_1_b_2), .c_2(decbcd7s_1_c_2));  // open: a_2, d_2, e, f, g
  J_K_Flip_Flop j_k_ff_3 (
    .J(1'b1), .clk(j_k_ff_2_qn), .K(1'b1), .Q(j_k_ff_3_q), .Qn(j_k_ff_3_qn), .reset(and_1_out));  // open: preset, en
  DecH7S dech7s_1 (
    .A(j_k_ff_4_q), .B(j_k_ff_3_q), .C(j_k_ff_2_q), .D(j_k_ff_1_q), .a_2(dech7s_1_a_2), .b_2(dech7s_1_b_2),
    .c_2(dech7s_1_c_2), .d_2(dech7s_1_d_2), .e(dech7s_1_e), .f(dech7s_1_f), .g(dech7s_1_g));
  J_K_Flip_Flop j_k_ff_4 (
    .J(1'b1), .clk(j_k_ff_3_qn), .K(1'b1), .Q(j_k_ff_4_q), .Qn(j_k_ff_4_qn), .reset(and_1_out));  // open: preset, en
  J_K_Flip_Flop j_k_ff_5 (
    .J(1'b1), .clk(j_k_ff_4_qn), .K(1'b1), .Q(j_k_ff_5_q), .reset(and_1_out));  // open: Qn, preset, en
  _7_Segment_Display u_7_segment_display_1 (.b(decbcd7s_1_b_2), .c(decbcd7s_1_c_2));  // open: g, f, a, e, d, dp
  _7_Segment_Display u_7_segment_display_2 (
    .g(dech7s_1_g), .f(dech7s_1_f), .a(dech7s_1_a_2), .b(dech7s_1_b_2), .e(dech7s_1_e), .d(dech7s_1_d_2),
    .c(dech7s_1_c_2));  // open: dp
  and and_1 (and_1_out, j_k_ff_1_q, j_k_ff_2_q, ~j_k_ff_3_q, ~j_k_ff_4_q, j_k_ff_5_q);  // AND_Gate

  // Notes on the sheet:
  //   10011b - 19d
endmodule

module Timer30 (
  output out_1
);

  wire and_1_out, base1s_1__1_hz, j_k_ff_1_q, j_k_ff_2_q, j_k_ff_3_q, j_k_ff_4_q, j_k_ff_5_q, Load_out,
       or_1_out;
  wire [2:0] dech7s_1_c_2, dech7s_2_c_2;
  wire [3:0] dech7s_1_b_2, dech7s_2_b_2;

  Base1s base1s_1 (._1_Hz(base1s_1__1_hz));
  Button Load (.out(Load_out));
  and and_1 (and_1_out, base1s_1__1_hz, or_1_out);
  J_K_Flip_Flop j_k_ff_1 (
    .J(1'b1), .clk(and_1_out), .K(1'b1), .Q(j_k_ff_1_q), .reset(Load_out));  // open: Qn, preset, en
  J_K_Flip_Flop j_k_ff_2 (
    .J(1'b1), .clk(j_k_ff_1_q), .K(1'b1), .Q(j_k_ff_2_q), .preset(Load_out));  // open: Qn, en, reset
  DecH7S dech7s_1 (
    .A(1'b0), .B(1'b0), .C(1'b0), .D(j_k_ff_5_q), .a_2(dech7s_1_b_2[1]), .b_2(dech7s_1_b_2[0]),
    .c_2(dech7s_1_c_2[0]), .d_2(dech7s_1_c_2[1]), .e(dech7s_1_c_2[2]), .f(dech7s_1_b_2[2]),
    .g(dech7s_1_b_2[3]));
  J_K_Flip_Flop j_k_ff_3 (
    .J(1'b1), .clk(j_k_ff_2_q), .K(1'b1), .Q(j_k_ff_3_q), .preset(Load_out));  // open: Qn, en, reset
  DecH7S dech7s_2 (
    .A(j_k_ff_4_q), .B(j_k_ff_3_q), .C(j_k_ff_2_q), .D(j_k_ff_1_q), .a_2(dech7s_2_b_2[1]),
    .b_2(dech7s_2_b_2[0]), .c_2(dech7s_2_c_2[0]), .d_2(dech7s_2_c_2[1]), .e(dech7s_2_c_2[2]),
    .f(dech7s_2_b_2[2]), .g(dech7s_2_b_2[3]));
  J_K_Flip_Flop j_k_ff_4 (
    .J(1'b1), .clk(j_k_ff_3_q), .K(1'b1), .Q(j_k_ff_4_q), .preset(Load_out));  // open: Qn, en, reset
  _7_Segment_Display u_7_segment_display_1 (
    .g(dech7s_2_b_2[3]), .f(dech7s_2_b_2[2]), .a(dech7s_2_b_2[1]), .b(dech7s_2_b_2[0]), .e(dech7s_2_c_2[2]),
    .d(dech7s_2_c_2[1]), .c(dech7s_2_c_2[0]));  // open: dp
  _7_Segment_Display u_7_segment_display_2 (
    .g(dech7s_1_b_2[3]), .f(dech7s_1_b_2[2]), .a(dech7s_1_b_2[1]), .b(dech7s_1_b_2[0]), .e(dech7s_1_c_2[2]),
    .d(dech7s_1_c_2[1]), .c(dech7s_1_c_2[0]));  // open: dp
  J_K_Flip_Flop j_k_ff_5 (
    .J(1'b1), .clk(j_k_ff_4_q), .K(1'b1), .Q(j_k_ff_5_q), .preset(Load_out));  // open: Qn, en, reset
  or or_1 (or_1_out, j_k_ff_1_q, j_k_ff_2_q, j_k_ff_3_q, j_k_ff_4_q, j_k_ff_5_q);
  not not_1 (out_1, or_1_out);

  // Notes on the sheet:
  //   1Eh -> 30d
endmodule

module TimerCarga (
  input  in_1,
  input  in_2,
  input  in_3,
  input  in_4,
  input  in_5,
  input  in_6,
  input  in_7,
  input  in_8,
  input  in_9,
  input  in_10,
  output out_11
);

  wire and_1_out, and_2_out, and_3_out, base1s_1__1_hz, deccarga_1_p0, deccarga_1_p1, deccarga_1_p2,
       deccarga_1_p3, deccarga_1_p4, deccarga_1_p5, deccarga_1_p6, deccarga_1_p7, deccarga_1_p8,
       deccarga_1_p9, deccarga_2_p0, deccarga_2_p1, deccarga_2_p2, deccarga_2_p3, deccarga_2_p4,
       deccarga_2_p5, deccarga_2_p6, deccarga_2_p7, deccarga_2_p8, deccarga_2_p9, j_k_ff_1_q, j_k_ff_2_q,
       j_k_ff_3_q, j_k_ff_4_q, j_k_ff_5_q, j_k_ff_6_q, j_k_ff_7_q, j_k_ff_8_q, j_k_ff_9_q, j_k_ff_10_q,
       Load_out, not_1_out, or_1_out, or_2_out, or_3_out, or_4_out, or_5_out, or_6_out, or_7_out, or_8_out,
       or_9_out, or_10_out, or_11_out;
  wire [2:0] decbcd7s_1_c_2, decbcd7s_2_c_2, decbcd7s_3_c_2;
  wire [3:0] decbcd7s_1_b_2, decbcd7s_2_b_2, decbcd7s_3_b_2;

  not not_1 (not_1_out, 1'b0);
  Base1s base1s_1 (._1_Hz(base1s_1__1_hz));
  Button Load (.out(Load_out));
  DecBCD7S decbcd7s_1 (
    .A(1'b0), .B(1'b0), .C(j_k_ff_10_q), .D(j_k_ff_9_q), .a_2(decbcd7s_1_b_2[1]), .b_2(decbcd7s_1_b_2[0]),
    .c_2(decbcd7s_1_c_2[0]), .d_2(decbcd7s_1_c_2[1]), .e(decbcd7s_1_c_2[2]), .f(decbcd7s_1_b_2[2]),
    .g(decbcd7s_1_b_2[3]));
  and and_1 (and_1_out, j_k_ff_1_q, j_k_ff_2_q, j_k_ff_3_q, j_k_ff_4_q, ~base1s_1__1_hz);  // AND_Gate
  and and_2 (and_2_out, j_k_ff_5_q, j_k_ff_6_q, j_k_ff_7_q, j_k_ff_8_q, ~base1s_1__1_hz);  // AND_Gate
  and and_3 (and_3_out, base1s_1__1_hz, or_11_out);
  or or_1 (or_1_out, and_1_out, deccarga_1_p0);
  DecCarga deccarga_1 (
    .D9(in_10), .D8(in_9), .D7(in_8), .D6(in_7), .D5(in_6), .D4(in_5), .D3(in_4), .D2(in_3), .D1(in_2),
    .D0(in_1), .B__I(1'b0), .Load(Load_out), .P9(deccarga_1_p9), .P8(deccarga_1_p8), .P7(deccarga_1_p7),
    .P6(deccarga_1_p6), .P5(deccarga_1_p5), .P4(deccarga_1_p4), .P3(deccarga_1_p3), .P2(deccarga_1_p2),
    .P1(deccarga_1_p1), .P0(deccarga_1_p0));
  DecCarga deccarga_2 (
    .D9(in_10), .D8(in_9), .D7(in_8), .D6(in_7), .D5(in_6), .D4(in_5), .D3(in_4), .D2(in_3), .D1(in_2),
    .D0(in_1), .B__I(not_1_out), .Load(Load_out), .P9(deccarga_2_p9), .P8(deccarga_2_p8), .P7(deccarga_2_p7),
    .P6(deccarga_2_p6), .P5(deccarga_2_p5), .P4(deccarga_2_p4), .P3(deccarga_2_p3), .P2(deccarga_2_p2),
    .P1(deccarga_2_p1), .P0(deccarga_2_p0));
  J_K_Flip_Flop j_k_ff_1 (
    .J(1'b1), .clk(and_3_out), .K(1'b1), .Q(j_k_ff_1_q), .preset(or_1_out), .reset(deccarga_2_p0));  // open: Qn, en
  DecBCD7S decbcd7s_2 (
    .A(j_k_ff_8_q), .B(j_k_ff_7_q), .C(j_k_ff_6_q), .D(j_k_ff_5_q), .a_2(decbcd7s_2_b_2[1]),
    .b_2(decbcd7s_2_b_2[0]), .c_2(decbcd7s_2_c_2[0]), .d_2(decbcd7s_2_c_2[1]), .e(decbcd7s_2_c_2[2]),
    .f(decbcd7s_2_b_2[2]), .g(decbcd7s_2_b_2[3]));
  J_K_Flip_Flop j_k_ff_2 (
    .J(1'b1), .clk(j_k_ff_1_q), .K(1'b1), .Q(j_k_ff_2_q), .preset(deccarga_1_p1), .reset(or_3_out));  // open: Qn, en
  J_K_Flip_Flop j_k_ff_3 (
    .J(1'b1), .clk(j_k_ff_2_q), .K(1'b1), .Q(j_k_ff_3_q), .preset(deccarga_1_p2), .reset(or_2_out));  // open: Qn, en
  or or_2 (or_2_out, deccarga_2_p2, and_1_out);
  or or_3 (or_3_out, deccarga_2_p1, and_1_out);
  J_K_Flip_Flop j_k_ff_4 (
    .J(1'b1), .clk(j_k_ff_3_q), .K(1'b1), .Q(j_k_ff_4_q), .preset(or_4_out), .reset(deccarga_2_p3));  // open: Qn, en
  or or_4 (or_4_out, and_1_out, deccarga_1_p3);
  DecBCD7S decbcd7s_3 (
    .A(j_k_ff_4_q), .B(j_k_ff_3_q), .C(j_k_ff_2_q), .D(j_k_ff_1_q), .a_2(decbcd7s_3_b_2[1]),
    .b_2(decbcd7s_3_b_2[0]), .c_2(decbcd7s_3_c_2[0]), .d_2(decbcd7s_3_c_2[1]), .e(decbcd7s_3_c_2[2]),
    .f(decbcd7s_3_b_2[2]), .g(decbcd7s_3_b_2[3]));
  J_K_Flip_Flop j_k_ff_5 (
    .J(1'b1), .clk(j_k_ff_4_q), .K(1'b1), .Q(j_k_ff_5_q), .preset(or_5_out), .reset(deccarga_2_p4));  // open: Qn, en
  or or_5 (or_5_out, and_2_out, deccarga_1_p4);
  J_K_Flip_Flop j_k_ff_6 (
    .J(1'b1), .clk(j_k_ff_5_q), .K(1'b1), .Q(j_k_ff_6_q), .preset(deccarga_1_p5), .reset(or_6_out));  // open: Qn, en
  or or_6 (or_6_out, deccarga_2_p5, and_2_out);
  _7_Segment_Display u_7_segment_display_1 (
    .g(decbcd7s_1_b_2[3]), .f(decbcd7s_1_b_2[2]), .a(decbcd7s_1_b_2[1]), .b(decbcd7s_1_b_2[0]),
    .e(decbcd7s_1_c_2[2]), .d(decbcd7s_1_c_2[1]), .c(decbcd7s_1_c_2[0]));  // open: dp
  J_K_Flip_Flop j_k_ff_7 (
    .J(1'b1), .clk(j_k_ff_6_q), .K(1'b1), .Q(j_k_ff_7_q), .preset(deccarga_1_p6), .reset(or_7_out));  // open: Qn, en
  or or_7 (or_7_out, deccarga_2_p6, and_2_out);
  or or_8 (or_8_out, and_2_out, deccarga_1_p7);
  _7_Segment_Display u_7_segment_display_2 (
    .g(decbcd7s_2_b_2[3]), .f(decbcd7s_2_b_2[2]), .a(decbcd7s_2_b_2[1]), .b(decbcd7s_2_b_2[0]),
    .e(decbcd7s_2_c_2[2]), .d(decbcd7s_2_c_2[1]), .c(decbcd7s_2_c_2[0]));  // open: dp
  _7_Segment_Display u_7_segment_display_3 (
    .g(decbcd7s_3_b_2[3]), .f(decbcd7s_3_b_2[2]), .a(decbcd7s_3_b_2[1]), .b(decbcd7s_3_b_2[0]),
    .e(decbcd7s_3_c_2[2]), .d(decbcd7s_3_c_2[1]), .c(decbcd7s_3_c_2[0]));  // open: dp
  J_K_Flip_Flop j_k_ff_8 (
    .J(1'b1), .clk(j_k_ff_7_q), .K(1'b1), .Q(j_k_ff_8_q), .preset(or_8_out), .reset(deccarga_2_p7));  // open: Qn, en
  J_K_Flip_Flop j_k_ff_9 (
    .J(1'b1), .clk(j_k_ff_8_q), .K(1'b1), .Q(j_k_ff_9_q), .preset(deccarga_1_p8), .reset(deccarga_2_p8));  // open: Qn, en
  or or_9 (or_9_out, j_k_ff_1_q, j_k_ff_2_q, j_k_ff_3_q, j_k_ff_4_q, j_k_ff_5_q);
  or or_10 (or_10_out, j_k_ff_6_q, j_k_ff_7_q, j_k_ff_8_q, j_k_ff_9_q, j_k_ff_10_q);
  J_K_Flip_Flop j_k_ff_10 (
    .J(1'b1), .clk(j_k_ff_9_q), .K(1'b1), .Q(j_k_ff_10_q), .preset(deccarga_1_p9), .reset(deccarga_2_p9));  // open: Qn, en
  not not_2 (out_11, or_11_out);
  or or_11 (or_11_out, or_9_out, or_10_out);
endmodule

module BoxCounter (
  input  SI,
  input  S0,
  output out_3,
  output out_4,
  output out_5,
  output out_6,
  output out_7,
  output out_8,
  output out_9,
  output out_10,
  output out_11,
  output out_12
);

  wire and_1_out, and_2_out, and_3_out, j_k_ff_1_qn, j_k_ff_2_qn, j_k_ff_3_qn, j_k_ff_4_qn, j_k_ff_5_qn,
       j_k_ff_6_qn, j_k_ff_7_qn, j_k_ff_8_qn, j_k_ff_9_qn;

  J_K_Flip_Flop j_k_ff_1 (
    .J(1'b1), .clk(and_1_out), .K(1'b1), .Q(out_3), .Qn(j_k_ff_1_qn), .reset(and_2_out));  // open: preset, en
  and and_1 (and_1_out, SI, S0);
  J_K_Flip_Flop j_k_ff_2 (
    .J(1'b1), .clk(j_k_ff_1_qn), .K(1'b1), .Q(out_4), .Qn(j_k_ff_2_qn), .reset(and_2_out));  // open: preset, en
  J_K_Flip_Flop j_k_ff_3 (
    .J(1'b1), .clk(j_k_ff_2_qn), .K(1'b1), .Q(out_5), .Qn(j_k_ff_3_qn), .reset(and_2_out));  // open: preset, en
  J_K_Flip_Flop j_k_ff_4 (
    .J(1'b1), .clk(j_k_ff_3_qn), .K(1'b1), .Q(out_6), .Qn(j_k_ff_4_qn), .reset(and_2_out));  // open: preset, en
  and and_2 (and_2_out, ~j_k_ff_2_qn, ~j_k_ff_4_qn);  // AND_Gate
  J_K_Flip_Flop j_k_ff_5 (
    .J(1'b1), .clk(j_k_ff_4_qn), .K(1'b1), .Q(out_7), .Qn(j_k_ff_5_qn), .reset(and_3_out));  // open: preset, en
  J_K_Flip_Flop j_k_ff_6 (
    .J(1'b1), .clk(j_k_ff_5_qn), .K(1'b1), .Q(out_8), .Qn(j_k_ff_6_qn), .reset(and_3_out));  // open: preset, en
  J_K_Flip_Flop j_k_ff_7 (
    .J(1'b1), .clk(j_k_ff_6_qn), .K(1'b1), .Q(out_9), .Qn(j_k_ff_7_qn), .reset(and_3_out));  // open: preset, en
  J_K_Flip_Flop j_k_ff_8 (
    .J(1'b1), .clk(j_k_ff_9_qn), .K(1'b1), .Q(out_11), .Qn(j_k_ff_8_qn));  // open: preset, en, reset
  J_K_Flip_Flop j_k_ff_9 (
    .J(1'b1), .clk(j_k_ff_7_qn), .K(1'b1), .Q(out_10), .Qn(j_k_ff_9_qn), .reset(and_3_out));  // open: preset, en
  and and_3 (and_3_out, ~j_k_ff_6_qn, ~j_k_ff_9_qn);  // AND_Gate
  J_K_Flip_Flop j_k_ff_10 (.J(1'b1), .clk(j_k_ff_8_qn), .K(1'b1), .Q(out_12));  // open: Qn, preset, en, reset
endmodule

module BoxCounter2 (
  input  SI,
  input  S0,
  input  in_3
);

  wire and_1_out, and_2_out, and_3_out, and_4_out, and_5_out, and_6_out, and_7_out, and_8_out, clock_1_out,
       multiplexer_1_out, multiplexer_2_out, nor_1_out, not_1_out, not_2_out, not_3_out, or_1_out, or_2_out,
       random_1_out, s_r_ff_1_q, s_r_ff_1_qn, shift_register_1_out, shift_register_1_q6, shift_register_1_q7,
       shift_register_2_out, shift_register_2_q16, shift_register_2_q17, shift_register_3_q5,
       shift_register_3_q6, shift_register_3_q7, shift_register_3_q8, shift_register_3_q13,
       shift_register_3_q14, shift_register_3_q15, xor_1_out;

  and and_1 (and_1_out, multiplexer_1_out, multiplexer_2_out);
  Clock clock_1 (.out(clock_1_out));
  and and_2 (and_2_out, ~multiplexer_1_out, ~multiplexer_2_out);  // AND_Gate
  and and_3 (and_3_out, and_1_out, clock_1_out);
  not not_1 (not_1_out, shift_register_1_out);
  Shift_Register shift_register_1 (
    .in(not_1_out), .clk(clock_1_out), .out(shift_register_1_out), .q6(shift_register_1_q6),
    .q7(shift_register_1_q7));  // open: shift, load, clr, d0, q0, d1, q1, d2, q2, d3, q3, d4, q4, d5, q5, d6, d7
  Shift_Register #(.length(18)) shift_register_2 (
    .in(not_2_out), .clk(clock_1_out), .out(shift_register_2_out), .q16(shift_register_2_q16),
    .q17(shift_register_2_q17));  // open: shift, load, clr, d0, q0, d1, q1, d2, q2, d3, q3, d4, q4, d5, q5, d6, q6, d7, q7, d8, q8, d9, q9, d10, q10, d11, q11, d12, q12, d13, q13, d14, q14, d15, q15, d16, d17
  Shift_Register #(.length(16)) shift_register_3 (
    .in(1'b1), .clk(and_3_out), .clr(and_2_out), .q5(shift_register_3_q5), .q6(shift_register_3_q6),
    .q7(shift_register_3_q7), .q8(shift_register_3_q8), .q13(shift_register_3_q13),
    .q14(shift_register_3_q14), .q15(shift_register_3_q15));  // open: shift, out, load, d0, q0, d1, q1, d2, q2, d3, q3, d4, q4, d5, d6, d7, d8, d9, q9, d10, q10, d11, q11, d12, q12, d13, d14, d15
  not not_2 (not_2_out, shift_register_2_out);
  or or_1 (or_1_out, shift_register_3_q7, shift_register_3_q6, shift_register_3_q5);
  or or_2 (or_2_out, shift_register_3_q15, shift_register_3_q14, shift_register_3_q13);
  nor nor_1 (nor_1_out, shift_register_2_q17, shift_register_1_q7);
  xor xor_1 (xor_1_out, shift_register_3_q8, or_1_out);
  S_R_Flip_Flop s_r_ff_1 (
    .S(xor_1_out), .clk(clock_1_out), .R(or_2_out), .Q(s_r_ff_1_q), .Qn(s_r_ff_1_qn), .reset(and_2_out));  // open: preset, en
  LED led_1 (.in(not_3_out));
  not not_3 (not_3_out, random_1_out);
  LED led_2 (.in(random_1_out));
  Random #(.width(1)) random_1 (.clk(nor_1_out), .out(random_1_out));  // open: next, clr
  and and_4 (and_4_out, multiplexer_1_out, ~multiplexer_2_out);  // AND_Gate
  Counter counter_1 (.clk(and_5_out), .clr(in_3));  // open: load, D, count, Q, carry
  and and_5 (and_5_out, and_4_out, s_r_ff_1_q);
  Counter counter_2 (.clk(and_6_out), .clr(in_3));  // open: load, D, count, Q, carry
  and and_6 (and_6_out, and_4_out, s_r_ff_1_qn);
  Multiplexer multiplexer_1 (
    .in0(shift_register_1_q7), .in1(shift_register_2_q17), .out(multiplexer_1_out), .sel(random_1_out));  // open: en
  Multiplexer multiplexer_2 (
    .in0(shift_register_1_q6), .in1(shift_register_2_q16), .out(multiplexer_2_out), .sel(random_1_out));  // open: en
  Counter counter_3 (.clk(and_7_out), .clr(in_3));  // open: load, D, count, Q, carry
  and and_7 (and_7_out, not_3_out, shift_register_1_q7);
  Counter counter_4 (.clk(and_8_out), .clr(in_3));  // open: load, D, count, Q, carry
  and and_8 (and_8_out, shift_register_2_q17, random_1_out);

  // Notes on the sheet:
  //   20 Hz
  //   Circuito simulador para teste
endmodule

module OverCount (
  input  Q
);

  wire and_1_out, D_out, I_out, j_k_ff_1_q, nor_1_out, nor_2_out, or_1_out, or_2_out, R_out;
  wire [7:0] counter_1_q;

  Button I (.out(I_out));
  Button D (.out(D_out));
  Button R (.out(R_out));
  and and_1 (and_1_out, D_out, or_2_out);
  or or_1 (or_1_out, I_out, and_1_out);
  nor nor_1 (nor_1_out, nor_2_out, I_out);
  nor nor_2 (nor_2_out, and_1_out, nor_1_out);
  Counter counter_1 (.load(nor_1_out), .count(1'b1), .Q(counter_1_q), .clk(or_1_out), .clr(R_out));  // open: D, carry
  J_K_Flip_Flop j_k_ff_1 (.J(1'b1), .clk(Q), .K(1'b1), .Q(j_k_ff_1_q), .reset(R_out));  // open: Qn, preset, en
  not not_1 (Q, counter_1_q[7]);
  LED LED (.in(j_k_ff_1_q));
  or or_2 (or_2_out, counter_1_q[7], counter_1_q[6], counter_1_q[5], counter_1_q[4], counter_1_q[3], counter_1_q[2], counter_1_q[1], counter_1_q[0]);

  // Notes on the sheet:
  //   (Q) do FF mais significativo para BCD
  //   Ou combinação específica para binário
endmodule

module Cnt (
);

  wire _10_0_out, _15_9_out, atraso8_1_out, cntbcd_1_q0, cntbcd_1_q1, cntbcd_1_q2, cntbcd_1_q3, D_out, I_out,
       j_k_ff_1_q, j_k_ff_1_qn, j_k_ff_2_q, j_k_ff_2_qn, j_k_ff_3_q, j_k_ff_3_qn, j_k_ff_4_q, j_k_ff_4_qn,
       nor_1_out, nor_2_out, nor_3_out, or_1_out, or_2_out, R_out, xor_1_out, xor_2_out, xor_3_out, xor_4_out;
  wire [2:0] decbcd7s_1_c_2, decbcd7s_2_c_2;
  wire [3:0] decbcd7s_1_b_2, decbcd7s_2_b_2;

  Button I (.out(I_out));
  Button D (.out(D_out));
  nor nor_1 (nor_1_out, I_out, D_out);
  nor nor_2 (nor_2_out, D_out, nor_3_out);
  nor nor_3 (nor_3_out, nor_2_out, I_out);
  DecBCD7S decbcd7s_1 (
    .A(cntbcd_1_q3), .B(cntbcd_1_q2), .C(cntbcd_1_q1), .D(cntbcd_1_q0), .a_2(decbcd7s_1_b_2[1]),
    .b_2(decbcd7s_1_b_2[0]), .c_2(decbcd7s_1_c_2[0]), .d_2(decbcd7s_1_c_2[1]), .e(decbcd7s_1_c_2[2]),
    .f(decbcd7s_1_b_2[2]), .g(decbcd7s_1_b_2[3]));
  J_K_Flip_Flop j_k_ff_1 (
    .J(1'b1), .clk(nor_1_out), .K(1'b1), .Q(j_k_ff_1_q), .Qn(j_k_ff_1_qn), .preset(_15_9_out),
    .en(nor_1_out), .reset(or_2_out));
  xor xor_1 (xor_1_out, nor_3_out, j_k_ff_1_qn);
  Button R (.out(R_out));
  DecBCD7S decbcd7s_2 (
    .A(j_k_ff_4_q), .B(j_k_ff_3_q), .C(j_k_ff_2_q), .D(j_k_ff_1_q), .a_2(decbcd7s_2_b_2[1]),
    .b_2(decbcd7s_2_b_2[0]), .c_2(decbcd7s_2_c_2[0]), .d_2(decbcd7s_2_c_2[1]), .e(decbcd7s_2_c_2[2]),
    .f(decbcd7s_2_b_2[2]), .g(decbcd7s_2_b_2[3]));
  J_K_Flip_Flop j_k_ff_2 (
    .J(1'b1), .clk(xor_1_out), .K(1'b1), .Q(j_k_ff_2_q), .Qn(j_k_ff_2_qn), .en(nor_1_out), .reset(or_1_out));  // open: preset
  or or_1 (or_1_out, or_2_out, _15_9_out);
  xor xor_2 (xor_2_out, nor_3_out, j_k_ff_2_qn);
  or or_2 (or_2_out, _10_0_out, R_out);
  _7_Segment_Display u_7_segment_display_1 (
    .g(decbcd7s_1_b_2[3]), .f(decbcd7s_1_b_2[2]), .a(decbcd7s_1_b_2[1]), .b(decbcd7s_1_b_2[0]),
    .e(decbcd7s_1_c_2[2]), .d(decbcd7s_1_c_2[1]), .c(decbcd7s_1_c_2[0]));  // open: dp
  J_K_Flip_Flop j_k_ff_3 (
    .J(1'b1), .clk(xor_2_out), .K(1'b1), .Q(j_k_ff_3_q), .Qn(j_k_ff_3_qn), .en(nor_1_out), .reset(or_1_out));  // open: preset
  and _10_0 (_10_0_out, ~nor_3_out, j_k_ff_4_q, ~j_k_ff_3_q, j_k_ff_2_q, ~j_k_ff_1_q);  // AND_Gate
  and _15_9 (_15_9_out, nor_3_out, j_k_ff_4_q, atraso8_1_out, j_k_ff_2_q, j_k_ff_1_q);
  _7_Segment_Display u_7_segment_display_2 (
    .g(decbcd7s_2_b_2[3]), .f(decbcd7s_2_b_2[2]), .a(decbcd7s_2_b_2[1]), .b(decbcd7s_2_b_2[0]),
    .e(decbcd7s_2_c_2[2]), .d(decbcd7s_2_c_2[1]), .c(decbcd7s_2_c_2[0]));  // open: dp
  J_K_Flip_Flop j_k_ff_4 (
    .J(1'b1), .clk(xor_3_out), .K(1'b1), .Q(j_k_ff_4_q), .Qn(j_k_ff_4_qn), .preset(_15_9_out),
    .en(nor_1_out), .reset(or_2_out));
  xor xor_3 (xor_3_out, nor_3_out, j_k_ff_3_qn);
  xor xor_4 (xor_4_out, nor_3_out, j_k_ff_4_qn);
  Atraso8 atraso8_1 (.IN(j_k_ff_3_q), .OUT(atraso8_1_out));
  CntBCD cntbcd_1 (
    .CLK(xor_4_out), .EN(nor_1_out), .D__I(nor_3_out), .Q0(cntbcd_1_q0), .Q1(cntbcd_1_q1), .Q2(cntbcd_1_q2),
    .Q3(cntbcd_1_q3), .R(R_out));  // open: CO
endmodule

module Beep_2_1 (
  input  _1S,
  input  EN,
  output BO
);

  wire and_1_out, j_k_ff_1_q, j_k_ff_2_q, j_k_ff_2_qn, j_k_ff_3_qn, j_k_ff_4_q, n2clk_1_clkout, nand_1_out,
       nor_1_out, not_1_out;

  _2clk u_2clk_1 (.ClkIn(_1S), .ClkOut(n2clk_1_clkout));
  not not_1 (not_1_out, EN);
  and and_1 (and_1_out, n2clk_1_clkout, EN, nand_1_out);
  J_K_Flip_Flop j_k_ff_1 (
    .J(1'b1), .clk(and_1_out), .K(1'b1), .Q(j_k_ff_1_q), .preset(nor_1_out));  // open: Qn, en, reset
  J_K_Flip_Flop j_k_ff_2 (
    .J(1'b1), .clk(j_k_ff_3_qn), .K(1'b1), .Q(j_k_ff_2_q), .Qn(j_k_ff_2_qn), .reset(not_1_out));  // open: preset, en
  J_K_Flip_Flop j_k_ff_3 (
    .J(1'b1), .clk(j_k_ff_1_q), .K(1'b1), .Q(BO), .Qn(j_k_ff_3_qn), .preset(nor_1_out));  // open: en, reset
  nor nor_1 (nor_1_out, BO, j_k_ff_1_q);
  J_K_Flip_Flop j_k_ff_4 (
    .J(1'b1), .clk(j_k_ff_2_qn), .K(1'b1), .Q(j_k_ff_4_q), .reset(not_1_out));  // open: Qn, preset, en
  nand nand_1 (nand_1_out, j_k_ff_4_q, j_k_ff_2_q);
  Shift_Register #(.length(16)) shift_register_1 (
    .in(BO), .clk(n2clk_1_clkout));  // open: shift, out, load, clr, d0, q0, d1, q1, d2, q2, d3, q3, d4, q4, d5, q5, d6, q6, d7, q7, d8, q8, d9, q9, d10, q10, d11, q11, d12, q12, d13, q13, d14, q14, d15, q15
endmodule

module Beep2 (
  input  EN,
  input  _1s,
  output Out
);

  wire and_1_out, and_2_out, and_3_out, and_4_out, and_5_out, and_6_out, and_7_out, and_8_out, j_k_ff_1_q,
       j_k_ff_2_q, j_k_ff_2_qn, j_k_ff_3_q, j_k_ff_3_qn, j_k_ff_4_q, j_k_ff_4_qn, n2clk_1_clkout, not_1_out,
       not_2_out, not_3_out, not_4_out, not_5_out, not_6_out, not_7_out, not_8_out, not_9_out, not_10_out,
       not_11_out, not_12_out, not_13_out, not_14_out, not_15_out, not_16_out, not_17_out, or_2_out;

  _2clk u_2clk_1 (.ClkIn(_1s), .ClkOut(n2clk_1_clkout));
  J_K_Flip_Flop j_k_ff_1 (
    .J(1'b1), .clk(j_k_ff_2_qn), .K(1'b1), .Q(j_k_ff_1_q), .en(or_2_out), .reset(and_8_out));  // open: Qn, preset
  J_K_Flip_Flop j_k_ff_2 (
    .J(1'b1), .clk(j_k_ff_3_qn), .K(1'b1), .Q(j_k_ff_2_q), .Qn(j_k_ff_2_qn), .en(or_2_out), .reset(and_8_out));  // open: preset
  J_K_Flip_Flop j_k_ff_3 (
    .J(1'b1), .clk(j_k_ff_4_qn), .K(1'b1), .Q(j_k_ff_3_q), .Qn(j_k_ff_3_qn), .en(or_2_out), .reset(and_8_out));  // open: preset
  J_K_Flip_Flop j_k_ff_4 (
    .J(1'b1), .clk(n2clk_1_clkout), .K(1'b1), .Q(j_k_ff_4_q), .Qn(j_k_ff_4_qn), .en(or_2_out),
    .reset(and_8_out));  // open: preset
  not not_1 (not_1_out, j_k_ff_1_q);
  not not_2 (not_2_out, j_k_ff_3_q);
  not not_3 (not_3_out, j_k_ff_1_q);
  not not_4 (not_4_out, j_k_ff_2_q);
  not not_5 (not_5_out, j_k_ff_4_q);
  not not_6 (not_6_out, j_k_ff_1_q);
  not not_7 (not_7_out, j_k_ff_3_q);
  not not_8 (not_8_out, j_k_ff_1_q);
  not not_9 (not_9_out, j_k_ff_2_q);
  not not_10 (not_10_out, j_k_ff_3_q);
  not not_11 (not_11_out, j_k_ff_4_q);
  not not_12 (not_12_out, j_k_ff_1_q);
  not not_13 (not_13_out, j_k_ff_2_q);
  not not_14 (not_14_out, j_k_ff_3_q);
  not not_15 (not_15_out, EN);
  not not_16 (not_16_out, j_k_ff_2_q);
  not not_17 (not_17_out, j_k_ff_4_q);
  and and_1 (and_1_out, EN, not_1_out, not_2_out, j_k_ff_4_q);
  and and_2 (and_2_out, EN, not_3_out, not_4_out, j_k_ff_3_q, not_5_out);
  and and_3 (and_3_out, EN, not_6_out, j_k_ff_2_q, not_7_out);
  and and_4 (and_4_out, EN, not_8_out, j_k_ff_2_q, j_k_ff_4_q);
  and and_5 (and_5_out, EN, j_k_ff_1_q, not_9_out, not_10_out, not_11_out);
  and and_6 (and_6_out, EN, not_12_out);
  and and_7 (and_7_out, EN, not_13_out, not_14_out);
  and and_8 (and_8_out, not_15_out, j_k_ff_1_q, not_16_out, j_k_ff_3_q, not_17_out);
  or or_1 (Out, and_1_out, and_2_out, and_3_out, and_4_out, and_5_out);
  or or_2 (or_2_out, and_6_out, and_7_out);
  Shift_Register #(.length(16)) shift_register_1 (
    .in(Out), .clk(n2clk_1_clkout));  // open: shift, out, load, clr, d0, q0, d1, q1, d2, q2, d3, q3, d4, q4, d5, q5, d6, q6, d7, q7, d8, q8, d9, q9, d10, q10, d11, q11, d12, q12, d13, q13, d14, q14, d15, q15

  // Notes on the sheet:
  //   Clock Enable
  //   Reset Counter
endmodule

// 1s
module Base1s (
  output _1_Hz
);

  wire and_1_out, and_2_out, and_4_out, clock_1_out, j_k_ff_1_q, j_k_ff_1_qn, j_k_ff_2_q, j_k_ff_2_qn,
       j_k_ff_3_q, j_k_ff_3_qn, j_k_ff_4_q, j_k_ff_4_qn, j_k_ff_5_q, j_k_ff_5_qn, j_k_ff_6_q;
  wire [2:0] dech7s_1_c_2, dech7s_2_c_2;
  wire [3:0] dech7s_1_b_2, dech7s_2_b_2;

  Clock clock_1 (.out(clock_1_out));
  J_K_Flip_Flop j_k_ff_1 (
    .J(1'b1), .clk(clock_1_out), .K(1'b1), .Q(j_k_ff_1_q), .Qn(j_k_ff_1_qn), .reset(and_4_out));  // open: preset, en
  J_K_Flip_Flop j_k_ff_2 (
    .J(1'b1), .clk(j_k_ff_1_qn), .K(1'b1), .Q(j_k_ff_2_q), .Qn(j_k_ff_2_qn), .reset(and_4_out));  // open: preset, en
  DecH7S dech7s_1 (
    .A(1'b0), .B(1'b0), .C(j_k_ff_6_q), .D(j_k_ff_5_q), .a_2(dech7s_1_b_2[1]), .b_2(dech7s_1_b_2[0]),
    .c_2(dech7s_1_c_2[0]), .d_2(dech7s_1_c_2[1]), .e(dech7s_1_c_2[2]), .f(dech7s_1_b_2[2]),
    .g(dech7s_1_b_2[3]));
  J_K_Flip_Flop j_k_ff_3 (
    .J(1'b1), .clk(j_k_ff_2_qn), .K(1'b1), .Q(j_k_ff_3_q), .Qn(j_k_ff_3_qn), .reset(and_4_out));  // open: preset, en
  J_K_Flip_Flop j_k_ff_4 (
    .J(1'b1), .clk(j_k_ff_3_qn), .K(1'b1), .Q(j_k_ff_4_q), .Qn(j_k_ff_4_qn), .reset(and_4_out));  // open: preset, en
  DecH7S dech7s_2 (
    .A(j_k_ff_4_q), .B(j_k_ff_3_q), .C(j_k_ff_2_q), .D(j_k_ff_1_q), .a_2(dech7s_2_b_2[1]),
    .b_2(dech7s_2_b_2[0]), .c_2(dech7s_2_c_2[0]), .d_2(dech7s_2_c_2[1]), .e(dech7s_2_c_2[2]),
    .f(dech7s_2_b_2[2]), .g(dech7s_2_b_2[3]));
  J_K_Flip_Flop j_k_ff_5 (
    .J(1'b1), .clk(j_k_ff_4_qn), .K(1'b1), .Q(j_k_ff_5_q), .Qn(j_k_ff_5_qn), .reset(and_4_out));  // open: preset, en
  _7_Segment_Display u_7_segment_display_1 (
    .g(dech7s_1_b_2[3]), .f(dech7s_1_b_2[2]), .a(dech7s_1_b_2[1]), .b(dech7s_1_b_2[0]), .e(dech7s_1_c_2[2]),
    .d(dech7s_1_c_2[1]), .c(dech7s_1_c_2[0]));  // open: dp
  J_K_Flip_Flop j_k_ff_6 (
    .J(1'b1), .clk(j_k_ff_5_qn), .K(1'b1), .Q(j_k_ff_6_q), .reset(and_4_out));  // open: Qn, preset, en
  _7_Segment_Display u_7_segment_display_2 (
    .g(dech7s_2_b_2[3]), .f(dech7s_2_b_2[2]), .a(dech7s_2_b_2[1]), .b(dech7s_2_b_2[0]), .e(dech7s_2_c_2[2]),
    .d(dech7s_2_c_2[1]), .c(dech7s_2_c_2[0]));  // open: dp
  and and_1 (and_1_out, j_k_ff_1_q, j_k_ff_2_q, ~j_k_ff_3_q);  // AND_Gate
  and and_2 (and_2_out, j_k_ff_4_q, j_k_ff_5_q, j_k_ff_6_q);
  and and_3 (_1_Hz, and_1_out, and_2_out);
  and and_4 (and_4_out, and_2_out, j_k_ff_3_q);

  // Notes on the sheet:
  //   60 Hz
endmodule

module _2clk (
  input  ClkIn,
  output ClkOut
);

  wire and_1_out, nor_1_out, not_1_out, not_2_out, not_3_out, not_4_out, not_5_out, not_6_out, not_7_out,
       not_8_out, not_9_out, not_10_out;

  not not_1 (not_1_out, ClkIn);
  not not_2 (not_2_out, ClkIn);
  not not_3 (not_3_out, not_1_out);
  not not_4 (not_4_out, not_3_out);
  not not_5 (not_5_out, not_2_out);
  not not_6 (not_6_out, not_5_out);
  not not_7 (not_7_out, not_4_out);
  not not_8 (not_8_out, not_6_out);
  nor nor_1 (nor_1_out, ClkIn, not_9_out);
  not not_9 (not_9_out, not_7_out);
  and and_1 (and_1_out, ClkIn, not_10_out);
  not not_10 (not_10_out, not_8_out);
  or or_1 (ClkOut, nor_1_out, and_1_out);
endmodule

// HEX7S
module DecH7S (
  input  A,
  input  B,
  input  C,
  input  D,
  output a_2,
  output b_2,
  output c_2,
  output d_2,
  output e,
  output f,
  output g
);

  wire and_1_out, and_2_out, and_3_out, and_4_out, and_5_out, and_6_out, and_7_out, and_8_out, and_9_out,
       and_10_out, and_11_out, and_12_out, and_13_out, and_14_out, and_15_out, and_16_out, and_17_out,
       and_18_out, and_19_out, and_20_out, and_21_out, and_22_out, and_23_out, and_24_out, and_25_out,
       and_26_out, and_27_out, and_28_out, and_29_out, and_30_out, and_31_out, and_32_out, and_33_out,
       and_34_out, and_35_out, not_1_out, not_2_out, not_3_out, not_4_out, not_5_out, not_6_out, not_7_out,
       not_8_out, not_9_out, not_10_out, not_11_out, not_12_out, not_13_out, not_14_out, not_15_out,
       not_16_out, not_17_out, not_18_out, not_19_out, not_20_out, not_21_out, not_22_out, not_23_out,
       not_24_out, not_25_out, not_26_out, not_27_out, not_28_out, not_29_out, not_30_out, not_31_out,
       not_32_out, not_33_out, not_34_out, not_35_out, not_36_out, not_37_out, not_38_out, not_39_out,
       not_40_out, not_41_out, not_42_out, not_43_out;

  not not_1 (not_1_out, B);
  and and_1 (and_1_out, not_1_out, not_2_out);
  not not_2 (not_2_out, D);
  not not_3 (not_3_out, A);
  and and_2 (and_2_out, not_3_out, C);
  not not_4 (not_4_out, A);
  and and_3 (and_3_out, not_4_out, B, D);
  and and_4 (and_4_out, B, C);
  not not_5 (not_5_out, B);
  and and_5 (and_5_out, A, not_5_out, not_6_out);
  not not_6 (not_6_out, C);
  and and_6 (and_6_out, A, not_7_out);
  not not_7 (not_7_out, D);
  not not_8 (not_8_out, A);
  and and_7 (and_7_out, not_8_out, not_9_out);
  not not_9 (not_9_out, B);
  not not_10 (not_10_out, A);
  not not_11 (not_11_out, C);
  and and_8 (and_8_out, not_10_out, not_11_out, not_12_out);
  not not_12 (not_12_out, D);
  not not_13 (not_13_out, B);
  and and_9 (and_9_out, not_13_out, not_14_out);
  not not_14 (not_14_out, D);
  not not_15 (not_15_out, A);
  and and_10 (and_10_out, not_15_out, C, D);
  not not_16 (not_16_out, C);
  and and_11 (and_11_out, A, not_16_out, D);
  not not_17 (not_17_out, A);
  and and_12 (and_12_out, not_17_out, not_18_out);
  not not_18 (not_18_out, C);
  not not_19 (not_19_out, A);
  and and_13 (and_13_out, not_19_out, D);
  not not_20 (not_20_out, C);
  and and_14 (and_14_out, not_20_out, D);
  not not_21 (not_21_out, A);
  and and_15 (and_15_out, not_21_out, B);
  and and_16 (and_16_out, A, not_22_out);
  not not_22 (not_22_out, B);
  not not_23 (not_23_out, A);
  not not_24 (not_24_out, B);
  and and_17 (and_17_out, not_23_out, not_24_out, not_25_out);
  not not_25 (not_25_out, D);
  not not_26 (not_26_out, B);
  and and_18 (and_18_out, not_26_out, C, D);
  not not_27 (not_27_out, C);
  and and_19 (and_19_out, B, not_27_out, D);
  and and_20 (and_20_out, B, C, not_28_out);
  not not_28 (not_28_out, D);
  and and_21 (and_21_out, A, not_29_out);
  not not_29 (not_29_out, C);
  not not_30 (not_30_out, B);
  and and_22 (and_22_out, not_30_out, not_31_out);
  not not_31 (not_31_out, D);
  and and_23 (and_23_out, C, not_32_out);
  not not_32 (not_32_out, D);
  and and_24 (and_24_out, A, C);
  and and_25 (and_25_out, A, B);
  not not_33 (not_33_out, C);
  and and_26 (and_26_out, not_33_out, not_34_out);
  not not_34 (not_34_out, D);
  not not_35 (not_35_out, A);
  and and_27 (and_27_out, not_35_out, B, not_36_out);
  not not_36 (not_36_out, C);
  and and_28 (and_28_out, B, not_37_out);
  not not_37 (not_37_out, D);
  and and_29 (and_29_out, A, not_38_out);
  not not_38 (not_38_out, B);
  and and_30 (and_30_out, A, C);
  not not_39 (not_39_out, B);
  and and_31 (and_31_out, not_39_out, C);
  and and_32 (and_32_out, C, not_40_out);
  not not_40 (not_40_out, D);
  not not_41 (not_41_out, A);
  and and_33 (and_33_out, not_41_out, B, not_42_out);
  not not_42 (not_42_out, C);
  and and_34 (and_34_out, A, not_43_out);
  not not_43 (not_43_out, B);
  and and_35 (and_35_out, A, D);
  or or_1 (b_2, and_7_out, and_8_out, and_9_out, and_10_out, and_11_out);
  or or_2 (c_2, and_12_out, and_13_out, and_14_out, and_15_out, and_16_out);
  or or_3 (d_2, and_17_out, and_18_out, and_19_out, and_20_out, and_21_out);
  or or_4 (e, and_22_out, and_23_out, and_24_out, and_25_out);
  or or_5 (f, and_26_out, and_27_out, and_28_out, and_29_out, and_30_out);
  or or_6 (g, and_31_out, and_32_out, and_33_out, and_34_out, and_35_out);
  or or_7 (a_2, and_1_out, and_2_out, and_3_out, and_4_out, and_5_out, and_6_out);
endmodule

// BCD7S
module DecBCD7S (
  input  A,
  input  B,
  input  C,
  input  D,
  output a_2,
  output b_2,
  output c_2,
  output d_2,
  output e,
  output f,
  output g
);

  wire and_1_out, and_2_out, and_3_out, and_4_out, and_5_out, and_6_out, and_7_out, and_8_out, and_9_out,
       and_10_out, and_11_out, and_12_out, and_13_out, and_14_out, and_15_out, and_16_out, and_17_out,
       and_18_out, and_19_out, and_20_out, and_21_out, and_22_out, and_23_out, and_24_out, and_25_out,
       and_26_out, not_1_out, not_2_out, not_3_out, not_4_out, not_5_out, not_6_out, not_7_out, not_8_out,
       not_9_out, not_10_out, not_11_out, not_12_out, not_13_out, not_14_out, not_15_out, not_16_out,
       not_17_out, not_18_out, not_19_out, not_20_out, not_21_out, not_22_out, not_23_out, not_24_out,
       not_25_out, not_26_out, not_27_out, not_28_out, not_29_out, not_30_out, not_31_out, not_32_out,
       not_33_out, not_34_out, not_35_out, not_36_out, not_37_out, not_38_out, not_39_out, not_40_out,
       not_41_out, not_42_out, not_43_out, not_44_out, not_45_out, not_46_out, not_47_out, not_48_out,
       not_49_out, not_50_out, not_51_out, not_52_out;

  not not_1 (not_1_out, A);
  and and_1 (and_1_out, not_1_out, not_2_out, not_3_out);
  not not_2 (not_2_out, B);
  not not_3 (not_3_out, D);
  not not_4 (not_4_out, A);
  and and_2 (and_2_out, not_4_out, C);
  not not_5 (not_5_out, A);
  and and_3 (and_3_out, not_5_out, B, D);
  not not_6 (not_6_out, B);
  and and_4 (and_4_out, A, not_6_out, not_7_out);
  not not_7 (not_7_out, C);
  not not_8 (not_8_out, A);
  and and_5 (and_5_out, not_8_out, not_9_out);
  not not_9 (not_9_out, B);
  not not_10 (not_10_out, A);
  not not_11 (not_11_out, C);
  and and_6 (and_6_out, not_10_out, not_11_out, not_12_out);
  not not_12 (not_12_out, D);
  not not_13 (not_13_out, B);
  and and_7 (and_7_out, not_13_out, not_14_out);
  not not_14 (not_14_out, C);
  not not_15 (not_15_out, A);
  and and_8 (and_8_out, not_15_out, C, D);
  not not_16 (not_16_out, B);
  and and_9 (and_9_out, not_16_out, not_17_out);
  not not_17 (not_17_out, C);
  not not_18 (not_18_out, A);
  and and_10 (and_10_out, not_18_out, D);
  not not_19 (not_19_out, A);
  and and_11 (and_11_out, not_19_out, B);
  not not_20 (not_20_out, A);
  not not_21 (not_21_out, B);
  not not_22 (not_22_out, D);
  not not_23 (not_23_out, A);
  not not_24 (not_24_out, B);
  not not_25 (not_25_out, A);
  not not_26 (not_26_out, D);
  not not_27 (not_27_out, A);
  not not_28 (not_28_out, C);
  not not_29 (not_29_out, B);
  not not_30 (not_30_out, C);
  not not_31 (not_31_out, B);
  and and_12 (and_12_out, not_31_out, not_32_out, not_33_out);
  not not_32 (not_32_out, C);
  not not_33 (not_33_out, D);
  not not_34 (not_34_out, A);
  and and_13 (and_13_out, not_34_out, C, not_35_out);
  not not_35 (not_35_out, D);
  not not_36 (not_36_out, A);
  not not_37 (not_37_out, C);
  and and_14 (and_14_out, not_36_out, not_37_out, not_38_out);
  not not_38 (not_38_out, D);
  not not_39 (not_39_out, A);
  and and_15 (and_15_out, not_39_out, B, not_40_out);
  not not_40 (not_40_out, C);
  not not_41 (not_41_out, A);
  and and_16 (and_16_out, not_41_out, B, not_42_out);
  not not_42 (not_42_out, D);
  not not_43 (not_43_out, B);
  and and_17 (and_17_out, A, not_43_out, not_44_out);
  not not_44 (not_44_out, C);
  not not_45 (not_45_out, A);
  and and_18 (and_18_out, not_45_out, not_46_out, C);
  not not_46 (not_46_out, B);
  not not_47 (not_47_out, A);
  and and_19 (and_19_out, not_47_out, B, not_48_out);
  not not_48 (not_48_out, C);
  not not_49 (not_49_out, A);
  and and_20 (and_20_out, not_49_out, B, not_50_out);
  not not_50 (not_50_out, D);
  and and_21 (and_21_out, A, not_51_out, not_52_out);
  not not_51 (not_51_out, B);
  not not_52 (not_52_out, C);
  or or_1 (a_2, and_1_out, and_2_out, and_3_out, and_4_out);
  or or_2 (b_2, and_5_out, and_6_out, and_7_out, and_8_out);
  or or_3 (c_2, and_9_out, and_10_out, and_11_out);
  and and_22 (and_22_out, not_20_out, not_21_out, not_22_out);
  and and_23 (and_23_out, not_23_out, not_24_out, C);
  and and_24 (and_24_out, not_25_out, C, not_26_out);
  and and_25 (and_25_out, not_27_out, B, not_28_out, D);
  and and_26 (and_26_out, A, not_29_out, not_30_out);
  or or_4 (e, and_12_out, and_13_out);
  or or_5 (f, and_14_out, and_15_out, and_16_out, and_17_out);
  or or_6 (g, and_18_out, and_19_out, and_20_out, and_21_out);
  or or_7 (d_2, and_22_out, and_23_out, and_24_out, and_25_out, and_26_out);
endmodule

module DecCarga (
  input  D9,
  input  D8,
  input  D7,
  input  D6,
  input  D5,
  input  D4,
  input  D3,
  input  D2,
  input  D1,
  input  D0,
  input  B__I,
  input  Load,
  output P9,
  output P8,
  output P7,
  output P6,
  output P5,
  output P4,
  output P3,
  output P2,
  output P1,
  output P0
);

  wire and_1_out, and_2_out, and_3_out, and_4_out, and_5_out, and_6_out, and_7_out, and_8_out, and_9_out,
       and_10_out, and_11_out, and_12_out, and_13_out, and_14_out, and_15_out, and_16_out, and_17_out,
       and_18_out, and_19_out, and_20_out, and_21_out, and_22_out, and_23_out, and_24_out, and_25_out,
       and_26_out, and_27_out, and_28_out, and_29_out, and_30_out, and_31_out, and_32_out, and_33_out,
       and_34_out, and_35_out, and_36_out, and_37_out, and_38_out, and_39_out, and_40_out, and_41_out,
       and_42_out, and_43_out, and_44_out, not_1_out, not_2_out, not_3_out, not_4_out, not_5_out, not_6_out,
       not_7_out, not_8_out, not_9_out, not_10_out, not_11_out, not_12_out, not_13_out, not_14_out,
       not_15_out, not_16_out, not_17_out, not_18_out, not_19_out, not_20_out, not_21_out, not_22_out,
       not_23_out, not_24_out, not_25_out, not_26_out, not_27_out, not_28_out, not_29_out, not_30_out,
       not_31_out, not_32_out, not_33_out, not_34_out, not_35_out, not_36_out, not_37_out, not_38_out,
       not_39_out, not_40_out, not_41_out, not_42_out, not_43_out, not_44_out, not_45_out, not_46_out,
       not_47_out, not_48_out, not_49_out, not_50_out, not_51_out, not_52_out, not_53_out, not_54_out,
       not_55_out, not_56_out, not_57_out, not_58_out, not_59_out, not_60_out, not_61_out, not_62_out,
       not_63_out, not_64_out, or_1_out, or_2_out, or_3_out, or_4_out, or_5_out, or_6_out, or_7_out,
       or_8_out, xor_1_out, xor_2_out, xor_3_out, xor_4_out, xor_5_out, xor_6_out, xor_7_out, xor_8_out,
       xor_9_out, xor_10_out;

  not not_1 (not_1_out, D9);
  not not_2 (not_2_out, D8);
  not not_3 (not_3_out, D9);
  not not_4 (not_4_out, D7);
  not not_5 (not_5_out, D8);
  not not_6 (not_6_out, D7);
  not not_7 (not_7_out, D9);
  not not_8 (not_8_out, D8);
  not not_9 (not_9_out, D7);
  not not_10 (not_10_out, D6);
  not not_11 (not_11_out, D9);
  not not_12 (not_12_out, D7);
  not not_13 (not_13_out, D8);
  not not_14 (not_14_out, D7);
  not not_15 (not_15_out, D9);
  not not_16 (not_16_out, D8);
  not not_17 (not_17_out, D7);
  not not_18 (not_18_out, D6);
  not not_19 (not_19_out, D9);
  not not_20 (not_20_out, D8);
  not not_21 (not_21_out, D9);
  not not_22 (not_22_out, D8);
  not not_23 (not_23_out, D9);
  not not_24 (not_24_out, D8);
  not not_25 (not_25_out, D9);
  not not_26 (not_26_out, D9);
  not not_27 (not_27_out, D9);
  not not_28 (not_28_out, D9);
  not not_29 (not_29_out, D8);
  not not_30 (not_30_out, D8);
  not not_31 (not_31_out, D3);
  not not_32 (not_32_out, D8);
  not not_33 (not_33_out, D3);
  not not_34 (not_34_out, D9);
  not not_35 (not_35_out, D3);
  not not_36 (not_36_out, D9);
  not not_37 (not_37_out, D3);
  not not_38 (not_38_out, D8);
  not not_39 (not_39_out, D3);
  not not_40 (not_40_out, D8);
  not not_41 (not_41_out, D3);
  not not_42 (not_42_out, D8);
  not not_43 (not_43_out, D3);
  not not_44 (not_44_out, D9);
  not not_45 (not_45_out, D3);
  not not_46 (not_46_out, D9);
  not not_47 (not_47_out, D3);
  not not_48 (not_48_out, D8);
  not not_49 (not_49_out, D3);
  not not_50 (not_50_out, D8);
  not not_51 (not_51_out, D9);
  not not_52 (not_52_out, D9);
  not not_53 (not_53_out, D9);
  not not_54 (not_54_out, D9);
  not not_55 (not_55_out, D9);
  not not_56 (not_56_out, D9);
  not not_57 (not_57_out, D9);
  not not_58 (not_58_out, D9);
  not not_59 (not_59_out, D9);
  not not_60 (not_60_out, D9);
  not not_61 (not_61_out, D9);
  not not_62 (not_62_out, D8);
  not not_63 (not_63_out, D8);
  not not_64 (not_64_out, D8);
  and and_1 (and_1_out, not_1_out, D7);
  and and_2 (and_2_out, not_2_out, D7);
  and and_3 (and_3_out, not_3_out, not_4_out, D6);
  and and_4 (and_4_out, not_5_out, not_6_out, D6);
  and and_5 (and_5_out, not_7_out, not_8_out, not_9_out, not_10_out);
  and and_6 (and_6_out, not_11_out, not_12_out, D5);
  and and_7 (and_7_out, not_13_out, not_14_out, D5);
  and and_8 (and_8_out, not_15_out, not_16_out, not_17_out, not_18_out);
  and and_9 (and_9_out, not_19_out, D4);
  and and_10 (and_10_out, not_20_out, D4);
  and and_11 (and_11_out, not_21_out, D7, D5);
  and and_12 (and_12_out, not_22_out, D7, D5);
  and and_13 (and_13_out, not_23_out, D7, D6);
  and and_14 (and_14_out, not_24_out, D7, D6);
  and and_15 (and_15_out, not_25_out, D5, D4, D3);
  and and_16 (and_16_out, not_26_out, D6, D3);
  and and_17 (and_17_out, not_27_out, D7, D3);
  and and_18 (and_18_out, not_28_out, D8, D3);
  and and_19 (and_19_out, D9, not_29_out, D3);
  and and_20 (and_20_out, not_30_out, D5, D4, not_31_out, D2);
  and and_21 (and_21_out, not_32_out, D6, not_33_out, D2);
  and and_22 (and_22_out, not_34_out, D7, not_35_out, D2);
  and and_23 (and_23_out, not_36_out, D8, not_37_out, D2);
  and and_24 (and_24_out, D9, not_38_out, not_39_out, D2);
  and and_25 (and_25_out, not_40_out, D5, D4, not_41_out, D1);
  and and_26 (and_26_out, not_42_out, D6, not_43_out, D1);
  and and_27 (and_27_out, not_44_out, D7, not_45_out, D1);
  and and_28 (and_28_out, not_46_out, D8, not_47_out, D1);
  and and_29 (and_29_out, D9, not_48_out, not_49_out, D1);
  and and_30 (and_30_out, not_50_out, D5, D4, D0);
  and and_31 (and_31_out, not_51_out, D5, D4, D3, D1);
  and and_32 (and_32_out, not_52_out, D5, D4, D3, D2);
  and and_33 (and_33_out, not_53_out, D6, D0);
  and and_34 (and_34_out, not_54_out, D6, D3, D1);
  and and_35 (and_35_out, not_55_out, D6, D3, D2);
  and and_36 (and_36_out, not_56_out, D7, D0);
  and and_37 (and_37_out, not_57_out, D7, D3, D1);
  and and_38 (and_38_out, not_58_out, D7, D3, D2);
  and and_39 (and_39_out, not_59_out, D8, D0);
  and and_40 (and_40_out, not_60_out, D8, D3, D1);
  and and_41 (and_41_out, not_61_out, D8, D3, D2);
  and and_42 (and_42_out, D9, not_62_out, D0);
  and and_43 (and_43_out, D9, not_63_out, D3, D1);
  and and_44 (and_44_out, D9, not_64_out, D3, D2);
  or or_1 (or_1_out, and_1_out, and_2_out);
  or or_2 (or_2_out, and_3_out, and_4_out);
  or or_3 (or_3_out, and_5_out, and_6_out, and_7_out);
  or or_4 (or_4_out, and_8_out, and_9_out, and_10_out, and_11_out, and_12_out, and_13_out, and_14_out);
  or or_5 (or_5_out, and_15_out, and_16_out, and_17_out, and_18_out, and_19_out);
  or or_6 (or_6_out, and_20_out, and_21_out, and_22_out, and_23_out, and_24_out);
  or or_7 (or_7_out, and_25_out, and_26_out, and_27_out, and_28_out, and_29_out);
  or or_8 (or_8_out, and_30_out, and_31_out, and_32_out, and_33_out, and_34_out, and_35_out, and_36_out, and_37_out, and_38_out, and_39_out, and_40_out, and_41_out, and_42_out, and_43_out, and_44_out);
  xor xor_1 (xor_1_out, D9, B__I);
  xor xor_2 (xor_2_out, D8, B__I);
  xor xor_3 (xor_3_out, or_1_out, B__I);
  xor xor_4 (xor_4_out, or_2_out, B__I);
  xor xor_5 (xor_5_out, or_3_out, B__I);
  xor xor_6 (xor_6_out, or_4_out, B__I);
  xor xor_7 (xor_7_out, or_5_out, B__I);
  xor xor_8 (xor_8_out, or_6_out, B__I);
  xor xor_9 (xor_9_out, or_7_out, B__I);
  xor xor_10 (xor_10_out, or_8_out, B__I);
  and and_45 (P9, xor_1_out, Load);
  and and_46 (P8, xor_2_out, Load);
  and and_47 (P7, xor_3_out, Load);
  and and_48 (P6, xor_4_out, Load);
  and and_49 (P5, xor_5_out, Load);
  and and_50 (P4, xor_6_out, Load);
  and and_51 (P3, xor_7_out, Load);
  and and_52 (P2, xor_8_out, Load);
  and and_53 (P1, xor_9_out, Load);
  and and_54 (P0, xor_10_out, Load);

  // Notes on the sheet:
  //   0 => buffer
  //   1 => Inversor
endmodule

module DecDir (
  input  A,
  input  A__B,
  input  B,
  output S
);

  wire and_1_out, and_2_out;

  and and_1 (and_1_out, ~A__B, A);  // AND_Gate
  and and_2 (and_2_out, A__B, B);
  or or_1 (S, and_1_out, and_2_out);
endmodule

// A8
module Atraso8 (
  input  IN,
  output OUT
);

  wire not_1_out, not_2_out, not_3_out, not_4_out, not_5_out, not_6_out, not_8_out;

  not not_1 (not_1_out, IN);
  not not_2 (not_2_out, not_1_out);
  not not_3 (not_3_out, not_4_out);
  not not_4 (not_4_out, not_2_out);
  not not_5 (not_5_out, not_6_out);
  not not_6 (not_6_out, not_3_out);
  not not_7 (OUT, not_8_out);
  not not_8 (not_8_out, not_5_out);
endmodule

// A16
module Atraso16 (
  input  IN,
  output OUT
);

  wire atraso8_1_out;

  Atraso8 atraso8_1 (.IN(IN), .OUT(atraso8_1_out));
  Atraso8 atraso8_2 (.IN(atraso8_1_out), .OUT(OUT));
endmodule

module CntBCD (
  input  CLK,
  input  EN,
  input  D__I,
  input  R,
  output Q0,
  output Q1,
  output Q2,
  output Q3,
  output CO
);

  wire _10_0_out, _15_9_out, atraso8_1_out, j_k_ff_1_qn, j_k_ff_2_qn, j_k_ff_3_qn, j_k_ff_4_qn, or_1_out,
       or_2_out, xor_1_out, xor_2_out, xor_3_out;

  J_K_Flip_Flop j_k_ff_1 (
    .J(1'b1), .clk(CLK), .K(1'b1), .Q(Q0), .Qn(j_k_ff_1_qn), .preset(_15_9_out), .en(EN), .reset(or_2_out));
  xor xor_1 (xor_1_out, D__I, j_k_ff_1_qn);
  J_K_Flip_Flop j_k_ff_2 (
    .J(1'b1), .clk(xor_1_out), .K(1'b1), .Q(Q1), .Qn(j_k_ff_2_qn), .en(EN), .reset(or_1_out));  // open: preset
  or or_1 (or_1_out, or_2_out, _15_9_out);
  J_K_Flip_Flop j_k_ff_3 (
    .J(1'b1), .clk(xor_2_out), .K(1'b1), .Q(Q2), .Qn(j_k_ff_3_qn), .en(EN), .reset(or_1_out));  // open: preset
  xor xor_2 (xor_2_out, D__I, j_k_ff_2_qn);
  or or_2 (or_2_out, _10_0_out, R);
  xor xor_3 (xor_3_out, D__I, j_k_ff_3_qn);
  and _10_0 (_10_0_out, ~D__I, Q3, ~Q2, Q1, ~Q0);  // AND_Gate
  and _15_9 (_15_9_out, D__I, Q3, atraso8_1_out, Q1, Q0);
  J_K_Flip_Flop j_k_ff_4 (
    .J(1'b1), .clk(xor_3_out), .K(1'b1), .Q(Q3), .Qn(j_k_ff_4_qn), .preset(_15_9_out), .en(EN),
    .reset(or_2_out));
  xor xor_4 (CO, D__I, j_k_ff_4_qn);
  Atraso8 atraso8_1 (.IN(Q2), .OUT(atraso8_1_out));
endmodule

module teste (
);

  wire and_1_out, and_2_out, button_1_out, j_k_ff_1_q, j_k_ff_1_qn, j_k_ff_2_q, j_k_ff_3_q, j_k_ff_3_qn,
       or_1_out;

  Button button_1 (.out(button_1_out));
  LED led_1 (.in(j_k_ff_1_q));
  J_K_Flip_Flop j_k_ff_1 (
    .J(and_1_out), .clk(button_1_out), .K(or_1_out), .Q(j_k_ff_1_q), .Qn(j_k_ff_1_qn));  // open: preset, en, reset
  LED led_2 (.in(j_k_ff_2_q));
  J_K_Flip_Flop j_k_ff_2 (
    .J(1'b1), .clk(button_1_out), .K(j_k_ff_1_qn), .Q(j_k_ff_2_q));  // open: Qn, preset, en, reset
  and and_1 (and_1_out, j_k_ff_2_q, j_k_ff_3_q);
  or or_1 (or_1_out, j_k_ff_2_q, j_k_ff_3_qn);
  and and_2 (and_2_out, j_k_ff_1_q, j_k_ff_2_q);
  LED led_3 (.in(j_k_ff_3_q));
  J_K_Flip_Flop j_k_ff_3 (
    .J(1'b1), .clk(button_1_out), .K(and_2_out), .Q(j_k_ff_3_q), .Qn(j_k_ff_3_qn));  // open: preset, en, reset
endmodule

module teste2 (
);

  wire and_1_out, button_1_out, button_2_out, d_ff_1_q, d_ff_1_qn, d_ff_2_q, d_ff_2_qn, d_ff_3_q, d_ff_3_qn,
       d_ff_4_q, d_ff_4_qn, d_ff_5_q, d_ff_5_qn, d_ff_6_q, d_ff_6_qn, or_1_out;

  Button button_1 (.out(button_1_out));
  Button button_2 (.out(button_2_out));
  D_Flip_Flop d_ff_1 (
    .clk(button_1_out), .D(or_1_out), .Q(d_ff_1_q), .Qn(d_ff_1_qn), .preset(button_2_out));  // open: en, reset
  LED led_1 (.in(d_ff_1_q));
  D_Flip_Flop d_ff_2 (.clk(button_1_out), .D(d_ff_1_q), .Q(d_ff_2_q), .Qn(d_ff_2_qn));  // open: preset, en, reset
  or or_1 (or_1_out, and_1_out, d_ff_6_q);
  LED led_2 (.in(d_ff_2_q));
  LED led_3 (.in(d_ff_3_q));
  D_Flip_Flop d_ff_3 (.clk(button_1_out), .D(d_ff_2_q), .Q(d_ff_3_q), .Qn(d_ff_3_qn));  // open: preset, en, reset
  and and_1 (and_1_out, d_ff_1_qn, d_ff_2_qn, d_ff_3_qn, d_ff_4_qn, d_ff_5_qn, d_ff_6_qn);
  LED led_4 (.in(d_ff_4_q));
  D_Flip_Flop d_ff_4 (.clk(button_1_out), .D(d_ff_3_q), .Q(d_ff_4_q), .Qn(d_ff_4_qn));  // open: preset, en, reset
  LED led_5 (.in(d_ff_5_q));
  D_Flip_Flop d_ff_5 (.clk(button_1_out), .D(d_ff_4_q), .Q(d_ff_5_q), .Qn(d_ff_5_qn));  // open: preset, en, reset
  LED led_6 (.in(d_ff_6_q));
  D_Flip_Flop d_ff_6 (.clk(button_1_out), .D(d_ff_5_q), .Q(d_ff_6_q), .Qn(d_ff_6_qn));  // open: preset, en, reset
endmodule
