// Logisim project Lista.circ as structural Verilog: 2 circuits, main circuit main
module main (
  input  C,
  input  B,
  input  A,
  input  C_2,
  input  B_2,
  input  A_2,
  input  C_3,
  input  B_3,
  input  A_3,
  input  A_4,
  input  B_4,
  input  C_4
);

  wire and_1_out, nand_1_out, nand_2_out, nand_3_out, nand_4_out, nand_5_out, nand_6_out, nand_7_out,
       nand_8_out, nand_9_out, nand_10_out, nand_11_out, nand_12_out, nand_13_out, nand_14_out, nand_15_out,
       nand_16_out, nand_17_out, nand_18_out, nand_19_out, xnor_1_out, xor_1_out;

  nand nand_1 (nand_1_out, A, A);
  nand nand_2 (nand_2_out, B, B);
  nand nand_3 (nand_3_out, C, C);
  nand nand_4 (nand_4_out, A_3, A_3);
  nand nand_5 (nand_5_out, C_3, C_3);
  nand nand_6 (nand_6_out, nand_1_out, nand_3_out);
  nand nand_7 (nand_7_out, nand_2_out, nand_1_out);
  nand nand_8 (nand_8_out, nand_3_out, nand_2_out);
  nand nand_9 (nand_9_out, nand_6_out, nand_7_out);
  nand nand_10 (nand_10_out, nand_4_out, nand_5_out);
  nand nand_11 (nand_11_out, nand_10_out, nand_12_out);
  nand nand_12 (nand_12_out, B_3, nand_4_out);
  nand nand_13 (nand_13_out, nand_9_out, nand_9_out);
  LED led_1 (.in(nand_11_out));
  nand nand_14 (nand_14_out, nand_13_out, nand_8_out);
  LED led_2 (.in(nand_14_out));
  xor xor_1 (xor_1_out, A_4, B_4);
  and and_1 (and_1_out, xor_1_out, xnor_1_out, C_4);
  xnor xnor_1 (xnor_1_out, B_4, C_4);
  nand nand_15 (nand_15_out, B_2, B_2);
  nand nand_16 (nand_16_out, C_2, C_2);
  LED led_3 (.in(and_1_out));
  nand nand_17 (nand_17_out, C_2, B_2);
  nand nand_18 (nand_18_out, nand_15_out, nand_16_out);
  nand nand_19 (nand_19_out, nand_17_out, nand_18_out);
  LED led_4 (.in(nand_19_out));
endmodule

module _7 (
  input  P1,
  input  P2,
  input  P3,
  output S
);

  wire and_1_out, and_2_out, not_1_out;

  not not_1 (not_1_out, P2);
  and and_1 (and_1_out, not_1_out, P3);
  and and_2 (and_2_out, P1, P2);
  or or_1 (S, and_1_out, and_2_out);
endmodule
