// Logisim project semaforo.circ as structural Verilog: 2 circuits, main circuit main
module main (
  input  Sensor_A,
  input  Sensor_B,
  input  Sensor_C,
  input  Sensor_D
);

  wire and_1_out, and_2_out, and_3_out, or_1_out, or_2_out;

  and and_1 (and_1_out, ~Sensor_A, ~Sensor_B);  // AND_Gate
  and and_2 (and_2_out, Sensor_A, ~Sensor_C);  // AND_Gate
  and and_3 (and_3_out, Sensor_B, ~Sensor_D);  // AND_Gate
  or or_1 (or_1_out, and_1_out, Sensor_D);
  or or_2 (or_2_out, and_2_out, and_3_out);
  LED L_O (.in(or_1_out));
  LED N_S (.in(or_2_out));
endmodule

module semaforo (
  input  SensorA,
  input  SensorB,
  input  SensorC,
  input  SensorD,
  output LO,
  output NS
);

  wire and_1_out, and_2_out, and_3_out, not_1_out, not_2_out, not_3_out, not_4_out;

  not not_1 (not_1_out, SensorA);
  and and_1 (and_1_out, not_1_out, not_2_out);
  not not_2 (not_2_out, SensorB);
  and and_2 (and_2_out, SensorB, not_3_out);
  not not_3 (not_3_out, SensorD);
  and and_3 (and_3_out, SensorA, not_4_out);
  not not_4 (not_4_out, SensorD);
  or or_1 (LO, and_1_out, SensorD);
  or or_2 (NS, and_2_out, and_3_out);
endmodule
