// Logisim project TimerBCD999.circ as structural Verilog: 4 circuits, main circuit main
module main (
  input  in_1,
  input  in_2,
  input  in_3,
  input  in_4,
  input  in_5,
  input  in_6,
  input  in_7,
  input  in_8,
  input  in_9,
  input  in_10,
  output out_11
);

  wire and_1_out, and_2_out, and_3_out, base1s_1_out_1, deccarga_1_p0, deccarga_1_p1, deccarga_1_p2,
       deccarga_1_p3, deccarga_1_p4, deccarga_1_p5, deccarga_1_p6, deccarga_1_p7, deccarga_1_p8,
       deccarga_1_p9, deccarga_2_p0, deccarga_2_p1, deccarga_2_p2, deccarga_2_p3, deccarga_2_p4,
       deccarga_2_p5, deccarga_2_p6, deccarga_2_p7, deccarga_2_p8, deccarga_2_p9, j_k_ff_1_q, j_k_ff_2_q,
       j_k_ff_3_q, j_k_ff_4_q, j_k_ff_5_q, j_k_ff_6_q, j_k_ff_7_q, j_k_ff_8_q, j_k_ff_9_q, j_k_ff_10_q,
       Load_out, not_1_out, or_1_out, or_2_out, or_3_out, or_4_out, or_5_out, or_6_out, or_7_out, or_8_out,
       or_9_out, or_10_out, or_11_out;
  wire [2:0] decbcd7s_1_c_2, decbcd7s_2_c_2, decbcd7s_3_c_2;
  wire [3:0] decbcd7s_1_b_2, decbcd7s_2_b_2, decbcd7s_3_b_2;

  not not_1 (not_1_out, 1'b0);
  Base1s base1s_1 (.out_1(base1s_1_out_1));
  Button Load (.out(Load_out));
  DecBCD7S decbcd7s_1 (
    .A(1'b0), .B(1'b0), .C(j_k_ff_10_q), .D(j_k_ff_9_q), .a_2(decbcd7s_1_b_2[1]), .b_2(decbcd7s_1_b_2[0]),
    .c_2(decbcd7s_1_c_2[0]), .d_2(decbcd7s_1_c_2[1]), .e(decbcd7s_1_c_2[2]), .f(decbcd7s_1_b_2[2]),
    .g(decbcd7s_1_b_2[3]));
  and and_1 (and_1_out, j_k_ff_1_q, j_k_ff_3_q, j_k_ff_2_q, j_k_ff_4_q, ~base1s_1_out_1);  // AND_Gate
  and and_2 (and_2_out, j_k_ff_5_q, j_k_ff_6_q, j_k_ff_7_q, j_k_ff_8_q, ~base1s_1_out_1);  // AND_Gate
  and and_3 (and_3_out, base1s_1_out_1, or_11_out);
  or or_1 (or_1_out, and_1_out, deccarga_1_p0);
  DecCarga deccarga_1 (
    .D9(in_10), .D8(in_9), .D7(in_8), .D6(in_7), .D5(in_6), .D4(in_5), .D3(in_4), .D2(in_3), .D1(in_2),
    .D0(in_1), .B__I(1'b0), .Load(Load_out), .P9(deccarga_1_p9), .P8(deccarga_1_p8), .P7(deccarga_1_p7),
    .P6(deccarga_1_p6), .P5(deccarga_1_p5), .P4(deccarga_1_p4), .P3(deccarga_1_p3), .P2(deccarga_1_p2),
    .P1(deccarga_1_p1), .P0(deccarga_1_p0));
  DecCarga deccarga_2 (
    .D9(in_10), .D8(in_9), .D7(in_8), .D6(in_7), .D5(in_6), .D4(in_5), .D3(in_4), .D2(in_3), .D1(in_2),
    .D0(in_1), .B__I(not_1_out), .Load(Load_out), .P9(deccarga_2_p9), .P8(deccarga_2_p8), .P7(deccarga_2_p7),
    .P6(deccarga_2_p6), .P5(deccarga_2_p5), .P4(deccarga_2_p4), .P3(deccarga_2_p3), .P2(deccarga_2_p2),
    .P1(deccarga_2_p1), .P0(deccarga_2_p0));
  J_K_Flip_Flop j_k_ff_1 (
    .J(1'b1), .clk(and_3_out), .K(1'b1), .Q(j_k_ff_1_q), .preset(or_1_out), .reset(deccarga_2_p0));  // open: Qn, en
  DecBCD7S decbcd7s_2 (
    .A(j_k_ff_8_q), .B(j_k_ff_7_q), .C(j_k_ff_6_q), .D(j_k_ff_5_q), .a_2(decbcd7s_2_b_2[1]),
    .b_2(decbcd7s_2_b_2[0]), .c_2(decbcd7s_2_c_2[0]), .d_2(decbcd7s_2_c_2[1]), .e(decbcd7s_2_c_2[2]),
    .f(decbcd7s_2_b_2[2]), .g(decbcd7s_2_b_2[3]));
  J_K_Flip_Flop j_k_ff_2 (
    .J(1'b1), .clk(j_k_ff_3_q), .K(1'b1), .Q(j_k_ff_2_q), .preset(deccarga_1_p2), .reset(or_3_out));  // open: Qn, en
  J_K_Flip_Flop j_k_ff_3 (
    .J(1'b1), .clk(j_k_ff_1_q), .K(1'b1), .Q(j_k_ff_3_q), .preset(deccarga_1_p1), .reset(or_2_out));  // open: Qn, en
  or or_2 (or_2_out, deccarga_2_p1, and_1_out);
  or or_3 (or_3_out, deccarga_2_p2, and_1_out);
  J_K_Flip_Flop j_k_ff_4 (
    .J(1'b1), .clk(j_k_ff_2_q), .K(1'b1), .Q(j_k_ff_4_q), .preset(or_4_out), .reset(deccarga_2_p3));  // open: Qn, en
  or or_4 (or_4_out, and_1_out, deccarga_1_p3);
  DecBCD7S decbcd7s_3 (
    .A(j_k_ff_4_q), .B(j_k_ff_2_q), .C(j_k_ff_3_q), .D(j_k_ff_1_q), .a_2(decbcd7s_3_b_2[1]),
    .b_2(decbcd7s_3_b_2[0]), .c_2(decbcd7s_3_c_2[0]), .d_2(decbcd7s_3_c_2[1]), .e(decbcd7s_3_c_2[2]),
    .f(decbcd7s_3_b_2[2]), .g(decbcd7s_3_b_2[3]));
  J_K_Flip_Flop j_k_ff_5 (
    .J(1'b1), .clk(j_k_ff_4_q), .K(1'b1), .Q(j_k_ff_5_q), .preset(or_5_out), .reset(deccarga_2_p4));  // open: Qn, en
  or or_5 (or_5_out, and_2_out, deccarga_1_p4);
  J_K_Flip_Flop j_k_ff_6 (
    .J(1'b1), .clk(j_k_ff_5_q), .K(1'b1), .Q(j_k_ff_6_q), .preset(deccarga_1_p5), .reset(or_6_out));  // open: Qn, en
  or or_6 (or_6_out, deccarga_2_p5, and_2_out);
  _7_Segment_Display u_7_segment_display_1 (
    .g(decbcd7s_1_b_2[3]), .f(decbcd7s_1_b_2[2]), .a(decbcd7s_1_b_2[1]), .b(decbcd7s_1_b_2[0]),
    .e(decbcd7s_1_c_2[2]), .d(decbcd7s_1_c_2[1]), .c(decbcd7s_1_c_2[0]));  // open: dp
  J_K_Flip_Flop j_k_ff_7 (
    .J(1'b1), .clk(j_k_ff_6_q), .K(1'b1), .Q(j_k_ff_7_q), .preset(deccarga_1_p6), .reset(or_8_out));  // open: Qn, en
  or or_7 (or_7_out, and_2_out, deccarga_1_p7);
  or or_8 (or_8_out, deccarga_2_p6, and_2_out);
  _7_Segment_Display u_7_segment_display_2 (
    .g(decbcd7s_3_b_2[3]), .f(decbcd7s_3_b_2[2]), .a(decbcd7s_3_b_2[1]), .b(decbcd7s_3_b_2[0]),
    .e(decbcd7s_3_c_2[2]), .d(decbcd7s_3_c_2[1]), .c(decbcd7s_3_c_2[0]));  // open: dp
  _7_Segment_Display u_7_segment_display_3 (
    .g(decbcd7s_2_b_2[3]), .f(decbcd7s_2_b_2[2]), .a(decbcd7s_2_b_2[1]), .b(decbcd7s_2_b_2[0]),
    .e(decbcd7s_2_c_2[2]), .d(decbcd7s_2_c_2[1]), .c(decbcd7s_2_c_2[0]));  // open: dp
  J_K_Flip_Flop j_k_ff_8 (
    .J(1'b1), .clk(j_k_ff_7_q), .K(1'b1), .Q(j_k_ff_8_q), .preset(or_7_out), .reset(deccarga_2_p7));  // open: Qn, en
  J_K_Flip_Flop j_k_ff_9 (
    .J(1'b1), .clk(j_k_ff_8_q), .K(1'b1), .Q(j_k_ff_9_q), .preset(deccarga_1_p8), .reset(deccarga_2_p8));  // open: Qn, en
  or or_9 (or_9_out, j_k_ff_1_q, j_k_ff_3_q, j_k_ff_2_q, j_k_ff_4_q, j_k_ff_5_q);
  or or_10 (or_10_out, j_k_ff_6_q, j_k_ff_7_q, j_k_ff_8_q, j_k_ff_9_q, j_k_ff_10_q);
  J_K_Flip_Flop j_k_ff_10 (
    .J(1'b1), .clk(j_k_ff_9_q), .K(1'b1), .Q(j_k_ff_10_q), .preset(deccarga_1_p9), .reset(deccarga_2_p9));  // open: Qn, en
  not not_2 (out_11, or_11_out);
  or or_11 (or_11_out, or_9_out, or_10_out);
endmodule

module DecCarga (
  input  D9,
  input  D8,
  input  D7,
  input  D6,
  input  D5,
  input  D4,
  input  D3,
  input  D2,
  input  D1,
  input  D0,
  input  B__I,
  input  Load,
  output P9,
  output P8,
  output P7,
  output P6,
  output P5,
  output P4,
  output P3,
  output P2,
  output P1,
  output P0
);

  wire and_1_out, and_2_out, and_3_out, and_4_out, and_5_out, and_6_out, and_7_out, and_8_out, and_9_out,
       and_10_out, and_11_out, and_12_out, and_13_out, and_14_out, and_15_out, and_16_out, and_17_out,
       and_18_out, and_19_out, and_20_out, and_21_out, and_22_out, and_23_out, and_24_out, and_25_out,
       and_26_out, and_27_out, and_28_out, and_29_out, and_30_out, and_31_out, and_32_out, and_33_out,
       and_34_out, and_35_out, and_36_out, and_37_out, and_38_out, and_39_out, and_40_out, and_41_out,
       and_42_out, and_43_out, and_44_out, not_1_out, not_2_out, not_3_out, not_4_out, not_5_out, not_6_out,
       not_7_out, not_8_out, not_9_out, not_10_out, not_11_out, not_12_out, not_13_out, not_14_out,
       not_15_out, not_16_out, not_17_out, not_18_out, not_19_out, not_20_out, not_21_out, not_22_out,
       not_23_out, not_24_out, not_25_out, not_26_out, not_27_out, not_28_out, not_29_out, not_30_out,
       not_31_out, not_32_out, not_33_out, not_34_out, not_35_out, not_36_out, not_37_out, not_38_out,
       not_39_out, not_40_out, not_41_out, not_42_out, not_43_out, not_44_out, not_45_out, not_46_out,
       not_47_out, not_48_out, not_49_out, not_50_out, not_51_out, not_52_out, not_53_out, not_54_out,
       not_55_out, not_56_out, not_57_out, not_58_out, not_59_out, not_60_out, not_61_out, not_62_out,
       not_63_out, not_64_out, or_1_out, or_2_out, or_3_out, or_4_out, or_5_out, or_6_out, or_7_out,
       or_8_out, xor_1_out, xor_2_out, xor_3_out, xor_4_out, xor_5_out, xor_6_out, xor_7_out, xor_8_out,
       xor_9_out, xor_10_out;

  not not_1 (not_1_out, D9);
  not not_2 (not_2_out, D8);
  not not_3 (not_3_out, D9);
  not not_4 (not_4_out, D7);
  not not_5 (not_5_out, D8);
  not not_6 (not_6_out, D7);
  not not_7 (not_7_out, D9);
  not not_8 (not_8_out, D8);
  not not_9 (not_9_out, D7);
  not not_10 (not_10_out, D6);
  not not_11 (not_11_out, D9);
  not not_12 (not_12_out, D7);
  not not_13 (not_13_out, D8);
  not not_14 (not_14_out, D7);
  not not_15 (not_15_out, D9);
  not not_16 (not_16_out, D8);
  not not_17 (not_17_out, D7);
  not not_18 (not_18_out, D6);
  not not_19 (not_19_out, D9);
  not not_20 (not_20_out, D8);
  not not_21 (not_21_out, D9);
  not not_22 (not_22_out, D8);
  not not_23 (not_23_out, D9);
  not not_24 (not_24_out, D8);
  not not_25 (not_25_out, D9);
  not not_26 (not_26_out, D9);
  not not_27 (not_27_out, D9);
  not not_28 (not_28_out, D9);
  not not_29 (not_29_out, D8);
  not not_30 (not_30_out, D8);
  not not_31 (not_31_out, D3);
  not not_32 (not_32_out, D8);
  not not_33 (not_33_out, D3);
  not not_34 (not_34_out, D9);
  not not_35 (not_35_out, D3);
  not not_36 (not_36_out, D9);
  not not_37 (not_37_out, D3);
  not not_38 (not_38_out, D8);
  not not_39 (not_39_out, D3);
  not not_40 (not_40_out, D8);
  not not_41 (not_41_out, D3);
  not not_42 (not_42_out, D8);
  not not_43 (not_43_out, D3);
  not not_44 (not_44_out, D9);
  not not_45 (not_45_out, D3);
  not not_46 (not_46_out, D9);
  not not_47 (not_47_out, D3);
  not not_48 (not_48_out, D8);
  not not_49 (not_49_out, D3);
  not not_50 (not_50_out, D8);
  not not_51 (not_51_out, D9);
  not not_52 (not_52_out, D9);
  not not_53 (not_53_out, D9);
  not not_54 (not_54_out, D9);
  not not_55 (not_55_out, D9);
  not not_56 (not_56_out, D9);
  not not_57 (not_57_out, D9);
  not not_58 (not_58_out, D9);
  not not_59 (not_59_out, D9);
  not not_60 (not_60_out, D9);
  not not_61 (not_61_out, D9);
  not not_62 (not_62_out, D8);
  not not_63 (not_63_out, D8);
  not not_64 (not_64_out, D8);
  and and_1 (and_1_out, not_1_out, D7);
  and and_2 (and_2_out, not_2_out, D7);
  and and_3 (and_3_out, not_3_out, not_4_out, D6);
  and and_4 (and_4_out, not_5_out, not_6_out, D6);
  and and_5 (and_5_out, not_7_out, not_8_out, not_9_out, not_10_out);
  and and_6 (and_6_out, not_11_out, not_12_out, D5);
  and and_7 (and_7_out, not_13_out, not_14_out, D5);
  and and_8 (and_8_out, not_15_out, not_16_out, not_17_out, not_18_out);
  and and_9 (and_9_out, not_19_out, D4);
  and and_10 (and_10_out, not_20_out, D4);
  and and_11 (and_11_out, not_21_out, D7, D5);
  and and_12 (and_12_out, not_22_out, D7, D5);
  and and_13 (and_13_out, not_23_out, D7, D6);
  and and_14 (and_14_out, not_24_out, D7, D6);
  and and_15 (and_15_out, not_25_out, D5, D4, D3);
  and and_16 (and_16_out, not_26_out, D6, D3);
  and and_17 (and_17_out, not_27_out, D7, D3);
  and and_18 (and_18_out, not_28_out, D8, D3);
  and and_19 (and_19_out, D9, not_29_out, D3);
  and and_20 (and_20_out, not_30_out, D5, D4, not_31_out, D2);
  and and_21 (and_21_out, not_32_out, D6, not_33_out, D2);
  and and_22 (and_22_out, not_34_out, D7, not_35_out, D2);
  and and_23 (and_23_out, not_36_out, D8, not_37_out, D2);
  and and_24 (and_24_out, D9, not_38_out, not_39_out, D2);
  and and_25 (and_25_out, not_40_out, D5, D4, not_41_out, D1);
  and and_26 (and_26_out, not_42_out, D6, not_43_out, D1);
  and and_27 (and_27_out, not_44_out, D7, not_45_out, D1);
  and and_28 (and_28_out, not_46_out, D8, not_47_out, D1);
  and and_29 (and_29_out, D9, not_48_out, not_49_out, D1);
  and and_30 (and_30_out, not_50_out, D5, D4, D0);
  and and_31 (and_31_out, not_51_out, D5, D4, D3, D1);
  and and_32 (and_32_out, not_52_out, D5, D4, D3, D2);
  and and_33 (and_33_out, not_53_out, D6, D0);
  and and_34 (and_34_out, not_54_out, D6, D3, D1);
  and and_35 (and_35_out, not_55_out, D6, D3, D2);
  and and_36 (and_36_out, not_56_out, D7, D0);
  and and_37 (and_37_out, not_57_out, D7, D3, D1);
  and and_38 (and_38_out, not_58_out, D7, D3, D2);
  and and_39 (and_39_out, not_59_out, D8, D0);
  and and_40 (and_40_out, not_60_out, D8, D3, D1);
  and and_41 (and_41_out, not_61_out, D8, D3, D2);
  and and_42 (and_42_out, D9, not_62_out, D0);
  and and_43 (and_43_out, D9, not_63_out, D3, D1);
  and and_44 (and_44_out, D9, not_64_out, D3, D2);
  or or_1 (or_1_out, and_1_out, and_2_out);
  or or_2 (or_2_out, and_3_out, and_4_out);
  or or_3 (or_3_out, and_5_out, and_6_out, and_7_out);
  or or_4 (or_4_out, and_8_out, and_9_out, and_10_out, and_11_out, and_12_out, and_13_out, and_14_out);
  or or_5 (or_5_out, and_15_out, and_16_out, and_17_out, and_18_out, and_19_out);
  or or_6 (or_6_out, and_20_out, and_21_out, and_22_out, and_23_out, and_24_out);
  or or_7 (or_7_out, and_25_out, and_26_out, and_27_out, and_28_out, and_29_out);
  or or_8 (or_8_out, and_30_out, and_31_out, and_32_out, and_33_out, and_34_out, and_35_out, and_36_out, and_37_out, and_38_out, and_39_out, and_40_out, and_41_out, and_42_out, and_43_out, and_44_out);
  xor xor_1 (xor_1_out, D9, B__I);
  xor xor_2 (xor_2_out, D8, B__I);
  xor xor_3 (xor_3_out, or_1_out, B__I);
  xor xor_4 (xor_4_out, or_2_out, B__I);
  xor xor_5 (xor_5_out, or_3_out, B__I);
  xor xor_6 (xor_6_out, or_4_out, B__I);
  xor xor_7 (xor_7_out, or_5_out, B__I);
  xor xor_8 (xor_8_out, or_6_out, B__I);
  xor xor_9 (xor_9_out, or_7_out, B__I);
  xor xor_10 (xor_10_out, or_8_out, B__I);
  and and_45 (P9, xor_1_out, Load);
  and and_46 (P8, xor_2_out, Load);
  and and_47 (P7, xor_3_out, Load);
  and and_48 (P6, xor_4_out, Load);
  and and_49 (P5, xor_5_out, Load);
  and and_50 (P4, xor_6_out, Load);
  and and_51 (P3, xor_7_out, Load);
  and and_52 (P2, xor_8_out, Load);
  and and_53 (P1, xor_9_out, Load);
  and and_54 (P0, xor_10_out, Load);

  // Notes on the sheet:
  //   0 => buffer
  //   1 => Inversor
endmodule

// BCD7S
module DecBCD7S (
  input  A,
  input  B,
  input  C,
  input  D,
  output a_2,
  output b_2,
  output c_2,
  output d_2,
  output e,
  output f,
  output g
);

  wire and_1_out, and_2_out, and_3_out, and_4_out, and_5_out, and_6_out, and_7_out, and_8_out, and_9_out,
       and_10_out, and_11_out, and_12_out, and_13_out, and_14_out, and_15_out, and_16_out, and_17_out,
       and_18_out, and_19_out, and_20_out, and_21_out, and_22_out, and_23_out, and_24_out, and_25_out,
       and_26_out, not_1_out, not_2_out, not_3_out, not_4_out, not_5_out, not_6_out, not_7_out, not_8_out,
       not_9_out, not_10_out, not_11_out, not_12_out, not_13_out, not_14_out, not_15_out, not_16_out,
       not_17_out, not_18_out, not_19_out, not_20_out, not_21_out, not_22_out, not_23_out, not_24_out,
       not_25_out, not_26_out, not_27_out, not_28_out, not_29_out, not_30_out, not_31_out, not_32_out,
       not_33_out, not_34_out, not_35_out, not_36_out, not_37_out, not_38_out, not_39_out, not_40_out,
       not_41_out, not_42_out, not_43_out, not_44_out, not_45_out, not_46_out, not_47_out, not_48_out,
       not_49_out, not_50_out, not_51_out, not_52_out;

  not not_1 (not_1_out, A);
  not not_2 (not_2_out, B);
  and and_1 (and_1_out, not_1_out, not_2_out, not_3_out);
  not not_3 (not_3_out, D);
  not not_4 (not_4_out, A);
  and and_2 (and_2_out, not_4_out, C);
  not not_5 (not_5_out, A);
  and and_3 (and_3_out, not_5_out, B, D);
  and and_4 (and_4_out, A, not_6_out, not_7_out);
  not not_6 (not_6_out, B);
  not not_7 (not_7_out, C);
  not not_8 (not_8_out, A);
  and and_5 (and_5_out, not_8_out, not_9_out);
  not not_9 (not_9_out, B);
  not not_10 (not_10_out, A);
  not not_11 (not_11_out, C);
  and and_6 (and_6_out, not_10_out, not_11_out, not_12_out);
  not not_12 (not_12_out, D);
  not not_13 (not_13_out, B);
  and and_7 (and_7_out, not_13_out, not_14_out);
  not not_14 (not_14_out, C);
  not not_15 (not_15_out, A);
  and and_8 (and_8_out, not_15_out, C, D);
  not not_16 (not_16_out, B);
  and and_9 (and_9_out, not_16_out, not_17_out);
  not not_17 (not_17_out, C);
  not not_18 (not_18_out, A);
  and and_10 (and_10_out, not_18_out, D);
  not not_19 (not_19_out, A);
  and and_11 (and_11_out, not_19_out, B);
  not not_20 (not_20_out, A);
  not not_21 (not_21_out, B);
  not not_22 (not_22_out, D);
  not not_23 (not_23_out, A);
  not not_24 (not_24_out, B);
  not not_25 (not_25_out, A);
  not not_26 (not_26_out, D);
  not not_27 (not_27_out, A);
  not not_28 (not_28_out, C);
  not not_29 (not_29_out, B);
  not not_30 (not_30_out, C);
  not not_31 (not_31_out, B);
  not not_32 (not_32_out, C);
  and and_12 (and_12_out, not_31_out, not_32_out, not_33_out);
  not not_33 (not_33_out, D);
  not not_34 (not_34_out, A);
  and and_13 (and_13_out, not_34_out, C, not_35_out);
  not not_35 (not_35_out, D);
  not not_36 (not_36_out, A);
  and and_14 (and_14_out, not_36_out, not_37_out, not_38_out);
  not not_37 (not_37_out, C);
  not not_38 (not_38_out, D);
  not not_39 (not_39_out, A);
  and and_15 (and_15_out, not_39_out, B, not_40_out);
  not not_40 (not_40_out, C);
  not not_41 (not_41_out, A);
  and and_16 (and_16_out, not_41_out, B, not_42_out);
  not not_42 (not_42_out, D);
  not not_43 (not_43_out, B);
  and and_17 (and_17_out, A, not_43_out, not_44_out);
  not not_44 (not_44_out, C);
  not not_45 (not_45_out, A);
  and and_18 (and_18_out, not_45_out, not_46_out, C);
  not not_46 (not_46_out, B);
  not not_47 (not_47_out, A);
  and and_19 (and_19_out, not_47_out, B, not_48_out);
  not not_48 (not_48_out, C);
  not not_49 (not_49_out, A);
  and and_20 (and_20_out, not_49_out, B, not_50_out);
  not not_50 (not_50_out, D);
  and and_21 (and_21_out, A, not_51_out, not_52_out);
  not not_51 (not_51_out, B);
  not not_52 (not_52_out, C);
  or or_1 (a_2, and_1_out, and_2_out, and_3_out, and_4_out);
  or or_2 (b_2, and_5_out, and_6_out, and_7_out, and_8_out);
  or or_3 (c_2, and_9_out, and_10_out, and_11_out);
  and and_22 (and_22_out, not_20_out, not_21_out, not_22_out);
  and and_23 (and_23_out, not_23_out, not_24_out, C);
  and and_24 (and_24_out, not_25_out, C, not_26_out);
  and and_25 (and_25_out, not_27_out, B, not_28_out, D);
  and and_26 (and_26_out, A, not_29_out, not_30_out);
  or or_4 (e, and_12_out, and_13_out);
  or or_5 (f, and_14_out, and_15_out, and_16_out, and_17_out);
  or or_6 (g, and_18_out, and_19_out, and_20_out, and_21_out);
  or or_7 (d_2, and_22_out, and_23_out, and_24_out, and_25_out, and_26_out);
endmodule

module Base1s (
  output out_1
);

  wire and_1_out, and_2_out, and_4_out, clock_1_out, j_k_ff_1_q, j_k_ff_1_qn, j_k_ff_2_q, j_k_ff_2_qn,
       j_k_ff_3_q, j_k_ff_3_qn, j_k_ff_4_q, j_k_ff_4_qn, j_k_ff_5_q, j_k_ff_5_qn, j_k_ff_6_q;

  Clock clock_1 (.out(clock_1_out));
  J_K_Flip_Flop j_k_ff_1 (
    .J(1'b1), .clk(clock_1_out), .K(1'b1), .Q(j_k_ff_1_q), .Qn(j_k_ff_1_qn), .reset(and_4_out));  // open: preset, en
  J_K_Flip_Flop j_k_ff_2 (
    .J(1'b1), .clk(j_k_ff_1_qn), .K(1'b1), .Q(j_k_ff_2_q), .Qn(j_k_ff_2_qn), .reset(and_4_out));  // open: preset, en
  J_K_Flip_Flop j_k_ff_3 (
    .J(1'b1), .clk(j_k_ff_2_qn), .K(1'b1), .Q(j_k_ff_3_q), .Qn(j_k_ff_3_qn), .reset(and_4_out));  // open: preset, en
  J_K_Flip_Flop j_k_ff_4 (
    .J(1'b1), .clk(j_k_ff_3_qn), .K(1'b1), .Q(j_k_ff_4_q), .Qn(j_k_ff_4_qn), .reset(and_4_out));  // open: preset, en
  J_K_Flip_Flop j_k_ff_5 (
    .J(1'b1), .clk(j_k_ff_4_qn), .K(1'b1), .Q(j_k_ff_5_q), .Qn(j_k_ff_5_qn), .reset(and_4_out));  // open: preset, en
  J_K_Flip_Flop j_k_ff_6 (
    .J(1'b1), .clk(j_k_ff_5_qn), .K(1'b1), .Q(j_k_ff_6_q), .reset(and_4_out));  // open: Qn, preset, en
  and and_1 (and_1_out, j_k_ff_1_q, j_k_ff_2_q, ~j_k_ff_3_q);  // AND_Gate
  and and_2 (and_2_out, j_k_ff_4_q, j_k_ff_5_q, j_k_ff_6_q);
  and and_3 (out_1, and_1_out, and_2_out);
  and and_4 (and_4_out, and_2_out, j_k_ff_3_q);
endmodule
